// Logisim project CI RELOGIO.circ as structural Verilog: 1 circuit, main circuit main
module main (
  input  AJUSHOR,
  input  AJUSMIN,
  input  CLOCK,
  output [3:0] HOR_plus,
  output [3:0] HOR_minus,
  output [3:0] Min_plus,
  output [3:0] MIN_minus,
  output [3:0] SEG_plus,
  output [3:0] Seg_minus
);

  wire and_1_out, and_2_out, and_3_out, and_4_out, and_5_out, and_6_out, and_7_out, and_8_out, or_1_out,
       or_2_out, or_3_out, or_4_out, or_5_out, or_6_out;

  or or_1 (or_1_out, or_6_out, and_1_out);
  T_Flip_Flop #(.trigger("falling")) t_ff_1 (
    .clk(or_2_out), .T(1'b1), .Q(Seg_minus[0]), .reset(or_1_out));  // open: Qn, preset, en
  or or_2 (or_2_out, or_6_out, CLOCK);
  T_Flip_Flop #(.trigger("falling")) t_ff_2 (
    .clk(and_1_out), .T(1'b1), .Q(SEG_plus[0]), .reset(or_6_out));  // open: Qn, preset, en
  T_Flip_Flop #(.trigger("falling")) t_ff_3 (
    .clk(Seg_minus[0]), .T(1'b1), .Q(Seg_minus[1]), .reset(or_1_out));  // open: Qn, preset, en
  T_Flip_Flop #(.trigger("falling")) t_ff_4 (
    .clk(SEG_plus[0]), .T(1'b1), .Q(SEG_plus[1]), .reset(or_6_out));  // open: Qn, preset, en
  T_Flip_Flop #(.trigger("falling")) t_ff_5 (
    .clk(or_4_out), .T(1'b1), .Q(MIN_minus[0]), .reset(and_3_out));  // open: Qn, preset, en
  T_Flip_Flop #(.trigger("falling")) t_ff_6 (
    .clk(and_3_out), .T(1'b1), .Q(Min_plus[0]), .reset(and_4_out));  // open: Qn, preset, en
  T_Flip_Flop #(.trigger("falling")) t_ff_7 (
    .clk(or_5_out), .T(1'b1), .Q(HOR_minus[0]), .reset(or_3_out));  // open: Qn, preset, en
  T_Flip_Flop #(.trigger("falling")) t_ff_8 (
    .clk(and_5_out), .T(1'b1), .Q(HOR_plus[0]), .reset(and_8_out));  // open: Qn, preset, en
  T_Flip_Flop #(.trigger("falling")) t_ff_9 (
    .clk(Seg_minus[1]), .T(1'b1), .Q(Seg_minus[2]), .reset(or_1_out));  // open: Qn, preset, en
  T_Flip_Flop #(.trigger("falling")) t_ff_10 (
    .clk(SEG_plus[1]), .T(1'b1), .Q(SEG_plus[2]), .reset(or_6_out));  // open: Qn, preset, en
  T_Flip_Flop #(.trigger("falling")) t_ff_11 (
    .clk(MIN_minus[0]), .T(1'b1), .Q(MIN_minus[1]), .reset(and_3_out));  // open: Qn, preset, en
  T_Flip_Flop #(.trigger("falling")) t_ff_12 (
    .clk(Min_plus[0]), .T(1'b1), .Q(Min_plus[1]), .reset(and_4_out));  // open: Qn, preset, en
  T_Flip_Flop #(.trigger("falling")) t_ff_13 (
    .clk(HOR_minus[0]), .T(1'b1), .Q(HOR_minus[1]), .reset(or_3_out));  // open: Qn, preset, en
  T_Flip_Flop #(.trigger("falling")) t_ff_14 (
    .clk(HOR_plus[0]), .T(1'b1), .Q(HOR_plus[1]), .reset(and_8_out));  // open: Qn, preset, en
  T_Flip_Flop #(.trigger("falling")) t_ff_15 (
    .clk(Seg_minus[2]), .T(1'b1), .Q(Seg_minus[3]), .reset(or_1_out));  // open: Qn, preset, en
  T_Flip_Flop #(.trigger("falling")) t_ff_16 (
    .clk(SEG_plus[2]), .T(1'b1), .Q(SEG_plus[3]), .reset(or_6_out));  // open: Qn, preset, en
  T_Flip_Flop #(.trigger("falling")) t_ff_17 (
    .clk(MIN_minus[1]), .T(1'b1), .Q(MIN_minus[2]), .reset(and_3_out));  // open: Qn, preset, en
  T_Flip_Flop #(.trigger("falling")) t_ff_18 (
    .clk(Min_plus[1]), .T(1'b1), .Q(Min_plus[2]), .reset(and_4_out));  // open: Qn, preset, en
  T_Flip_Flop #(.trigger("falling")) t_ff_19 (
    .clk(HOR_minus[1]), .T(1'b1), .Q(HOR_minus[2]), .reset(or_3_out));  // open: Qn, preset, en
  T_Flip_Flop #(.trigger("falling")) t_ff_20 (
    .clk(HOR_plus[1]), .T(1'b1), .Q(HOR_plus[2]), .reset(and_8_out));  // open: Qn, preset, en
  T_Flip_Flop #(.trigger("falling")) t_ff_21 (
    .clk(MIN_minus[2]), .T(1'b1), .Q(MIN_minus[3]), .reset(and_3_out));  // open: Qn, preset, en
  T_Flip_Flop #(.trigger("falling")) t_ff_22 (
    .clk(Min_plus[2]), .T(1'b1), .Q(Min_plus[3]), .reset(and_4_out));  // open: Qn, preset, en
  T_Flip_Flop #(.trigger("falling")) t_ff_23 (
    .clk(HOR_minus[2]), .T(1'b1), .Q(HOR_minus[3]), .reset(or_3_out));  // open: Qn, preset, en
  T_Flip_Flop #(.trigger("falling")) t_ff_24 (
    .clk(HOR_plus[2]), .T(1'b1), .Q(HOR_plus[3]), .reset(and_8_out));  // open: Qn, preset, en
  and and_1 (and_1_out, ~Seg_minus[0], Seg_minus[1], ~Seg_minus[2], Seg_minus[3]);  // AND_Gate
  and and_2 (and_2_out, ~SEG_plus[0], SEG_plus[1], SEG_plus[2], ~SEG_plus[3]);  // AND_Gate
  and and_3 (and_3_out, ~MIN_minus[0], MIN_minus[1], ~MIN_minus[2], MIN_minus[3]);  // AND_Gate
  and and_4 (and_4_out, ~Min_plus[0], Min_plus[1], Min_plus[2], ~Min_plus[3]);  // AND_Gate
  and and_5 (and_5_out, ~HOR_minus[0], HOR_minus[1], ~HOR_minus[2], HOR_minus[3]);  // AND_Gate
  and and_6 (and_6_out, ~HOR_minus[0], ~HOR_minus[1], HOR_minus[2], ~HOR_minus[3]);  // AND_Gate
  and and_7 (and_7_out, ~HOR_plus[0], HOR_plus[1], ~HOR_plus[2], ~HOR_plus[3]);  // AND_Gate
  and and_8 (and_8_out, and_6_out, and_7_out);
  or or_3 (or_3_out, and_5_out, and_8_out);
  or or_4 (or_4_out, and_2_out, AJUSMIN);
  or or_5 (or_5_out, AJUSHOR, and_4_out);
  or or_6 (or_6_out, and_2_out, or_4_out);
endmodule
