// Logisim project CI cod. Display 7SEG.circ as structural Verilog: 2 circuits, main circuit Codificador Display 7SEG
// D
module Codificador_Display_7SEG (
  input  D,
  input  C,
  input  B,
  input  A,
  input  ponto,
  output ponto_2,
  output C_2,
  output D_2,
  output E,
  output F,
  output G,
  output B_2,
  output A_2
);

  wire _0_out, _1_2_out, _1_3_out, _1_4_out, _1_5_out, _1_6_out, _1_7_out, _1_8_out, _1_9_out, _1_10_out,
       _1_11_out, _1_12_out, _1_out, _2_out, _3_out, _4_out;

  and _0 (_0_out, ~A, ~B, ~C, ~D);  // AND_Gate
  and _1 (_1_out, A, ~B, ~C, ~D);  // AND_Gate
  and _2 (_2_out, ~A, B, ~C, ~D);  // AND_Gate
  and _3 (_3_out, A, B, ~C, ~D);  // AND_Gate
  and _4 (_4_out, ~A, ~B, C, ~D);  // AND_Gate
  and _1_2 (_1_2_out, A, ~B, C, ~D);  // AND_Gate
  and _1_3 (_1_3_out, ~A, B, C, ~D);  // AND_Gate
  and _1_4 (_1_4_out, A, B, C, ~D);  // AND_Gate
  and _1_5 (_1_5_out, ~A, ~B, ~C, D);  // AND_Gate
  and _1_6 (_1_6_out, A, ~B, ~C, D);  // AND_Gate
  and _1_7 (_1_7_out, ~A, B, ~C, D);  // AND_Gate
  and _1_8 (_1_8_out, A, B, ~C, D);  // AND_Gate
  and _1_9 (_1_9_out, ~A, ~B, C, D);  // AND_Gate
  and _1_10 (_1_10_out, A, ~B, C, D);  // AND_Gate
  and _1_11 (_1_11_out, ~A, B, C, D);  // AND_Gate
  and _1_12 (_1_12_out, A, B, C, D);
  or or_1 (A_2, _1_12_out, _1_11_out, ~1'b1, _1_9_out, ~1'b1, _1_7_out, _1_6_out, _1_5_out, _1_4_out, _1_3_out, _1_2_out, ~1'b1, _3_out, _2_out, ~1'b1, _0_out);  // OR_Gate
  or or_2 (B_2, ~1'b1, ~1'b1, _1_10_out, ~1'b1, ~1'b1, _1_7_out, _1_6_out, _1_5_out, _1_4_out, ~1'b1, ~1'b1, _4_out, _3_out, _2_out, _1_out, _0_out);  // OR_Gate
  or or_3 (C_2, ~1'b1, ~1'b1, _1_10_out, ~1'b1, _1_8_out, _1_7_out, _1_6_out, _1_5_out, _1_4_out, _1_3_out, _1_2_out, _4_out, _3_out, ~1'b1, _1_out, _0_out);  // OR_Gate
  or u_D (D_2, ~1'b1, _1_11_out, _1_10_out, _1_9_out, _1_8_out, ~1'b1, ~1'b1, _1_5_out, ~1'b1, _1_3_out, _1_2_out, ~1'b1, _3_out, _2_out, ~1'b1, _0_out);  // OR_Gate
  or or_4 (E, _1_12_out, _1_11_out, _1_10_out, _1_9_out, _1_8_out, _1_7_out, ~1'b1, _1_5_out, ~1'b1, _1_3_out, ~1'b1, ~1'b1, ~1'b1, _2_out, ~1'b1, _0_out);  // OR_Gate
  or or_5 (F, _1_12_out, _1_11_out, ~1'b1, _1_9_out, _1_8_out, _1_7_out, _1_6_out, _1_5_out, ~1'b1, _1_3_out, _1_2_out, _4_out, ~1'b1, ~1'b1, ~1'b1, _0_out);  // OR_Gate
  or or_6 (G, _1_12_out, _1_11_out, _1_10_out, ~1'b1, _1_8_out, _1_7_out, _1_6_out, _1_5_out, ~1'b1, _1_3_out, _1_2_out, _4_out, _3_out, _2_out, ~1'b1, ~1'b1);  // OR_Gate

  assign ponto_2 = ponto;
endmodule

// D
module Cod__display_7SEG_adaptavel (
  input  D,
  input  C,
  input  B,
  input  A,
  input  ponto,
  output ponto_2,
  output C_2,
  output D_2,
  output E,
  output F,
  output G,
  output B_2,
  output A_2
);

  wire _0_out, _1_2_out, _1_3_out, _1_4_out, _1_5_out, _1_6_out, _1_7_out, _1_8_out, _1_9_out, _1_10_out,
       _1_11_out, _1_12_out, _1_out, _2_out, _3_out, _4_out;

  and _0 (_0_out, ~A, ~B, ~C, ~D);  // AND_Gate
  and _1 (_1_out, A, ~B, ~C, ~D);  // AND_Gate
  and _2 (_2_out, ~A, B, ~C, ~D);  // AND_Gate
  and _3 (_3_out, A, B, ~C, ~D);  // AND_Gate
  and _4 (_4_out, ~A, ~B, C, ~D);  // AND_Gate
  and _1_2 (_1_2_out, A, ~B, C, ~D);  // AND_Gate
  and _1_3 (_1_3_out, ~A, B, C, ~D);  // AND_Gate
  and _1_4 (_1_4_out, A, B, C, ~D);  // AND_Gate
  and _1_5 (_1_5_out, ~A, ~B, ~C, D);  // AND_Gate
  and _1_6 (_1_6_out, A, ~B, ~C, D);  // AND_Gate
  and _1_7 (_1_7_out, ~A, B, ~C, D);  // AND_Gate
  and _1_8 (_1_8_out, A, B, ~C, D);  // AND_Gate
  and _1_9 (_1_9_out, ~A, ~B, C, D);  // AND_Gate
  and _1_10 (_1_10_out, A, ~B, C, D);  // AND_Gate
  and _1_11 (_1_11_out, ~A, B, C, D);  // AND_Gate
  and _1_12 (_1_12_out, A, B, C, D);
  or or_1 (A_2, _1_12_out, _1_11_out, ~1'b1, _1_9_out, ~1'b1, _1_7_out, _1_6_out, _1_5_out, _1_4_out, _1_3_out, _1_2_out, ~1'b1, _3_out, _2_out, ~1'b1, _0_out);  // OR_Gate
  or or_2 (B_2, ~1'b1, ~1'b1, _1_10_out, ~1'b1, ~1'b1, _1_7_out, _1_6_out, _1_5_out, _1_4_out, ~1'b1, ~1'b1, _4_out, _3_out, _2_out, _1_out, _0_out);  // OR_Gate
  or or_3 (C_2, ~1'b1, ~1'b1, _1_10_out, ~1'b1, _1_8_out, _1_7_out, _1_6_out, _1_5_out, _1_4_out, _1_3_out, _1_2_out, _4_out, _3_out, ~1'b1, _1_out, _0_out);  // OR_Gate
  or u_D (D_2, ~1'b1, _1_11_out, _1_10_out, _1_9_out, _1_8_out, ~1'b1, ~1'b1, _1_5_out, ~1'b1, _1_3_out, _1_2_out, ~1'b1, _3_out, _2_out, ~1'b1, _0_out);  // OR_Gate
  or or_4 (E, _1_12_out, _1_11_out, _1_10_out, _1_9_out, _1_8_out, _1_7_out, ~1'b1, _1_5_out, ~1'b1, _1_3_out, ~1'b1, ~1'b1, ~1'b1, _2_out, ~1'b1, _0_out);  // OR_Gate
  or or_5 (F, _1_12_out, _1_11_out, ~1'b1, _1_9_out, _1_8_out, _1_7_out, _1_6_out, _1_5_out, ~1'b1, _1_3_out, _1_2_out, _4_out, ~1'b1, ~1'b1, ~1'b1, _0_out);  // OR_Gate
  or or_6 (G, _1_12_out, _1_11_out, _1_10_out, ~1'b1, _1_8_out, _1_7_out, _1_6_out, _1_5_out, ~1'b1, _1_3_out, _1_2_out, _4_out, _3_out, _2_out, ~1'b1, ~1'b1);  // OR_Gate

  assign ponto_2 = ponto;
endmodule
