// Logisim project CI contadores.circ as structural Verilog: 7 circuits, main circuit Contador Sincrono Impar
module Contador_Sincrono_Impar (
  input  CLOCK,
  output [3:0] Saiuda_BCD
);

  wire and_1_out, j_k_ff_1_qn;

  J_K_Flip_Flop j_k_ff_1 (
    .J(and_1_out), .clk(CLOCK), .K(1'b1), .Q(Saiuda_BCD[3]), .Qn(j_k_ff_1_qn));  // open: preset, en, reset
  and and_1 (and_1_out, Saiuda_BCD[1], Saiuda_BCD[2]);
  J_K_Flip_Flop j_k_ff_2 (
    .J(Saiuda_BCD[1]), .clk(CLOCK), .K(Saiuda_BCD[1]), .Q(Saiuda_BCD[2]));  // open: Qn, preset, en, reset
  J_K_Flip_Flop j_k_ff_3 (.J(j_k_ff_1_qn), .clk(CLOCK), .K(1'b1), .Q(Saiuda_BCD[1]));  // open: Qn, preset, en, reset
  J_K_Flip_Flop j_k_ff_4 (.J(1'b1), .clk(CLOCK), .K(1'b0), .Q(Saiuda_BCD[0]));  // open: Qn, preset, en, reset
endmodule

module Contador_Sincrono_Par (
  input  CLOCK,
  output [3:0] SAIDA_BCD
);

  wire and_1_out, j_k_ff_1_qn;

  J_K_Flip_Flop j_k_ff_1 (
    .J(and_1_out), .clk(CLOCK), .K(1'b1), .Q(SAIDA_BCD[3]), .Qn(j_k_ff_1_qn));  // open: preset, en, reset
  and and_1 (and_1_out, SAIDA_BCD[1], SAIDA_BCD[2]);
  J_K_Flip_Flop j_k_ff_2 (
    .J(SAIDA_BCD[1]), .clk(CLOCK), .K(SAIDA_BCD[1]), .Q(SAIDA_BCD[2]));  // open: Qn, preset, en, reset
  J_K_Flip_Flop j_k_ff_3 (.J(j_k_ff_1_qn), .clk(CLOCK), .K(1'b1), .Q(SAIDA_BCD[1]));  // open: Qn, preset, en, reset
  J_K_Flip_Flop j_k_ff_4 (.J(1'b0), .clk(CLOCK), .K(1'b0), .Q(SAIDA_BCD[0]));  // open: Qn, preset, en, reset
endmodule

module Contador_Decimal (
  input  CLOCK,
  input  Reset,
  output [3:0] SAIDA_BCD
);

  wire and_1_out, or_1_out;

  T_Flip_Flop #(.trigger("falling")) t_ff_1 (
    .clk(CLOCK), .T(1'b1), .Q(SAIDA_BCD[0]), .reset(or_1_out));  // open: Qn, preset, en
  T_Flip_Flop #(.trigger("falling")) t_ff_2 (
    .clk(SAIDA_BCD[0]), .T(1'b1), .Q(SAIDA_BCD[1]), .reset(or_1_out));  // open: Qn, preset, en
  T_Flip_Flop #(.trigger("falling")) t_ff_3 (
    .clk(SAIDA_BCD[1]), .T(1'b1), .Q(SAIDA_BCD[2]), .reset(or_1_out));  // open: Qn, preset, en
  and and_1 (and_1_out, SAIDA_BCD[1], SAIDA_BCD[3]);
  T_Flip_Flop #(.trigger("falling")) t_ff_4 (
    .clk(SAIDA_BCD[2]), .T(1'b1), .Q(SAIDA_BCD[3]), .reset(or_1_out));  // open: Qn, preset, en
  or or_1 (or_1_out, and_1_out, Reset);
endmodule

module Contador_Hexadecimal (
  input  CLOCK,
  input  Reset,
  output [3:0] SAIDA_BCD
);

  T_Flip_Flop #(.trigger("falling")) t_ff_1 (
    .clk(CLOCK), .T(1'b1), .Q(SAIDA_BCD[0]), .reset(Reset));  // open: Qn, preset, en
  T_Flip_Flop #(.trigger("falling")) t_ff_2 (
    .clk(SAIDA_BCD[0]), .T(1'b1), .Q(SAIDA_BCD[1]), .reset(Reset));  // open: Qn, preset, en
  T_Flip_Flop #(.trigger("falling")) t_ff_3 (
    .clk(SAIDA_BCD[1]), .T(1'b1), .Q(SAIDA_BCD[2]), .reset(Reset));  // open: Qn, preset, en
  T_Flip_Flop #(.trigger("falling")) t_ff_4 (
    .clk(SAIDA_BCD[2]), .T(1'b1), .Q(SAIDA_BCD[3]), .reset(Reset));  // open: Qn, preset, en
endmodule

module Contador_Assincrono_Crescente (
  input  CLOCK,
  output [3:0] SAIDA_BCD
);

  wire and_1_out, and_2_out, and_3_out, and_4_out, and_5_out, and_6_out, nor_1_out, nor_2_out, nor_3_out,
       not_1_out, t_ff_1_qn, t_ff_2_qn, t_ff_3_qn;

  T_Flip_Flop t_ff_1 (.clk(CLOCK), .T(1'b1), .Q(SAIDA_BCD[0]), .Qn(t_ff_1_qn));  // open: preset, reset, en
  not not_1 (not_1_out, 1'b1);
  and and_1 (and_1_out, SAIDA_BCD[0], 1'b1);
  and and_2 (and_2_out, t_ff_1_qn, not_1_out);
  nor nor_1 (nor_1_out, and_1_out, and_2_out);
  T_Flip_Flop t_ff_2 (.clk(nor_1_out), .T(1'b1), .Q(SAIDA_BCD[1]), .Qn(t_ff_2_qn));  // open: preset, reset, en
  and and_3 (and_3_out, SAIDA_BCD[1], 1'b1);
  nor nor_2 (nor_2_out, and_3_out, and_4_out);
  and and_4 (and_4_out, t_ff_2_qn, not_1_out);
  T_Flip_Flop t_ff_3 (.clk(nor_2_out), .T(1'b1), .Q(SAIDA_BCD[2]), .Qn(t_ff_3_qn));  // open: preset, reset, en
  and and_5 (and_5_out, SAIDA_BCD[2], 1'b1);
  and and_6 (and_6_out, t_ff_3_qn, not_1_out);
  nor nor_3 (nor_3_out, and_5_out, and_6_out);
  T_Flip_Flop t_ff_4 (.clk(nor_3_out), .T(1'b1), .Q(SAIDA_BCD[3]));  // open: Qn, preset, reset, en
endmodule

module Contador_Asssincrono_Decrescente (
  input  CLOCK,
  output [3:0] SAIDA_BCD
);

  wire and_1_out, and_2_out, and_3_out, and_4_out, and_5_out, and_6_out, nor_1_out, nor_2_out, nor_3_out,
       not_1_out, t_ff_1_qn, t_ff_2_qn, t_ff_3_qn;

  T_Flip_Flop t_ff_1 (.clk(CLOCK), .T(1'b1), .Q(SAIDA_BCD[0]), .Qn(t_ff_1_qn));  // open: preset, reset, en
  not not_1 (not_1_out, 1'b0);
  and and_1 (and_1_out, SAIDA_BCD[0], 1'b0);
  nor nor_1 (nor_1_out, and_1_out, and_2_out);
  and and_2 (and_2_out, t_ff_1_qn, not_1_out);
  T_Flip_Flop t_ff_2 (.clk(nor_1_out), .T(1'b1), .Q(SAIDA_BCD[1]), .Qn(t_ff_2_qn));  // open: preset, reset, en
  and and_3 (and_3_out, SAIDA_BCD[1], 1'b0);
  and and_4 (and_4_out, t_ff_2_qn, not_1_out);
  nor nor_2 (nor_2_out, and_3_out, and_4_out);
  T_Flip_Flop t_ff_3 (.clk(nor_2_out), .T(1'b1), .Q(SAIDA_BCD[2]), .Qn(t_ff_3_qn));  // open: preset, reset, en
  and and_5 (and_5_out, SAIDA_BCD[2], 1'b0);
  nor nor_3 (nor_3_out, and_5_out, and_6_out);
  and and_6 (and_6_out, t_ff_3_qn, not_1_out);
  T_Flip_Flop t_ff_4 (.clk(nor_3_out), .T(1'b1), .Q(SAIDA_BCD[3]));  // open: Qn, preset, reset, en
endmodule

module Contador_Qualquer (
  input  CLOCK,
  output [3:0] SAIDA_BCD
);

  wire and_1_out, and_2_out, and_3_out, and_4_out, and_5_out, and_6_out, and_7_out, j_k_ff_3_qn, j_k_ff_4_qn,
       or_1_out, or_2_out, or_3_out, or_4_out, xor_1_out;

  or or_1 (or_1_out, j_k_ff_4_qn, j_k_ff_3_qn, SAIDA_BCD[1]);
  or or_2 (or_2_out, j_k_ff_4_qn, SAIDA_BCD[2], SAIDA_BCD[1]);
  J_K_Flip_Flop #(.trigger("falling")) j_k_ff_1 (
    .J(or_1_out), .clk(CLOCK), .K(or_2_out), .Q(SAIDA_BCD[0]));  // open: Qn, preset, en, reset
  or or_3 (or_3_out, and_2_out, and_1_out);
  xor xor_1 (xor_1_out, and_3_out, SAIDA_BCD[0]);
  and and_1 (and_1_out, SAIDA_BCD[2], SAIDA_BCD[0]);
  and and_2 (and_2_out, j_k_ff_3_qn, SAIDA_BCD[3]);
  J_K_Flip_Flop #(.trigger("falling")) j_k_ff_2 (
    .J(xor_1_out), .clk(CLOCK), .K(or_3_out), .Q(SAIDA_BCD[1]));  // open: Qn, preset, en, reset
  and and_3 (and_3_out, SAIDA_BCD[2], SAIDA_BCD[3]);
  and and_4 (and_4_out, SAIDA_BCD[3], SAIDA_BCD[1]);
  or or_4 (or_4_out, and_6_out, and_5_out);
  and and_5 (and_5_out, SAIDA_BCD[3], SAIDA_BCD[0]);
  J_K_Flip_Flop #(.trigger("falling")) j_k_ff_3 (
    .J(and_4_out), .clk(CLOCK), .K(or_4_out), .Q(SAIDA_BCD[2]), .Qn(j_k_ff_3_qn));  // open: preset, en, reset
  and and_6 (and_6_out, SAIDA_BCD[1], SAIDA_BCD[0]);
  and and_7 (and_7_out, SAIDA_BCD[2], SAIDA_BCD[0]);
  J_K_Flip_Flop #(.trigger("falling")) j_k_ff_4 (
    .J(and_6_out), .clk(CLOCK), .K(and_7_out), .Q(SAIDA_BCD[3]), .Qn(j_k_ff_4_qn));  // open: preset, en, reset
endmodule
