// Logisim project CI coracao.circ as structural Verilog: 1 circuit, main circuit Coração de LEDs
module \Coração_de_LEDs  (
  input  btn_2,
  input  btn_4,
  input  btn_8,
  input  btn_16,
  input  Ligar,
  input  CLOCK_64Hz,
  input  LED_0,
  input  LED_1,
  input  LED_2,
  input  LED_3,
  input  LED_4,
  input  LED_5,
  input  LED_6,
  input  LED_7,
  input  LED_8,
  input  LED_9,
  input  LED_10,
  input  LED_11,
  input  LED_12,
  input  LED_13,
  input  LED_14,
  input  LED_15,
  input  LED_16,
  input  LED_17,
  input  btn_Atualizar,
  input  Inverter,
  output LED_8_2,
  output LED_12_2,
  output LED_11_2,
  output LED_9_2,
  output LED_13_2,
  output LED_10_2,
  output LED_7_2,
  output LED_14_2,
  output LED_6_2,
  output LED_15_2,
  output LED_5_2,
  output LED_16_2,
  output LED_4_2,
  output LED_17_2,
  output LED_3_2,
  output LED_0_2,
  output LED_2_2,
  output LED_1_2,
  output [3:0] VEL_plus,
  output [3:0] VEL_minus,
  output [8:0] Matriz_9,
  output [8:0] Matriz_8,
  output [8:0] Matriz_7,
  output [8:0] Matriz_6,
  output [8:0] Matriz_5,
  output [8:0] Matriz_4,
  output [8:0] Matriz_3,
  output [8:0] Matriz_2,
  output [8:0] Matriz_1
);

  wire and_1_out, and_2_out, and_3_out, and_4_out, and_25_out, and_26_out, and_27_out, and_28_out,
       and_29_out, and_30_out, and_31_out, and_32_out, and_33_out, and_34_out, and_35_out, and_36_out,
       and_37_out, and_38_out, and_39_out, and_40_out, and_41_out, and_42_out, and_43_out,
       controlled_buffer_1_out, controlled_buffer_2_out, controlled_buffer_3_out, controlled_buffer_4_out,
       controlled_buffer_5_out, controlled_buffer_6_out, d_ff_1_qn, d_ff_2_q, d_ff_3_q, d_ff_4_q, d_ff_5_q,
       d_ff_6_q, d_ff_7_q, d_ff_8_q, d_ff_9_q, d_ff_10_q, d_ff_11_q, d_ff_12_q, d_ff_13_q, d_ff_14_q,
       d_ff_15_q, d_ff_16_q, d_ff_17_q, d_ff_18_q, d_ff_19_q, nor_1_out, not_1_out, not_2_out, not_3_out,
       not_4_out, not_5_out, not_6_out, not_7_out, not_8_out, not_9_out, not_10_out, not_11_out, not_12_out,
       not_13_out, not_14_out, not_15_out, not_16_out, not_17_out, not_18_out, not_19_out, not_20_out,
       not_21_out, not_22_out, not_23_out, not_24_out, or_1_out, or_2_out, t_ff_1_q, t_ff_2_q, t_ff_3_q,
       t_ff_4_q, t_ff_5_q, t_ff_6_q, t_ff_7_q, t_ff_8_q, t_ff_9_q, t_ff_10_q, t_ff_11_q, t_ff_12_q,
       t_ff_13_q, t_ff_14_q, t_ff_15_q, t_ff_16_q;
  wire [1:0] and_5_out, and_7_out, and_9_out, and_11_out, and_13_out, and_15_out, and_17_out, and_19_out,
       and_21_out, and_23_out;
  wire [3:0] or_3_out;
  wire [17:0] controlled_inverter_1_out;

  or or_1 (or_1_out, or_3_out[0], or_3_out[1], or_3_out[2], or_3_out[3]);
  T_Flip_Flop t_ff_1 (.clk(t_ff_11_q), .T(1'b1), .Q(t_ff_1_q));  // open: Qn, preset, reset, en
  not not_1 (not_1_out, or_1_out);
  T_Flip_Flop t_ff_2 (.clk(t_ff_1_q), .T(btn_2), .Q(t_ff_2_q));  // open: Qn, preset, reset, en
  assign controlled_buffer_1_out = Ligar ? CLOCK_64Hz : 1'bz;  // Controlled_Buffer controlled_buffer_1
  not not_2 (not_2_out, Inverter);
  assign controlled_buffer_2_out = or_3_out[0] ? controlled_buffer_1_out : 1'bz;  // Controlled_Buffer controlled_buffer_2
  T_Flip_Flop t_ff_3 (
    .clk(controlled_buffer_2_out), .T(1'b1), .Q(t_ff_3_q), .reset(and_3_out));  // open: Qn, preset, en
  assign controlled_buffer_3_out = or_3_out[1] ? controlled_buffer_1_out : 1'bz;  // Controlled_Buffer controlled_buffer_3
  T_Flip_Flop t_ff_4 (
    .clk(controlled_buffer_3_out), .T(1'b1), .Q(t_ff_4_q), .reset(and_4_out));  // open: Qn, preset, en
  assign controlled_buffer_4_out = or_3_out[2] ? controlled_buffer_1_out : 1'bz;  // Controlled_Buffer controlled_buffer_4
  T_Flip_Flop t_ff_5 (
    .clk(controlled_buffer_4_out), .T(1'b1), .Q(t_ff_5_q), .reset(and_2_out));  // open: Qn, preset, en
  T_Flip_Flop t_ff_6 (
    .clk(controlled_buffer_5_out), .T(1'b1), .Q(t_ff_6_q), .reset(and_1_out));  // open: Qn, preset, en
  assign controlled_buffer_5_out = or_3_out[3] ? controlled_buffer_1_out : 1'bz;  // Controlled_Buffer controlled_buffer_5
  D_Flip_Flop #(.trigger("high")) d_ff_1 (
    .clk(1'b1), .D(controlled_buffer_6_out), .Qn(d_ff_1_qn));  // open: Q, preset, en, reset
  assign controlled_buffer_6_out = not_1_out ? controlled_buffer_1_out : 1'bz;  // Controlled_Buffer controlled_buffer_6
  or or_2 (or_2_out, d_ff_1_qn, t_ff_14_q, t_ff_12_q, t_ff_7_q, t_ff_3_q);
  T_Flip_Flop t_ff_7 (.clk(t_ff_4_q), .T(1'b1), .Q(t_ff_7_q), .reset(and_4_out));  // open: Qn, preset, en
  T_Flip_Flop t_ff_8 (.clk(t_ff_5_q), .T(1'b1), .Q(t_ff_8_q), .reset(and_2_out));  // open: Qn, preset, en
  T_Flip_Flop t_ff_9 (.clk(t_ff_6_q), .T(1'b1), .Q(t_ff_9_q), .reset(and_1_out));  // open: Qn, preset, en
  and and_1 (and_1_out, t_ff_14_q, not_1_out);
  and and_2 (and_2_out, t_ff_12_q, not_1_out);
  T_Flip_Flop t_ff_10 (.clk(t_ff_1_q), .T(btn_4), .Q(t_ff_10_q));  // open: Qn, preset, reset, en
  T_Flip_Flop t_ff_11 (.clk(CLOCK_64Hz), .T(1'b1), .Q(t_ff_11_q));  // open: Qn, preset, reset, en
  assign controlled_inverter_1_out = btn_Atualizar ? ~{LED_17, LED_16, LED_15, LED_14, LED_13, LED_12, LED_11, LED_10, LED_9, LED_8, LED_7, LED_6, LED_5, LED_4, LED_3, LED_2, LED_1, LED_0} : 18'bz;  // Controlled_Inverter controlled_inverter_1
  T_Flip_Flop t_ff_12 (.clk(t_ff_8_q), .T(1'b1), .Q(t_ff_12_q), .reset(and_2_out));  // open: Qn, preset, en
  T_Flip_Flop t_ff_13 (.clk(t_ff_9_q), .T(1'b1), .Q(t_ff_13_q), .reset(and_1_out));  // open: Qn, preset, en
  and and_3 (and_3_out, t_ff_3_q, not_1_out);
  and and_4 (and_4_out, t_ff_7_q, not_1_out);
  T_Flip_Flop t_ff_14 (.clk(t_ff_13_q), .T(1'b1), .Q(t_ff_14_q), .reset(and_1_out));  // open: Qn, preset, en
  not not_3 (not_3_out, not_2_out);
  T_Flip_Flop t_ff_15 (.clk(t_ff_1_q), .T(btn_8), .Q(t_ff_15_q));  // open: Qn, preset, reset, en
  T_Flip_Flop t_ff_16 (.clk(t_ff_1_q), .T(btn_16), .Q(t_ff_16_q));  // open: Qn, preset, reset, en
  not not_4 (not_4_out, controlled_inverter_1_out[0]);
  not not_5 (not_5_out, controlled_inverter_1_out[1]);
  not not_6 (not_6_out, controlled_inverter_1_out[2]);
  not not_7 (not_7_out, controlled_inverter_1_out[3]);
  not not_8 (not_8_out, controlled_inverter_1_out[4]);
  not not_9 (not_9_out, controlled_inverter_1_out[5]);
  not not_10 (not_10_out, controlled_inverter_1_out[6]);
  not not_11 (not_11_out, controlled_inverter_1_out[7]);
  not not_12 (not_12_out, controlled_inverter_1_out[8]);
  not not_13 (not_13_out, controlled_inverter_1_out[9]);
  not not_14 (not_14_out, controlled_inverter_1_out[10]);
  not not_15 (not_15_out, controlled_inverter_1_out[11]);
  not not_16 (not_16_out, controlled_inverter_1_out[12]);
  not not_17 (not_17_out, controlled_inverter_1_out[13]);
  not not_18 (not_18_out, controlled_inverter_1_out[14]);
  not not_19 (not_19_out, controlled_inverter_1_out[15]);
  not not_20 (not_20_out, controlled_inverter_1_out[16]);
  not not_21 (not_21_out, controlled_inverter_1_out[17]);
  and and_5 (and_5_out[0], d_ff_11_q, not_2_out);
  and and_6 (and_5_out[1], not_3_out, d_ff_2_q);
  and and_7 (and_7_out[0], d_ff_6_q, not_2_out);
  and and_8 (and_7_out[1], d_ff_7_q, not_3_out);
  and and_9 (and_9_out[0], d_ff_19_q, not_2_out);
  and and_10 (and_9_out[1], d_ff_15_q, not_3_out);
  and and_11 (and_11_out[0], d_ff_14_q, not_2_out);
  and and_12 (and_11_out[1], d_ff_16_q, not_3_out);
  and and_13 (and_13_out[0], d_ff_10_q, not_2_out);
  and and_14 (and_13_out[1], d_ff_3_q, not_3_out);
  and and_15 (and_15_out[0], d_ff_5_q, not_2_out);
  and and_16 (and_15_out[1], d_ff_8_q, not_3_out);
  and and_17 (and_17_out[0], d_ff_18_q, not_2_out);
  and and_18 (and_17_out[1], d_ff_12_q, not_3_out);
  and and_19 (and_19_out[0], d_ff_13_q, not_2_out);
  and and_20 (and_19_out[1], d_ff_17_q, not_3_out);
  and and_21 (and_21_out[0], d_ff_9_q, not_2_out);
  and and_22 (and_21_out[1], d_ff_4_q, not_3_out);
  and and_23 (and_23_out[0], d_ff_4_q, not_2_out);
  and and_24 (and_23_out[1], d_ff_9_q, not_3_out);
  D_Flip_Flop d_ff_2 (
    .clk(or_2_out), .D(d_ff_11_q), .Q(d_ff_2_q), .preset(not_4_out), .reset(controlled_inverter_1_out[0]));  // open: Qn, en
  D_Flip_Flop d_ff_3 (
    .clk(or_2_out), .D(d_ff_16_q), .Q(d_ff_3_q), .preset(not_8_out), .reset(controlled_inverter_1_out[4]));  // open: Qn, en
  D_Flip_Flop d_ff_4 (
    .clk(or_2_out), .D(d_ff_17_q), .Q(d_ff_4_q), .preset(not_12_out), .reset(controlled_inverter_1_out[8]));  // open: Qn, en
  D_Flip_Flop d_ff_5 (
    .clk(or_2_out), .D(d_ff_18_q), .Q(d_ff_5_q), .preset(not_16_out), .reset(controlled_inverter_1_out[12]));  // open: Qn, en
  D_Flip_Flop d_ff_6 (
    .clk(or_2_out), .D(d_ff_19_q), .Q(d_ff_6_q), .preset(not_20_out), .reset(controlled_inverter_1_out[16]));  // open: Qn, en
  D_Flip_Flop d_ff_7 (
    .clk(or_2_out), .D(d_ff_2_q), .Q(d_ff_7_q), .preset(not_5_out), .reset(controlled_inverter_1_out[1]));  // open: Qn, en
  D_Flip_Flop d_ff_8 (
    .clk(or_2_out), .D(d_ff_3_q), .Q(d_ff_8_q), .preset(not_9_out), .reset(controlled_inverter_1_out[5]));  // open: Qn, en
  D_Flip_Flop d_ff_9 (
    .clk(or_2_out), .D(d_ff_4_q), .Q(d_ff_9_q), .preset(not_13_out), .reset(controlled_inverter_1_out[9]));  // open: Qn, en
  D_Flip_Flop d_ff_10 (
    .clk(or_2_out), .D(d_ff_5_q), .Q(d_ff_10_q), .preset(not_17_out), .reset(controlled_inverter_1_out[13]));  // open: Qn, en
  D_Flip_Flop d_ff_11 (
    .clk(or_2_out), .D(d_ff_6_q), .Q(d_ff_11_q), .preset(not_21_out), .reset(controlled_inverter_1_out[17]));  // open: Qn, en
  or or_3 (or_3_out[0], t_ff_2_q, t_ff_2_q);
  D_Flip_Flop d_ff_12 (
    .clk(or_2_out), .D(d_ff_8_q), .Q(d_ff_12_q), .preset(not_10_out), .reset(controlled_inverter_1_out[6]));  // open: Qn, en
  D_Flip_Flop d_ff_13 (
    .clk(or_2_out), .D(d_ff_9_q), .Q(d_ff_13_q), .preset(not_14_out), .reset(controlled_inverter_1_out[10]));  // open: Qn, en
  D_Flip_Flop d_ff_14 (
    .clk(or_2_out), .D(d_ff_10_q), .Q(d_ff_14_q), .preset(not_18_out), .reset(controlled_inverter_1_out[14]));  // open: Qn, en
  or or_4 (LED_9_2, and_23_out[0], and_23_out[1]);
  or or_5 (LED_8_2, and_21_out[0], and_21_out[1]);
  or or_6 (LED_7_2, and_19_out[0], and_19_out[1]);
  or or_7 (LED_6_2, and_17_out[0], and_17_out[1]);
  or or_8 (LED_5_2, and_15_out[0], and_15_out[1]);
  or or_9 (LED_4_2, and_13_out[0], and_13_out[1]);
  or or_10 (LED_3_2, and_11_out[0], and_11_out[1]);
  or or_11 (LED_2_2, and_9_out[0], and_9_out[1]);
  or or_12 (LED_1_2, and_7_out[0], and_7_out[1]);
  or or_13 (LED_0_2, and_5_out[0], and_5_out[1]);
  D_Flip_Flop d_ff_15 (
    .clk(or_2_out), .D(d_ff_7_q), .Q(d_ff_15_q), .preset(not_6_out), .reset(controlled_inverter_1_out[2]));  // open: Qn, en
  D_Flip_Flop d_ff_16 (
    .clk(or_2_out), .D(d_ff_15_q), .Q(d_ff_16_q), .preset(not_7_out), .reset(controlled_inverter_1_out[3]));  // open: Qn, en
  D_Flip_Flop d_ff_17 (
    .clk(or_2_out), .D(d_ff_12_q), .Q(d_ff_17_q), .preset(not_11_out), .reset(controlled_inverter_1_out[7]));  // open: Qn, en
  D_Flip_Flop d_ff_18 (
    .clk(or_2_out), .D(d_ff_13_q), .Q(d_ff_18_q), .preset(not_15_out), .reset(controlled_inverter_1_out[11]));  // open: Qn, en
  D_Flip_Flop d_ff_19 (
    .clk(or_2_out), .D(d_ff_14_q), .Q(d_ff_19_q), .preset(not_19_out), .reset(controlled_inverter_1_out[15]));  // open: Qn, en
  and and_25 (and_25_out, d_ff_17_q, not_2_out);
  and and_26 (and_26_out, d_ff_13_q, not_3_out);
  and and_27 (and_27_out, d_ff_12_q, not_2_out);
  and and_28 (and_28_out, d_ff_18_q, not_3_out);
  and and_29 (and_29_out, d_ff_8_q, not_2_out);
  and and_30 (and_30_out, d_ff_5_q, not_3_out);
  and and_31 (and_31_out, d_ff_3_q, not_2_out);
  and and_32 (and_32_out, d_ff_10_q, not_3_out);
  and and_33 (and_33_out, d_ff_16_q, not_2_out);
  and and_34 (and_34_out, d_ff_14_q, not_3_out);
  and and_35 (and_35_out, d_ff_15_q, not_2_out);
  and and_36 (and_36_out, d_ff_19_q, not_3_out);
  and and_37 (and_37_out, d_ff_7_q, not_2_out);
  and and_38 (and_38_out, d_ff_6_q, not_3_out);
  and and_39 (and_39_out, d_ff_2_q, not_2_out);
  and and_40 (and_40_out, d_ff_11_q, not_2_out);
  or or_14 (or_3_out[1], t_ff_10_q, t_ff_10_q);
  or or_15 (or_3_out[2], t_ff_15_q, t_ff_15_q);
  or or_16 (or_3_out[3], t_ff_16_q, t_ff_16_q);
  or or_17 (LED_10_2, and_25_out, and_26_out);
  or or_18 (LED_11_2, and_27_out, and_28_out);
  or or_19 (LED_12_2, and_29_out, and_30_out);
  or or_20 (LED_13_2, and_31_out, and_32_out);
  or or_21 (LED_14_2, and_33_out, and_34_out);
  or or_22 (LED_15_2, and_35_out, and_36_out);
  or or_23 (LED_16_2, and_37_out, and_38_out);
  or or_24 (LED_17_2, and_39_out, and_40_out);
  assign VEL_minus[3] = nor_1_out ? ~nor_1_out : 1'bz;  // Controlled_Inverter controlled_inverter_2
  assign VEL_plus[1] = nor_1_out ? ~nor_1_out : 1'bz;  // Controlled_Inverter controlled_inverter_3
  assign VEL_minus[2] = nor_1_out ? ~nor_1_out : 1'bz;  // Controlled_Inverter controlled_inverter_4
  assign VEL_minus[0] = nor_1_out ? nor_1_out : 1'bz;  // Controlled_Buffer controlled_buffer_7
  assign VEL_minus[1] = nor_1_out ? ~nor_1_out : 1'bz;  // Controlled_Inverter controlled_inverter_5
  assign VEL_plus[0] = nor_1_out ? ~nor_1_out : 1'bz;  // Controlled_Inverter controlled_inverter_6
  assign VEL_plus[1] = and_42_out ? ~and_42_out : 1'bz;  // Controlled_Inverter controlled_inverter_7
  assign VEL_plus[0] = and_42_out ? ~and_42_out : 1'bz;  // Controlled_Inverter controlled_inverter_8
  assign VEL_minus[0] = and_42_out ? ~and_42_out : 1'bz;  // Controlled_Inverter controlled_inverter_9
  assign VEL_minus[2] = and_42_out ? ~and_42_out : 1'bz;  // Controlled_Inverter controlled_inverter_10
  assign VEL_minus[1] = and_42_out ? and_42_out : 1'bz;  // Controlled_Buffer controlled_buffer_8
  not not_22 (not_22_out, or_3_out[3]);
  not not_23 (not_23_out, or_3_out[2]);
  assign VEL_minus[3] = and_43_out ? ~and_43_out : 1'bz;  // Controlled_Inverter controlled_inverter_11
  assign VEL_minus[2] = and_43_out ? and_43_out : 1'bz;  // Controlled_Buffer controlled_buffer_9
  assign VEL_minus[0] = and_43_out ? ~and_43_out : 1'bz;  // Controlled_Inverter controlled_inverter_12
  assign VEL_minus[1] = and_43_out ? ~and_43_out : 1'bz;  // Controlled_Inverter controlled_inverter_13
  assign VEL_plus[0] = and_43_out ? ~and_43_out : 1'bz;  // Controlled_Inverter controlled_inverter_14
  assign VEL_plus[1] = and_43_out ? ~and_43_out : 1'bz;  // Controlled_Inverter controlled_inverter_15
  nor nor_1 (nor_1_out, or_3_out[0], or_3_out[1], or_3_out[2], or_3_out[3]);
  assign VEL_minus[3] = or_3_out[3] ? ~or_3_out[3] : 1'bz;  // Controlled_Inverter controlled_inverter_16
  assign VEL_minus[3] = or_3_out[3] ? ~or_3_out[3] : 1'bz;  // Controlled_Inverter controlled_inverter_17
  assign VEL_minus[0] = or_3_out[3] ? ~or_3_out[3] : 1'bz;  // Controlled_Inverter controlled_inverter_18
  assign VEL_plus[1] = or_3_out[3] ? ~or_3_out[3] : 1'bz;  // Controlled_Inverter controlled_inverter_19
  assign VEL_minus[2] = or_3_out[3] ? or_3_out[3] : 1'bz;  // Controlled_Buffer controlled_buffer_10
  assign VEL_plus[0] = or_3_out[3] ? or_3_out[3] : 1'bz;  // Controlled_Buffer controlled_buffer_11
  assign VEL_minus[1] = or_3_out[3] ? or_3_out[3] : 1'bz;  // Controlled_Buffer controlled_buffer_12
  assign VEL_plus[1] = and_41_out ? ~and_41_out : 1'bz;  // Controlled_Inverter controlled_inverter_20
  assign VEL_plus[0] = and_41_out ? ~and_41_out : 1'bz;  // Controlled_Inverter controlled_inverter_21
  assign VEL_minus[1] = and_41_out ? ~and_41_out : 1'bz;  // Controlled_Inverter controlled_inverter_22
  assign VEL_minus[0] = and_41_out ? ~and_41_out : 1'bz;  // Controlled_Inverter controlled_inverter_23
  assign VEL_minus[2] = and_41_out ? ~and_41_out : 1'bz;  // Controlled_Inverter controlled_inverter_24
  assign VEL_minus[3] = and_41_out ? and_41_out : 1'bz;  // Controlled_Buffer controlled_buffer_13
  and and_41 (and_41_out, not_22_out, or_3_out[2]);
  assign VEL_minus[3] = and_42_out ? ~and_42_out : 1'bz;  // Controlled_Inverter controlled_inverter_25
  not not_24 (not_24_out, or_3_out[1]);
  and and_42 (and_42_out, not_22_out, not_24_out, or_3_out[0], not_23_out);
  and and_43 (and_43_out, or_3_out[1], not_22_out, not_23_out);

  assign Matriz_1 = {3'b000, {2{LED_15_2}}, 4'b0000};
  assign Matriz_2 = {1'b0, LED_13_2, LED_14_2, 2'b00, LED_16_2, 3'b000};
  assign Matriz_3 = {1'b0, LED_12_2, 4'b0000, LED_17_2, 2'b00};
  assign Matriz_4 = {2'b00, LED_11_2, 4'b0000, LED_0_2, 1'b0};
  assign Matriz_5 = {3'b000, LED_9_2, 4'b0000, LED_1_2};
  assign Matriz_6 = {2'b00, LED_10_2, 4'b0000, LED_2_2, 1'b0};
  assign Matriz_7 = {1'b0, LED_8_2, 4'b0000, LED_3_2, 2'b00};
  assign Matriz_8 = {1'b0, LED_7_2, LED_6_2, 2'b00, LED_4_2, 3'b000};
  assign Matriz_9 = {3'b000, {2{LED_5_2}}, 4'b0000};
  assign VEL_plus[3:2] = 2'b00;

  // Notes on the sheet:
  //   Velocidade Dividida por:
endmodule
