// Logisim project CI escrita 32.32.circ as structural Verilog: 3 circuits, main circuit main
module main (
  input  CLOCK,
  input  ON_OFF,
  output [7:0] A,
  output [31:0] D,
  output sel,
  output [31:0] out_6,
  output [31:0] out_7,
  output [31:0] out_8,
  output [31:0] out_9,
  output [31:0] out_10,
  output [31:0] out_11,
  output [31:0] out_12,
  output [31:0] out_13,
  output [31:0] out_14,
  output [31:0] out_15,
  output [31:0] out_16,
  output [31:0] out_17,
  output [31:0] out_18,
  output [31:0] out_19,
  output [31:0] out_20,
  output [31:0] out_21,
  output [31:0] out_22,
  output [31:0] out_23,
  output [31:0] out_24,
  output [31:0] out_25,
  output [31:0] out_26,
  output [31:0] out_27,
  output [31:0] out_28,
  output [31:0] out_29,
  output [31:0] out_30,
  output [31:0] out_31,
  output [31:0] out_32,
  output [31:0] out_33,
  output [31:0] out_34,
  output [31:0] out_35,
  output [31:0] out_36,
  output [31:0] out_37
);

  wire and_1_out, and_34_out, comparator_1_eq, controlled_buffer_1_out, controlled_buffer_2_out, d_ff_1_qn,
       not_1_out, not_2_out, or_1_out, shift_register_1_out, shift_register_1_q0, shift_register_1_q1,
       shift_register_1_q2, shift_register_1_q3, shift_register_1_q4, shift_register_1_q5,
       shift_register_1_q6, shift_register_1_q7, shift_register_1_q8, shift_register_1_q9,
       shift_register_1_q10, shift_register_1_q11, shift_register_1_q12, shift_register_1_q13,
       shift_register_1_q14, shift_register_1_q15, shift_register_1_q16, shift_register_1_q17,
       shift_register_1_q18, shift_register_1_q19, shift_register_1_q20, shift_register_1_q21,
       shift_register_1_q22, shift_register_1_q23, shift_register_1_q24, shift_register_1_q25,
       shift_register_1_q26, shift_register_1_q27, shift_register_1_q28, shift_register_1_q29,
       shift_register_1_q30, shift_register_1_q31;
  wire [31:0] and_2_out, and_3_out, and_4_out, and_5_out, and_6_out, and_7_out, and_8_out, and_9_out,
       and_10_out, and_11_out, and_12_out, and_13_out, and_14_out, and_15_out, and_16_out, and_17_out,
       and_18_out, and_19_out, and_20_out, and_21_out, and_22_out, and_23_out, and_24_out, and_25_out,
       and_26_out, and_27_out, and_28_out, and_29_out, and_30_out, and_31_out, and_32_out, and_33_out,
       aumentador_de_bits_1_out, aumentador_de_bits_2_out, aumentador_de_bits_3_out,
       aumentador_de_bits_4_out, aumentador_de_bits_5_out, aumentador_de_bits_6_out,
       aumentador_de_bits_7_out, aumentador_de_bits_8_out, aumentador_de_bits_9_out,
       aumentador_de_bits_10_out, aumentador_de_bits_11_out, aumentador_de_bits_12_out,
       aumentador_de_bits_13_out, aumentador_de_bits_14_out, aumentador_de_bits_15_out,
       aumentador_de_bits_16_out, aumentador_de_bits_17_out, aumentador_de_bits_18_out,
       aumentador_de_bits_19_out, aumentador_de_bits_20_out, aumentador_de_bits_21_out,
       aumentador_de_bits_22_out, aumentador_de_bits_23_out, aumentador_de_bits_24_out,
       aumentador_de_bits_25_out, aumentador_de_bits_26_out, aumentador_de_bits_27_out,
       aumentador_de_bits_28_out, aumentador_de_bits_29_out, aumentador_de_bits_30_out,
       aumentador_de_bits_31_out, aumentador_de_bits_32_out;

  T_Flip_Flop t_ff_1 (.clk(ON_OFF), .T(ON_OFF), .Q(sel));  // open: Qn, preset, reset, en
  not not_1 (not_1_out, ON_OFF);
  not not_2 (not_2_out, not_1_out);
  Counter counter_1 (.Q(A), .clk(and_1_out), .clr(comparator_1_eq));  // open: load, D, count, carry
  and and_1 (and_1_out, CLOCK, or_1_out);
  assign controlled_buffer_1_out = not_2_out ? 1'b1 : 1'bz;  // Controlled_Buffer controlled_buffer_1
  assign controlled_buffer_2_out = not_2_out ? 1'b0 : 1'bz;  // Controlled_Buffer controlled_buffer_2
  Shift_Register #(.length(32)) shift_register_1 (
    .in(shift_register_1_out), .clk(CLOCK), .out(shift_register_1_out), .load(controlled_buffer_1_out),
    .d0(controlled_buffer_1_out), .q0(shift_register_1_q0), .d1(controlled_buffer_2_out),
    .q1(shift_register_1_q1), .d2(controlled_buffer_2_out), .q2(shift_register_1_q2),
    .d3(controlled_buffer_2_out), .q3(shift_register_1_q3), .d4(controlled_buffer_2_out),
    .q4(shift_register_1_q4), .d5(controlled_buffer_2_out), .q5(shift_register_1_q5),
    .d6(controlled_buffer_2_out), .q6(shift_register_1_q6), .d7(controlled_buffer_2_out),
    .q7(shift_register_1_q7), .d8(controlled_buffer_2_out), .q8(shift_register_1_q8),
    .d9(controlled_buffer_2_out), .q9(shift_register_1_q9), .d10(controlled_buffer_2_out),
    .q10(shift_register_1_q10), .d11(controlled_buffer_2_out), .q11(shift_register_1_q11),
    .d12(controlled_buffer_2_out), .q12(shift_register_1_q12), .d13(controlled_buffer_2_out),
    .q13(shift_register_1_q13), .d14(controlled_buffer_2_out), .q14(shift_register_1_q14),
    .d15(controlled_buffer_2_out), .q15(shift_register_1_q15), .d16(controlled_buffer_2_out),
    .q16(shift_register_1_q16), .d17(controlled_buffer_2_out), .q17(shift_register_1_q17),
    .d18(controlled_buffer_2_out), .q18(shift_register_1_q18), .d19(controlled_buffer_2_out),
    .q19(shift_register_1_q19), .d20(controlled_buffer_2_out), .q20(shift_register_1_q20),
    .d21(controlled_buffer_2_out), .q21(shift_register_1_q21), .d22(controlled_buffer_2_out),
    .q22(shift_register_1_q22), .d23(controlled_buffer_2_out), .q23(shift_register_1_q23),
    .d24(controlled_buffer_2_out), .q24(shift_register_1_q24), .d25(controlled_buffer_2_out),
    .q25(shift_register_1_q25), .d26(controlled_buffer_2_out), .q26(shift_register_1_q26),
    .d27(controlled_buffer_2_out), .q27(shift_register_1_q27), .d28(controlled_buffer_2_out),
    .q28(shift_register_1_q28), .d29(controlled_buffer_2_out), .q29(shift_register_1_q29),
    .d30(controlled_buffer_2_out), .q30(shift_register_1_q30), .d31(controlled_buffer_2_out),
    .q31(shift_register_1_q31));  // open: shift, clr
  Comparator comparator_1 (.a(8'h20), .b(A), .eq(comparator_1_eq));  // open: gt, lt
  or or_1 (or_1_out, shift_register_1_q0, shift_register_1_q1, shift_register_1_q2, shift_register_1_q3, shift_register_1_q4, shift_register_1_q5, shift_register_1_q6, shift_register_1_q7, shift_register_1_q8, shift_register_1_q9, shift_register_1_q10, shift_register_1_q11, shift_register_1_q12, shift_register_1_q13, shift_register_1_q14, shift_register_1_q15, shift_register_1_q16, shift_register_1_q17, shift_register_1_q18, shift_register_1_q19, shift_register_1_q20, shift_register_1_q21, shift_register_1_q22, shift_register_1_q23, shift_register_1_q24, shift_register_1_q25, shift_register_1_q26, shift_register_1_q27, shift_register_1_q28, shift_register_1_q29, shift_register_1_q30, shift_register_1_q31);
  D_Flip_Flop d_ff_1 (
    .clk(shift_register_1_q31), .D(shift_register_1_q31), .Qn(d_ff_1_qn));  // open: Q, preset, en, reset
  assign and_2_out = D & aumentador_de_bits_1_out;  // AND_Gate and_2, 32 bits wide
  aumentador_de_bits aumentador_de_bits_1 (.IN(shift_register_1_q0), .Out(aumentador_de_bits_1_out));
  assign and_3_out = D & aumentador_de_bits_2_out;  // AND_Gate and_3, 32 bits wide
  aumentador_de_bits aumentador_de_bits_2 (.IN(shift_register_1_q1), .Out(aumentador_de_bits_2_out));
  assign and_4_out = D & aumentador_de_bits_3_out;  // AND_Gate and_4, 32 bits wide
  aumentador_de_bits aumentador_de_bits_3 (.IN(shift_register_1_q2), .Out(aumentador_de_bits_3_out));
  assign and_5_out = D & aumentador_de_bits_4_out;  // AND_Gate and_5, 32 bits wide
  aumentador_de_bits aumentador_de_bits_4 (.IN(shift_register_1_q3), .Out(aumentador_de_bits_4_out));
  assign and_6_out = D & aumentador_de_bits_5_out;  // AND_Gate and_6, 32 bits wide
  aumentador_de_bits aumentador_de_bits_5 (.IN(shift_register_1_q4), .Out(aumentador_de_bits_5_out));
  assign and_7_out = D & aumentador_de_bits_6_out;  // AND_Gate and_7, 32 bits wide
  aumentador_de_bits aumentador_de_bits_6 (.IN(shift_register_1_q5), .Out(aumentador_de_bits_6_out));
  assign and_8_out = D & aumentador_de_bits_7_out;  // AND_Gate and_8, 32 bits wide
  aumentador_de_bits aumentador_de_bits_7 (.IN(shift_register_1_q6), .Out(aumentador_de_bits_7_out));
  assign and_9_out = D & aumentador_de_bits_8_out;  // AND_Gate and_9, 32 bits wide
  aumentador_de_bits aumentador_de_bits_8 (.IN(shift_register_1_q7), .Out(aumentador_de_bits_8_out));
  assign and_10_out = D & aumentador_de_bits_9_out;  // AND_Gate and_10, 32 bits wide
  aumentador_de_bits aumentador_de_bits_9 (.IN(shift_register_1_q8), .Out(aumentador_de_bits_9_out));
  assign and_11_out = D & aumentador_de_bits_10_out;  // AND_Gate and_11, 32 bits wide
  aumentador_de_bits aumentador_de_bits_10 (.IN(shift_register_1_q9), .Out(aumentador_de_bits_10_out));
  assign and_12_out = D & aumentador_de_bits_11_out;  // AND_Gate and_12, 32 bits wide
  aumentador_de_bits aumentador_de_bits_11 (.IN(shift_register_1_q10), .Out(aumentador_de_bits_11_out));
  assign and_13_out = D & aumentador_de_bits_12_out;  // AND_Gate and_13, 32 bits wide
  aumentador_de_bits aumentador_de_bits_12 (.IN(shift_register_1_q11), .Out(aumentador_de_bits_12_out));
  assign and_14_out = D & aumentador_de_bits_13_out;  // AND_Gate and_14, 32 bits wide
  aumentador_de_bits aumentador_de_bits_13 (.IN(shift_register_1_q12), .Out(aumentador_de_bits_13_out));
  assign and_15_out = D & aumentador_de_bits_14_out;  // AND_Gate and_15, 32 bits wide
  aumentador_de_bits aumentador_de_bits_14 (.IN(shift_register_1_q13), .Out(aumentador_de_bits_14_out));
  assign and_16_out = D & aumentador_de_bits_15_out;  // AND_Gate and_16, 32 bits wide
  aumentador_de_bits aumentador_de_bits_15 (.IN(shift_register_1_q14), .Out(aumentador_de_bits_15_out));
  assign and_17_out = D & aumentador_de_bits_16_out;  // AND_Gate and_17, 32 bits wide
  aumentador_de_bits aumentador_de_bits_16 (.IN(shift_register_1_q15), .Out(aumentador_de_bits_16_out));
  assign and_18_out = D & aumentador_de_bits_17_out;  // AND_Gate and_18, 32 bits wide
  aumentador_de_bits aumentador_de_bits_17 (.IN(shift_register_1_q16), .Out(aumentador_de_bits_17_out));
  assign and_19_out = D & aumentador_de_bits_18_out;  // AND_Gate and_19, 32 bits wide
  aumentador_de_bits aumentador_de_bits_18 (.IN(shift_register_1_q17), .Out(aumentador_de_bits_18_out));
  assign and_20_out = D & aumentador_de_bits_19_out;  // AND_Gate and_20, 32 bits wide
  aumentador_de_bits aumentador_de_bits_19 (.IN(shift_register_1_q18), .Out(aumentador_de_bits_19_out));
  assign and_21_out = D & aumentador_de_bits_20_out;  // AND_Gate and_21, 32 bits wide
  aumentador_de_bits aumentador_de_bits_20 (.IN(shift_register_1_q19), .Out(aumentador_de_bits_20_out));
  assign and_22_out = D & aumentador_de_bits_21_out;  // AND_Gate and_22, 32 bits wide
  aumentador_de_bits aumentador_de_bits_21 (.IN(shift_register_1_q20), .Out(aumentador_de_bits_21_out));
  assign and_23_out = D & aumentador_de_bits_22_out;  // AND_Gate and_23, 32 bits wide
  aumentador_de_bits aumentador_de_bits_22 (.IN(shift_register_1_q21), .Out(aumentador_de_bits_22_out));
  assign and_24_out = D & aumentador_de_bits_23_out;  // AND_Gate and_24, 32 bits wide
  aumentador_de_bits aumentador_de_bits_23 (.IN(shift_register_1_q22), .Out(aumentador_de_bits_23_out));
  assign and_25_out = D & aumentador_de_bits_24_out;  // AND_Gate and_25, 32 bits wide
  aumentador_de_bits aumentador_de_bits_24 (.IN(shift_register_1_q23), .Out(aumentador_de_bits_24_out));
  assign and_26_out = D & aumentador_de_bits_25_out;  // AND_Gate and_26, 32 bits wide
  aumentador_de_bits aumentador_de_bits_25 (.IN(shift_register_1_q24), .Out(aumentador_de_bits_25_out));
  assign and_27_out = D & aumentador_de_bits_26_out;  // AND_Gate and_27, 32 bits wide
  aumentador_de_bits aumentador_de_bits_26 (.IN(shift_register_1_q25), .Out(aumentador_de_bits_26_out));
  assign and_28_out = D & aumentador_de_bits_27_out;  // AND_Gate and_28, 32 bits wide
  aumentador_de_bits aumentador_de_bits_27 (.IN(shift_register_1_q26), .Out(aumentador_de_bits_27_out));
  assign and_29_out = D & aumentador_de_bits_28_out;  // AND_Gate and_29, 32 bits wide
  aumentador_de_bits aumentador_de_bits_28 (.IN(shift_register_1_q27), .Out(aumentador_de_bits_28_out));
  assign and_30_out = D & aumentador_de_bits_29_out;  // AND_Gate and_30, 32 bits wide
  aumentador_de_bits aumentador_de_bits_29 (.IN(shift_register_1_q28), .Out(aumentador_de_bits_29_out));
  assign and_31_out = D & aumentador_de_bits_30_out;  // AND_Gate and_31, 32 bits wide
  aumentador_de_bits aumentador_de_bits_30 (.IN(shift_register_1_q29), .Out(aumentador_de_bits_30_out));
  assign and_32_out = D & aumentador_de_bits_31_out;  // AND_Gate and_32, 32 bits wide
  aumentador_de_bits aumentador_de_bits_31 (.IN(shift_register_1_q30), .Out(aumentador_de_bits_31_out));
  assign and_33_out = D & aumentador_de_bits_32_out;  // AND_Gate and_33, 32 bits wide
  aumentador_de_bits aumentador_de_bits_32 (.IN(shift_register_1_q31), .Out(aumentador_de_bits_32_out));
  and and_34 (and_34_out, d_ff_1_qn, and_1_out);
  translate translate_1 (.Reset(ON_OFF), .Clock(and_34_out), .Input(and_2_out), .Output(out_6));  // open: Set
  translate translate_2 (.Reset(ON_OFF), .Clock(and_34_out), .Input(and_3_out), .Output(out_7));  // open: Set
  translate translate_3 (.Reset(ON_OFF), .Clock(and_34_out), .Input(and_4_out), .Output(out_8));  // open: Set
  translate translate_4 (.Reset(ON_OFF), .Clock(and_34_out), .Input(and_5_out), .Output(out_9));  // open: Set
  translate translate_5 (.Reset(ON_OFF), .Clock(and_34_out), .Input(and_6_out), .Output(out_10));  // open: Set
  translate translate_6 (.Reset(ON_OFF), .Clock(and_34_out), .Input(and_7_out), .Output(out_11));  // open: Set
  translate translate_7 (.Reset(ON_OFF), .Clock(and_34_out), .Input(and_8_out), .Output(out_12));  // open: Set
  translate translate_8 (.Reset(ON_OFF), .Clock(and_34_out), .Input(and_9_out), .Output(out_13));  // open: Set
  translate translate_9 (.Reset(ON_OFF), .Clock(and_34_out), .Input(and_10_out), .Output(out_14));  // open: Set
  translate translate_10 (.Reset(ON_OFF), .Clock(and_34_out), .Input(and_11_out), .Output(out_15));  // open: Set
  translate translate_11 (.Reset(ON_OFF), .Clock(and_34_out), .Input(and_12_out), .Output(out_16));  // open: Set
  translate translate_12 (.Reset(ON_OFF), .Clock(and_34_out), .Input(and_13_out), .Output(out_17));  // open: Set
  translate translate_13 (.Reset(ON_OFF), .Clock(and_34_out), .Input(and_14_out), .Output(out_18));  // open: Set
  translate translate_14 (.Reset(ON_OFF), .Clock(and_34_out), .Input(and_15_out), .Output(out_19));  // open: Set
  translate translate_15 (.Reset(ON_OFF), .Clock(and_34_out), .Input(and_16_out), .Output(out_20));  // open: Set
  translate translate_16 (.Reset(ON_OFF), .Clock(and_34_out), .Input(and_17_out), .Output(out_21));  // open: Set
  translate translate_17 (.Reset(ON_OFF), .Clock(and_34_out), .Input(and_18_out), .Output(out_22));  // open: Set
  translate translate_18 (.Reset(ON_OFF), .Clock(and_34_out), .Input(and_19_out), .Output(out_23));  // open: Set
  translate translate_19 (.Reset(ON_OFF), .Clock(and_34_out), .Input(and_20_out), .Output(out_24));  // open: Set
  translate translate_20 (.Reset(ON_OFF), .Clock(and_34_out), .Input(and_21_out), .Output(out_25));  // open: Set
  translate translate_21 (.Reset(ON_OFF), .Clock(and_34_out), .Input(and_22_out), .Output(out_26));  // open: Set
  translate translate_22 (.Reset(ON_OFF), .Clock(and_34_out), .Input(and_23_out), .Output(out_27));  // open: Set
  translate translate_23 (.Reset(ON_OFF), .Clock(and_34_out), .Input(and_24_out), .Output(out_28));  // open: Set
  translate translate_24 (.Reset(ON_OFF), .Clock(and_34_out), .Input(and_25_out), .Output(out_29));  // open: Set
  translate translate_25 (.Reset(ON_OFF), .Clock(and_34_out), .Input(and_26_out), .Output(out_30));  // open: Set
  translate translate_26 (.Reset(ON_OFF), .Clock(and_34_out), .Input(and_27_out), .Output(out_31));  // open: Set
  translate translate_27 (.Reset(ON_OFF), .Clock(and_34_out), .Input(and_28_out), .Output(out_32));  // open: Set
  translate translate_28 (.Reset(ON_OFF), .Clock(and_34_out), .Input(and_29_out), .Output(out_33));  // open: Set
  translate translate_29 (.Reset(ON_OFF), .Clock(and_34_out), .Input(and_30_out), .Output(out_34));  // open: Set
  translate translate_30 (.Reset(ON_OFF), .Clock(and_34_out), .Input(and_31_out), .Output(out_35));  // open: Set
  translate translate_31 (.Reset(ON_OFF), .Clock(and_34_out), .Input(and_32_out), .Output(out_36));  // open: Set
  translate translate_32 (.Reset(ON_OFF), .Clock(and_34_out), .Input(and_33_out), .Output(out_37));  // open: Set
endmodule

module translate (
  input  Reset,
  input  Set,
  input  Clock,
  input  [31:0] Input,
  output [31:0] Output
);

  wire undriven;

  T_Flip_Flop t_ff_1 (
    .clk(Clock), .T(Input[0]), .Q(Output[0]), .preset(Set), .reset(Reset), .en(undriven));  // open: Qn
  T_Flip_Flop t_ff_2 (
    .clk(Clock), .T(Input[1]), .Q(Output[1]), .preset(Set), .reset(Reset), .en(undriven));  // open: Qn
  T_Flip_Flop t_ff_3 (
    .clk(Clock), .T(Input[2]), .Q(Output[2]), .preset(Set), .reset(Reset), .en(undriven));  // open: Qn
  T_Flip_Flop t_ff_4 (
    .clk(Clock), .T(Input[3]), .Q(Output[3]), .preset(Set), .reset(Reset), .en(undriven));  // open: Qn
  T_Flip_Flop t_ff_5 (
    .clk(Clock), .T(Input[4]), .Q(Output[4]), .preset(Set), .reset(Reset), .en(undriven));  // open: Qn
  T_Flip_Flop t_ff_6 (
    .clk(Clock), .T(Input[5]), .Q(Output[5]), .preset(Set), .reset(Reset), .en(undriven));  // open: Qn
  T_Flip_Flop t_ff_7 (
    .clk(Clock), .T(Input[6]), .Q(Output[6]), .preset(Set), .reset(Reset), .en(undriven));  // open: Qn
  T_Flip_Flop t_ff_8 (
    .clk(Clock), .T(Input[7]), .Q(Output[7]), .preset(Set), .reset(Reset), .en(undriven));  // open: Qn
  T_Flip_Flop t_ff_9 (
    .clk(Clock), .T(Input[8]), .Q(Output[8]), .preset(Set), .reset(Reset), .en(undriven));  // open: Qn
  T_Flip_Flop t_ff_10 (
    .clk(Clock), .T(Input[9]), .Q(Output[9]), .preset(Set), .reset(Reset), .en(undriven));  // open: Qn
  T_Flip_Flop t_ff_11 (
    .clk(Clock), .T(Input[10]), .Q(Output[10]), .preset(Set), .reset(Reset), .en(undriven));  // open: Qn
  T_Flip_Flop t_ff_12 (
    .clk(Clock), .T(Input[11]), .Q(Output[11]), .preset(Set), .reset(Reset), .en(undriven));  // open: Qn
  T_Flip_Flop t_ff_13 (
    .clk(Clock), .T(Input[12]), .Q(Output[12]), .preset(Set), .reset(Reset), .en(undriven));  // open: Qn
  T_Flip_Flop t_ff_14 (
    .clk(Clock), .T(Input[13]), .Q(Output[13]), .preset(Set), .reset(Reset), .en(undriven));  // open: Qn
  T_Flip_Flop t_ff_15 (
    .clk(Clock), .T(Input[14]), .Q(Output[14]), .preset(Set), .reset(Reset), .en(undriven));  // open: Qn
  T_Flip_Flop t_ff_16 (
    .clk(Clock), .T(Input[15]), .Q(Output[15]), .preset(Set), .reset(Reset), .en(undriven));  // open: Qn
  T_Flip_Flop t_ff_17 (
    .clk(Clock), .T(Input[16]), .Q(Output[16]), .preset(Set), .reset(Reset), .en(undriven));  // open: Qn
  T_Flip_Flop t_ff_18 (
    .clk(Clock), .T(Input[17]), .Q(Output[17]), .preset(Set), .reset(Reset), .en(undriven));  // open: Qn
  T_Flip_Flop t_ff_19 (
    .clk(Clock), .T(Input[18]), .Q(Output[18]), .preset(Set), .reset(Reset), .en(undriven));  // open: Qn
  T_Flip_Flop t_ff_20 (
    .clk(Clock), .T(Input[19]), .Q(Output[19]), .preset(Set), .reset(Reset), .en(undriven));  // open: Qn
  T_Flip_Flop t_ff_21 (
    .clk(Clock), .T(Input[20]), .Q(Output[20]), .preset(Set), .reset(Reset), .en(undriven));  // open: Qn
  T_Flip_Flop t_ff_22 (
    .clk(Clock), .T(Input[21]), .Q(Output[21]), .preset(Set), .reset(Reset), .en(undriven));  // open: Qn
  T_Flip_Flop t_ff_23 (
    .clk(Clock), .T(Input[22]), .Q(Output[22]), .preset(Set), .reset(Reset), .en(undriven));  // open: Qn
  T_Flip_Flop t_ff_24 (
    .clk(Clock), .T(Input[23]), .Q(Output[23]), .preset(Set), .reset(Reset), .en(undriven));  // open: Qn
  T_Flip_Flop t_ff_25 (
    .clk(Clock), .T(Input[24]), .Q(Output[24]), .preset(Set), .reset(Reset), .en(undriven));  // open: Qn
  T_Flip_Flop t_ff_26 (
    .clk(Clock), .T(Input[25]), .Q(Output[25]), .preset(Set), .reset(Reset), .en(undriven));  // open: Qn
  T_Flip_Flop t_ff_27 (
    .clk(Clock), .T(Input[26]), .Q(Output[26]), .preset(Set), .reset(Reset), .en(undriven));  // open: Qn
  T_Flip_Flop t_ff_28 (
    .clk(Clock), .T(Input[27]), .Q(Output[27]), .preset(Set), .reset(Reset), .en(undriven));  // open: Qn
  T_Flip_Flop t_ff_29 (
    .clk(Clock), .T(Input[28]), .Q(Output[28]), .preset(Set), .reset(Reset), .en(undriven));  // open: Qn
  T_Flip_Flop t_ff_30 (
    .clk(Clock), .T(Input[29]), .Q(Output[29]), .preset(Set), .reset(Reset), .en(undriven));  // open: Qn
  T_Flip_Flop t_ff_31 (.T(Input[30]), .Q(Output[30]), .preset(Set), .reset(Reset), .en(undriven));  // open: clk, Qn
  T_Flip_Flop t_ff_32 (
    .clk(Clock), .T(Input[31]), .Q(Output[31]), .preset(Set), .reset(Reset), .en(undriven));  // open: Qn
endmodule

module aumentador_de_bits (
  input  IN,
  output [31:0] Out
);


  assign Out = {32{IN}};
endmodule
