// Logisim project CI joystick.circ as structural Verilog: 1 circuit, main circuit main
module main (
  input  [3:0] EIXO_x,
  input  [3:0] EIXO_Y,
  output [14:0] Matriz_0,
  output [14:0] Matriz_1,
  output [14:0] Matriz_2,
  output [14:0] Matriz_3,
  output [14:0] Matriz_4,
  output [14:0] Matriz_5,
  output [14:0] Matriz_6,
  output [14:0] Matriz_7,
  output [14:0] Matriz_8,
  output [14:0] Matriz_9,
  output [14:0] Matriz_10,
  output [14:0] Matriz_11,
  output [14:0] Matriz_12,
  output [14:0] Matriz_13,
  output [14:0] Matriz_14
);

  wire decoder_1_out0, decoder_1_out1, decoder_1_out2, decoder_1_out3, decoder_1_out4, decoder_1_out5,
       decoder_1_out6, decoder_1_out7, decoder_1_out8, decoder_1_out9, decoder_1_out10, decoder_1_out11,
       decoder_1_out12, decoder_1_out13, decoder_1_out14, decoder_1_out15, decoder_2_out1, decoder_2_out2,
       decoder_2_out3, decoder_2_out4, decoder_2_out5, decoder_2_out6, decoder_2_out7, decoder_2_out8,
       decoder_2_out9, decoder_2_out10, decoder_2_out11, decoder_2_out12, decoder_2_out13, decoder_2_out14,
       decoder_2_out15;

  Decoder #(.select(4)) decoder_1 (
    .out0(decoder_1_out0), .out1(decoder_1_out1), .out2(decoder_1_out2), .out3(decoder_1_out3),
    .out4(decoder_1_out4), .out5(decoder_1_out5), .out6(decoder_1_out6), .out7(decoder_1_out7),
    .out8(decoder_1_out8), .out9(decoder_1_out9), .out10(decoder_1_out10), .out11(decoder_1_out11),
    .out12(decoder_1_out12), .out13(decoder_1_out13), .out14(decoder_1_out14), .out15(decoder_1_out15),
    .sel(EIXO_x));  // open: en
  Decoder #(.select(4)) decoder_2 (
    .out1(decoder_2_out1), .out2(decoder_2_out2), .out3(decoder_2_out3), .out4(decoder_2_out4),
    .out5(decoder_2_out5), .out6(decoder_2_out6), .out7(decoder_2_out7), .out8(decoder_2_out8),
    .out9(decoder_2_out9), .out10(decoder_2_out10), .out11(decoder_2_out11), .out12(decoder_2_out12),
    .out13(decoder_2_out13), .out14(decoder_2_out14), .out15(decoder_2_out15), .sel(EIXO_Y));  // open: out0, en
  and and_1 (Matriz_0[14], decoder_1_out1, decoder_2_out1);
  and and_2 (Matriz_0[13], decoder_1_out2, decoder_2_out1);
  and and_3 (Matriz_0[12], decoder_1_out3, decoder_2_out1);
  and and_4 (Matriz_0[11], decoder_1_out4, decoder_2_out1);
  and and_5 (Matriz_0[10], decoder_1_out5, decoder_2_out1);
  and and_6 (Matriz_0[9], decoder_1_out6, decoder_2_out1);
  and and_7 (Matriz_0[8], decoder_1_out7, decoder_2_out1);
  and and_8 (Matriz_0[7], decoder_1_out8, decoder_2_out1);
  and and_9 (Matriz_0[6], decoder_1_out9, decoder_2_out1);
  and and_10 (Matriz_0[5], decoder_1_out10, decoder_2_out1);
  and and_11 (Matriz_0[4], decoder_1_out11, decoder_2_out1);
  and and_12 (Matriz_0[3], decoder_1_out12, decoder_2_out1);
  and and_13 (Matriz_0[2], decoder_1_out13, decoder_2_out1);
  and and_14 (Matriz_0[1], decoder_1_out14, decoder_2_out1);
  and and_15 (Matriz_0[0], decoder_1_out15, decoder_2_out1);
  and and_16 (Matriz_1[14], decoder_1_out1, decoder_2_out2);
  and and_17 (Matriz_1[13], decoder_1_out2, decoder_2_out2);
  and and_18 (Matriz_1[12], decoder_1_out3, decoder_2_out2);
  and and_19 (Matriz_1[11], decoder_1_out4, decoder_2_out2);
  and and_20 (Matriz_1[10], decoder_1_out5, decoder_2_out2);
  and and_21 (Matriz_1[9], decoder_1_out6, decoder_2_out2);
  and and_22 (Matriz_1[8], decoder_1_out7, decoder_2_out2);
  and and_23 (Matriz_1[7], decoder_1_out8, decoder_2_out2);
  and and_24 (Matriz_1[6], decoder_1_out9, decoder_2_out2);
  and and_25 (Matriz_1[5], decoder_1_out10, decoder_2_out2);
  and and_26 (Matriz_1[4], decoder_1_out11, decoder_2_out2);
  and and_27 (Matriz_1[3], decoder_1_out12, decoder_2_out2);
  and and_28 (Matriz_1[2], decoder_1_out13, decoder_2_out2);
  and and_29 (Matriz_1[1], decoder_1_out14, decoder_2_out2);
  and and_30 (Matriz_1[0], decoder_1_out15, decoder_2_out2);
  and and_31 (Matriz_2[14], decoder_1_out1, decoder_2_out3);
  and and_32 (Matriz_2[13], decoder_1_out2, decoder_2_out3);
  and and_33 (Matriz_2[12], decoder_1_out3, decoder_2_out3);
  and and_34 (Matriz_2[11], decoder_1_out4, decoder_2_out3);
  and and_35 (Matriz_2[10], decoder_1_out5, decoder_2_out3);
  and and_36 (Matriz_2[9], decoder_1_out6, decoder_2_out3);
  and and_37 (Matriz_2[8], decoder_1_out7, decoder_2_out3);
  and and_38 (Matriz_2[7], decoder_1_out8, decoder_2_out3);
  and and_39 (Matriz_2[6], decoder_1_out9, decoder_2_out3);
  and and_40 (Matriz_2[5], decoder_1_out10, decoder_2_out3);
  and and_41 (Matriz_2[4], decoder_1_out11, decoder_2_out3);
  and and_42 (Matriz_2[3], decoder_1_out12, decoder_2_out3);
  and and_43 (Matriz_2[2], decoder_1_out13, decoder_2_out3);
  and and_44 (Matriz_2[1], decoder_1_out14, decoder_2_out3);
  and and_45 (Matriz_2[0], decoder_1_out15, decoder_2_out3);
  and and_46 (Matriz_3[14], decoder_1_out1, decoder_2_out4);
  and and_47 (Matriz_3[13], decoder_1_out2, decoder_2_out4);
  and and_48 (Matriz_3[12], decoder_1_out3, decoder_2_out4);
  and and_49 (Matriz_3[11], decoder_1_out4, decoder_2_out4);
  and and_50 (Matriz_3[10], decoder_1_out5, decoder_2_out4);
  and and_51 (Matriz_3[9], decoder_1_out6, decoder_2_out4);
  and and_52 (Matriz_3[8], decoder_1_out7, decoder_2_out4);
  and and_53 (Matriz_3[7], decoder_1_out8, decoder_2_out4);
  and and_54 (Matriz_3[6], decoder_1_out9, decoder_2_out4);
  and and_55 (Matriz_3[5], decoder_1_out10, decoder_2_out4);
  and and_56 (Matriz_3[4], decoder_1_out11, decoder_2_out4);
  and and_57 (Matriz_3[3], decoder_1_out12, decoder_2_out4);
  and and_58 (Matriz_3[2], decoder_1_out13, decoder_2_out4);
  and and_59 (Matriz_3[1], decoder_1_out14, decoder_2_out4);
  and and_60 (Matriz_3[0], decoder_1_out15, decoder_2_out4);
  and and_61 (Matriz_4[14], decoder_1_out1, decoder_2_out5);
  and and_62 (Matriz_4[13], decoder_1_out2, decoder_2_out5);
  and and_63 (Matriz_4[12], decoder_1_out3, decoder_2_out5);
  and and_64 (Matriz_4[11], decoder_1_out4, decoder_2_out5);
  and and_65 (Matriz_4[10], decoder_1_out5, decoder_2_out5);
  and and_66 (Matriz_4[9], decoder_1_out6, decoder_2_out5);
  and and_67 (Matriz_4[8], decoder_1_out7, decoder_2_out5);
  and and_68 (Matriz_4[7], decoder_1_out8, decoder_2_out5);
  and and_69 (Matriz_4[6], decoder_1_out9, decoder_2_out5);
  and and_70 (Matriz_4[5], decoder_1_out10, decoder_2_out5);
  and and_71 (Matriz_4[4], decoder_1_out11, decoder_2_out5);
  and and_72 (Matriz_4[3], decoder_1_out12, decoder_2_out5);
  and and_73 (Matriz_4[2], decoder_1_out13, decoder_2_out5);
  and and_74 (Matriz_4[1], decoder_1_out14, decoder_2_out5);
  and and_75 (Matriz_4[0], decoder_1_out15, decoder_2_out5);
  and and_76 (Matriz_5[14], decoder_1_out1, decoder_2_out6);
  and and_77 (Matriz_5[13], decoder_1_out2, decoder_2_out6);
  and and_78 (Matriz_5[12], decoder_1_out3, decoder_2_out6);
  and and_79 (Matriz_5[11], decoder_1_out4, decoder_2_out6);
  and and_80 (Matriz_5[10], decoder_1_out5, decoder_2_out6);
  and and_81 (Matriz_5[9], decoder_1_out6, decoder_2_out6);
  and and_82 (Matriz_5[8], decoder_1_out7, decoder_2_out6);
  and and_83 (Matriz_5[7], decoder_1_out8, decoder_2_out6);
  and and_84 (Matriz_5[6], decoder_1_out9, decoder_2_out6);
  and and_85 (Matriz_5[5], decoder_1_out10, decoder_2_out6);
  and and_86 (Matriz_5[4], decoder_1_out11, decoder_2_out6);
  and and_87 (Matriz_5[3], decoder_1_out12, decoder_2_out6);
  and and_88 (Matriz_5[2], decoder_1_out13, decoder_2_out6);
  and and_89 (Matriz_5[1], decoder_1_out14, decoder_2_out6);
  and and_90 (Matriz_5[0], decoder_1_out15, decoder_2_out6);
  and and_91 (Matriz_6[14], decoder_1_out1, decoder_2_out7);
  and and_92 (Matriz_6[13], decoder_1_out2, decoder_2_out7);
  and and_93 (Matriz_6[12], decoder_1_out3, decoder_2_out7);
  and and_94 (Matriz_6[11], decoder_1_out4, decoder_2_out7);
  and and_95 (Matriz_6[10], decoder_1_out5, decoder_2_out7);
  and and_96 (Matriz_6[9], decoder_1_out6, decoder_2_out7);
  and and_97 (Matriz_6[8], decoder_1_out7, decoder_2_out7);
  and and_98 (Matriz_6[7], decoder_1_out8, decoder_2_out7);
  and and_99 (Matriz_6[6], decoder_1_out9, decoder_2_out7);
  and and_100 (Matriz_6[5], decoder_1_out10, decoder_2_out7);
  and and_101 (Matriz_6[4], decoder_1_out11, decoder_2_out7);
  and and_102 (Matriz_6[3], decoder_1_out12, decoder_2_out7);
  and and_103 (Matriz_6[2], decoder_1_out13, decoder_2_out7);
  and and_104 (Matriz_6[1], decoder_1_out14, decoder_2_out7);
  and and_105 (Matriz_6[0], decoder_1_out15, decoder_2_out7);
  and and_106 (Matriz_7[14], decoder_1_out1, decoder_2_out8);
  and and_107 (Matriz_7[13], decoder_1_out2, decoder_2_out8);
  and and_108 (Matriz_7[12], decoder_1_out3, decoder_2_out8);
  and and_109 (Matriz_7[11], decoder_1_out4, decoder_2_out8);
  and and_110 (Matriz_7[10], decoder_1_out5, decoder_2_out8);
  and and_111 (Matriz_7[9], decoder_1_out6, decoder_2_out8);
  and and_112 (Matriz_7[8], decoder_1_out7, decoder_2_out8);
  and and_113 (Matriz_7[7], decoder_1_out8, decoder_2_out8);
  and and_114 (Matriz_7[6], decoder_1_out9, decoder_2_out8);
  and and_115 (Matriz_7[5], decoder_1_out10, decoder_2_out8);
  and and_116 (Matriz_7[4], decoder_1_out11, decoder_2_out8);
  and and_117 (Matriz_7[3], decoder_1_out12, decoder_2_out8);
  and and_118 (Matriz_7[2], decoder_1_out13, decoder_2_out8);
  and and_119 (Matriz_7[1], decoder_1_out14, decoder_2_out8);
  and and_120 (Matriz_7[0], decoder_1_out15, decoder_2_out8);
  and and_121 (Matriz_8[14], decoder_1_out1, decoder_2_out9);
  and and_122 (Matriz_8[13], decoder_1_out2, decoder_2_out9);
  and and_123 (Matriz_8[12], decoder_1_out3, decoder_2_out9);
  and and_124 (Matriz_8[11], decoder_1_out4, decoder_2_out9);
  and and_125 (Matriz_8[10], decoder_1_out5, decoder_2_out9);
  and and_126 (Matriz_8[9], decoder_1_out6, decoder_2_out9);
  and and_127 (Matriz_8[8], decoder_1_out7, decoder_2_out9);
  and and_128 (Matriz_8[7], decoder_1_out8, decoder_2_out9);
  and and_129 (Matriz_8[6], decoder_1_out9, decoder_2_out9);
  and and_130 (Matriz_8[5], decoder_1_out10, decoder_2_out9);
  and and_131 (Matriz_8[4], decoder_1_out11, decoder_2_out9);
  and and_132 (Matriz_8[3], decoder_1_out12, decoder_2_out9);
  and and_133 (Matriz_8[2], decoder_1_out13, decoder_2_out9);
  and and_134 (Matriz_8[1], decoder_1_out14, decoder_2_out9);
  and and_135 (Matriz_8[0], decoder_1_out15, decoder_2_out9);
  and and_136 (Matriz_9[14], decoder_1_out1, decoder_2_out10);
  and and_137 (Matriz_9[13], decoder_1_out2, decoder_2_out10);
  and and_138 (Matriz_9[12], decoder_1_out3, decoder_2_out10);
  and and_139 (Matriz_9[11], decoder_1_out4, decoder_2_out10);
  and and_140 (Matriz_9[10], decoder_1_out5, decoder_2_out10);
  and and_141 (Matriz_9[9], decoder_1_out6, decoder_2_out10);
  and and_142 (Matriz_9[8], decoder_1_out7, decoder_2_out10);
  and and_143 (Matriz_9[7], decoder_1_out8, decoder_2_out10);
  and and_144 (Matriz_9[6], decoder_1_out9, decoder_2_out10);
  and and_145 (Matriz_9[5], decoder_1_out10, decoder_2_out10);
  and and_146 (Matriz_9[4], decoder_1_out11, decoder_2_out10);
  and and_147 (Matriz_9[3], decoder_1_out12, decoder_2_out10);
  and and_148 (Matriz_9[2], decoder_1_out13, decoder_2_out10);
  and and_149 (Matriz_9[1], decoder_1_out14, decoder_2_out10);
  and and_150 (Matriz_9[0], decoder_1_out15, decoder_2_out10);
  and and_151 (Matriz_10[14], decoder_1_out1, decoder_2_out11);
  and and_152 (Matriz_10[13], decoder_1_out2, decoder_2_out11);
  and and_153 (Matriz_10[12], decoder_1_out3, decoder_2_out11);
  and and_154 (Matriz_10[11], decoder_1_out4, decoder_2_out11);
  and and_155 (Matriz_10[10], decoder_1_out5, decoder_2_out11);
  and and_156 (Matriz_10[9], decoder_1_out6, decoder_2_out11);
  and and_157 (Matriz_10[8], decoder_1_out7, decoder_2_out11);
  and and_158 (Matriz_10[7], decoder_1_out8, decoder_2_out11);
  and and_159 (Matriz_10[6], decoder_1_out9, decoder_2_out11);
  and and_160 (Matriz_10[5], decoder_1_out10, decoder_2_out11);
  and and_161 (Matriz_10[4], decoder_1_out11, decoder_2_out11);
  and and_162 (Matriz_10[3], decoder_1_out12, decoder_2_out11);
  and and_163 (Matriz_10[2], decoder_1_out13, decoder_2_out11);
  and and_164 (Matriz_10[1], decoder_1_out14, decoder_2_out11);
  and and_165 (Matriz_10[0], decoder_1_out15, decoder_2_out11);
  and and_166 (Matriz_11[14], decoder_1_out1, decoder_2_out12);
  and and_167 (Matriz_11[13], decoder_1_out2, decoder_2_out12);
  and and_168 (Matriz_11[12], decoder_1_out3, decoder_2_out12);
  and and_169 (Matriz_11[11], decoder_1_out4, decoder_2_out12);
  and and_170 (Matriz_11[10], decoder_1_out5, decoder_2_out12);
  and and_171 (Matriz_11[9], decoder_1_out6, decoder_2_out12);
  and and_172 (Matriz_11[8], decoder_1_out7, decoder_2_out12);
  and and_173 (Matriz_11[7], decoder_1_out8, decoder_2_out12);
  and and_174 (Matriz_11[6], decoder_1_out9, decoder_2_out12);
  and and_175 (Matriz_11[5], decoder_1_out10, decoder_2_out12);
  and and_176 (Matriz_11[4], decoder_1_out11, decoder_2_out12);
  and and_177 (Matriz_11[3], decoder_1_out12, decoder_2_out12);
  and and_178 (Matriz_11[2], decoder_1_out13, decoder_2_out12);
  and and_179 (Matriz_11[1], decoder_1_out14, decoder_2_out12);
  and and_180 (Matriz_11[0], decoder_1_out15, decoder_2_out12);
  and and_181 (Matriz_12[14], decoder_1_out1, decoder_2_out13);
  and and_182 (Matriz_12[13], decoder_1_out2, decoder_2_out13);
  and and_183 (Matriz_12[12], decoder_1_out3, decoder_2_out13);
  and and_184 (Matriz_12[11], decoder_1_out4, decoder_2_out13);
  and and_185 (Matriz_12[10], decoder_1_out5, decoder_2_out13);
  and and_186 (Matriz_12[9], decoder_1_out6, decoder_2_out13);
  and and_187 (Matriz_12[8], decoder_1_out7, decoder_2_out13);
  and and_188 (Matriz_12[7], decoder_1_out8, decoder_2_out13);
  and and_189 (Matriz_12[6], decoder_1_out9, decoder_2_out13);
  and and_190 (Matriz_12[5], decoder_1_out10, decoder_2_out13);
  and and_191 (Matriz_12[4], decoder_1_out11, decoder_2_out13);
  and and_192 (Matriz_12[3], decoder_1_out12, decoder_2_out13);
  and and_193 (Matriz_12[2], decoder_1_out13, decoder_2_out13);
  and and_194 (Matriz_12[1], decoder_1_out14, decoder_2_out13);
  and and_195 (Matriz_12[0], decoder_1_out15, decoder_2_out13);
  and and_196 (Matriz_13[14], decoder_1_out1, decoder_2_out14);
  and and_197 (Matriz_13[13], decoder_1_out2, decoder_2_out14);
  and and_198 (Matriz_13[12], decoder_1_out3, decoder_2_out14);
  and and_199 (Matriz_13[11], decoder_1_out4, decoder_2_out14);
  and and_200 (Matriz_13[10], decoder_1_out5, decoder_2_out14);
  and and_201 (Matriz_13[9], decoder_1_out6, decoder_2_out14);
  and and_202 (Matriz_13[8], decoder_1_out7, decoder_2_out14);
  and and_203 (Matriz_13[7], decoder_1_out8, decoder_2_out14);
  and and_204 (Matriz_13[6], decoder_1_out9, decoder_2_out14);
  and and_205 (Matriz_13[5], decoder_1_out10, decoder_2_out14);
  and and_206 (Matriz_13[4], decoder_1_out11, decoder_2_out14);
  and and_207 (Matriz_13[3], decoder_1_out12, decoder_2_out14);
  and and_208 (Matriz_13[2], decoder_1_out13, decoder_2_out14);
  and and_209 (Matriz_13[1], decoder_1_out14, decoder_2_out14);
  and and_210 (Matriz_13[0], decoder_1_out15, decoder_2_out14);
  and and_211 (Matriz_14[14], decoder_1_out1, decoder_2_out15);
  and and_212 (Matriz_14[13], decoder_1_out2, decoder_2_out15);
  and and_213 (Matriz_14[12], decoder_1_out3, decoder_2_out15);
  and and_214 (Matriz_14[11], decoder_1_out4, decoder_2_out15);
  and and_215 (Matriz_14[10], decoder_1_out5, decoder_2_out15);
  and and_216 (Matriz_14[9], decoder_1_out6, decoder_2_out15);
  and and_217 (Matriz_14[8], decoder_1_out7, decoder_2_out15);
  and and_218 (Matriz_14[7], decoder_1_out8, decoder_2_out15);
  and and_219 (Matriz_14[6], decoder_1_out9, decoder_2_out15);
  and and_220 (Matriz_14[5], decoder_1_out10, decoder_2_out15);
  and and_221 (Matriz_14[4], decoder_1_out11, decoder_2_out15);
  and and_222 (Matriz_14[3], decoder_1_out12, decoder_2_out15);
  and and_223 (Matriz_14[2], decoder_1_out13, decoder_2_out15);
  and and_224 (Matriz_14[1], decoder_1_out14, decoder_2_out15);
  and and_225 (Matriz_14[0], decoder_1_out15, decoder_2_out15);
endmodule
