// Logisim project CI led em coração.circ as structural Verilog: 1 circuit, main circuit main
module main (
  input  _0,
  input  _1,
  input  _2,
  input  _3,
  input  _4,
  input  _5,
  input  _6,
  input  _7,
  input  _8,
  input  _9,
  input  _10,
  input  _11,
  input  _12,
  input  _13,
  input  _14,
  input  _15,
  input  _16,
  input  _17,
  output out_19,
  output out_20,
  output out_21,
  output out_22,
  output out_23,
  output out_24,
  output out_25,
  output out_26,
  output out_27,
  output out_28,
  output out_29,
  output out_30,
  output out_31,
  output out_32,
  output out_33,
  output out_34,
  output out_35,
  output out_36
);


  assign _15 = _9;
  assign _17 = _8;
  assign out_19 = _16;
  assign out_20 = _2;
  assign out_21 = _9;
  assign out_22 = _8;
  assign out_23 = _1;
  assign out_24 = _3;
  assign out_25 = _0;
  assign out_26 = _13;
  assign out_27 = _4;
  assign out_28 = _14;
  assign out_29 = _5;
  assign out_30 = _12;
  assign out_31 = _6;
  assign out_32 = _11;
  assign out_33 = _7;
  assign out_34 = _10;
  assign out_35 = _8;
  assign out_36 = _9;
endmodule
