// Logisim project CI redutor de clock.circ as structural Verilog: 1 circuit, main circuit Redutor de Clock
module Redutor_de_Clock (
  input  CLOCK,
  input  btn_atualizar,
  output Saida_1,
  output Saida_2,
  output Saida_3,
  output Saida_4,
  output Saida_5,
  output Saida_6,
  output Saida_7,
  output [6:0] Saida_display_de_leds,
  output [6:0] Saida_display_de_leds_2,
  output [6:0] Saida_display_de_leds_3,
  output [6:0] Saida_display_de_leds_4,
  output [6:0] Saida_display_de_leds_5
);

  wire controlled_buffer_1_out, or_1_out;

  or or_1 (or_1_out, CLOCK, btn_atualizar);
  assign controlled_buffer_1_out = btn_atualizar ? btn_atualizar : 1'bz;  // Controlled_Buffer controlled_buffer_1
  D_Flip_Flop d_ff_1 (
    .clk(or_1_out), .D(Saida_7), .Q(Saida_1), .preset(controlled_buffer_1_out));  // open: Qn, en, reset
  D_Flip_Flop d_ff_2 (
    .clk(or_1_out), .D(Saida_1), .Q(Saida_2), .reset(controlled_buffer_1_out));  // open: Qn, preset, en
  D_Flip_Flop d_ff_3 (
    .clk(or_1_out), .D(Saida_2), .Q(Saida_3), .reset(controlled_buffer_1_out));  // open: Qn, preset, en
  D_Flip_Flop d_ff_4 (
    .clk(or_1_out), .D(Saida_3), .Q(Saida_4), .reset(controlled_buffer_1_out));  // open: Qn, preset, en
  D_Flip_Flop d_ff_5 (
    .clk(or_1_out), .D(Saida_4), .Q(Saida_5), .reset(controlled_buffer_1_out));  // open: Qn, preset, en
  D_Flip_Flop d_ff_6 (
    .clk(or_1_out), .D(Saida_5), .Q(Saida_6), .reset(controlled_buffer_1_out));  // open: Qn, preset, en
  D_Flip_Flop d_ff_7 (
    .clk(or_1_out), .D(Saida_6), .Q(Saida_7), .reset(controlled_buffer_1_out));  // open: Qn, preset, en

  assign Saida_display_de_leds = {Saida_1, Saida_2, Saida_3, Saida_4, Saida_5, Saida_6, Saida_7};
  assign Saida_display_de_leds_2 = {Saida_1, Saida_2, Saida_3, Saida_4, Saida_5, Saida_6, Saida_7};
  assign Saida_display_de_leds_3 = {Saida_1, Saida_2, Saida_3, Saida_4, Saida_5, Saida_6, Saida_7};
  assign Saida_display_de_leds_4 = {Saida_1, Saida_2, Saida_3, Saida_4, Saida_5, Saida_6, Saida_7};
  assign Saida_display_de_leds_5 = {Saida_1, Saida_2, Saida_3, Saida_4, Saida_5, Saida_6, Saida_7};
endmodule
