// Logisim project teste de cis.circ as structural Verilog: 2 circuits, main circuit main
module main (
  input  in_1,
  input  in_2,
  input  in_3,
  input  in_4
);

  wire button_1_out, button_2_out, button_3_out, button_4_out, button_5_out, button_6_out, button_7_out,
       button_8_out, clock_1_out, clock_2_out, clock_3_out, clock_4_out, cod_display_7seg_adaptavel_1_a_2,
       cod_display_7seg_adaptavel_1_b_2, cod_display_7seg_adaptavel_1_c_2, cod_display_7seg_adaptavel_1_d_2,
       cod_display_7seg_adaptavel_1_e, cod_display_7seg_adaptavel_1_f, cod_display_7seg_adaptavel_1_g,
       cod_display_7seg_adaptavel_1_ponto_2, cod_display_7seg_adaptavel_2_a_2,
       cod_display_7seg_adaptavel_2_b_2, cod_display_7seg_adaptavel_2_c_2, cod_display_7seg_adaptavel_2_d_2,
       cod_display_7seg_adaptavel_2_e, cod_display_7seg_adaptavel_2_f, cod_display_7seg_adaptavel_2_g,
       cod_display_7seg_adaptavel_2_ponto_2, cod_display_7seg_adaptavel_3_a_2,
       cod_display_7seg_adaptavel_3_b_2, cod_display_7seg_adaptavel_3_c_2, cod_display_7seg_adaptavel_3_d_2,
       cod_display_7seg_adaptavel_3_e, cod_display_7seg_adaptavel_3_f, cod_display_7seg_adaptavel_3_g,
       cod_display_7seg_adaptavel_3_ponto_2, cod_display_7seg_adaptavel_4_a_2,
       cod_display_7seg_adaptavel_4_b_2, cod_display_7seg_adaptavel_4_c_2, cod_display_7seg_adaptavel_4_d_2,
       cod_display_7seg_adaptavel_4_e, cod_display_7seg_adaptavel_4_f, cod_display_7seg_adaptavel_4_g,
       cod_display_7seg_adaptavel_4_ponto_2, cod_display_7seg_adaptavel_5_a_2,
       cod_display_7seg_adaptavel_5_b_2, cod_display_7seg_adaptavel_5_c_2, cod_display_7seg_adaptavel_5_d_2,
       cod_display_7seg_adaptavel_5_e, cod_display_7seg_adaptavel_5_f, cod_display_7seg_adaptavel_5_g,
       cod_display_7seg_adaptavel_5_ponto_2, cod_display_7seg_adaptavel_6_a_2,
       cod_display_7seg_adaptavel_6_b_2, cod_display_7seg_adaptavel_6_c_2, cod_display_7seg_adaptavel_6_d_2,
       cod_display_7seg_adaptavel_6_e, cod_display_7seg_adaptavel_6_f, cod_display_7seg_adaptavel_6_g,
       cod_display_7seg_adaptavel_6_ponto_2, cod_display_7seg_adaptavel_7_a_2,
       cod_display_7seg_adaptavel_7_b_2, cod_display_7seg_adaptavel_7_c_2, cod_display_7seg_adaptavel_7_d_2,
       cod_display_7seg_adaptavel_7_e, cod_display_7seg_adaptavel_7_f, cod_display_7seg_adaptavel_7_g,
       cod_display_7seg_adaptavel_7_ponto_2, \coração_de_leds_1_led_0_2 , \coração_de_leds_1_led_1_2 ,
       \coração_de_leds_1_led_2_2 , \coração_de_leds_1_led_3_2 , \coração_de_leds_1_led_4_2 ,
       \coração_de_leds_1_led_5_2 , \coração_de_leds_1_led_6_2 , \coração_de_leds_1_led_7_2 ,
       \coração_de_leds_1_led_8_2 , \coração_de_leds_1_led_9_2 , \coração_de_leds_1_led_10_2 ,
       \coração_de_leds_1_led_11_2 , \coração_de_leds_1_led_12_2 , \coração_de_leds_1_led_13_2 ,
       \coração_de_leds_1_led_14_2 , \coração_de_leds_1_led_15_2 , \coração_de_leds_1_led_16_2 ,
       \coração_de_leds_1_led_17_2 , main_2_out_19, main_2_out_20, main_2_out_21, main_2_out_22,
       main_2_out_23, main_2_out_24, main_2_out_25, main_2_out_26, main_2_out_27, main_2_out_28,
       main_2_out_29, main_2_out_30, main_2_out_31, main_2_out_32, main_2_out_33, main_2_out_34,
       main_2_out_35, main_2_out_36;
  wire [3:0] contador_assincrono_crescente_1_saida_bcd, contador_asssincrono_decrescente_1_saida_bcd,
       contador_decimal_1_saida_bcd, contador_hexadecimal_1_saida_bcd, contador_qualquer_1_saida_bcd,
       contador_sincrono_impar_1_saiuda_bcd, contador_sincrono_par_1_saida_bcd,
       \coração_de_leds_1_vel_minus , \coração_de_leds_1_vel_plus , joystick_1_x, joystick_1_y,
       main_3_hor_minus, main_3_hor_plus, main_3_min_minus, main_3_min_plus, main_3_seg_minus,
       main_3_seg_plus;
  wire [6:0] redutor_de_clock_1_saida_display_de_leds, redutor_de_clock_1_saida_display_de_leds_2,
       redutor_de_clock_1_saida_display_de_leds_3, redutor_de_clock_1_saida_display_de_leds_4,
       redutor_de_clock_1_saida_display_de_leds_5;
  wire [8:0] \coração_de_leds_1_matriz_1 , \coração_de_leds_1_matriz_2 , \coração_de_leds_1_matriz_3 ,
       \coração_de_leds_1_matriz_4 , \coração_de_leds_1_matriz_5 , \coração_de_leds_1_matriz_6 ,
       \coração_de_leds_1_matriz_7 , \coração_de_leds_1_matriz_8 , \coração_de_leds_1_matriz_9 ;
  wire [14:0] main_1_matriz_0, main_1_matriz_1, main_1_matriz_2, main_1_matriz_3, main_1_matriz_4,
       main_1_matriz_5, main_1_matriz_6, main_1_matriz_7, main_1_matriz_8, main_1_matriz_9, main_1_matriz_10,
       main_1_matriz_11, main_1_matriz_12, main_1_matriz_13, main_1_matriz_14;

  Button button_1 (.out(button_1_out));
  Button button_2 (.out(button_2_out));
  Clock clock_1 (.out(clock_1_out));
  Button button_3 (.out(button_3_out));
  Button button_4 (.out(button_4_out));
  Button button_5 (.out(button_5_out));
  DotMatrix #(.matrixcols(15), .matrixrows(15)) dotmatrix_1 (
    .col0(main_1_matriz_0), .col1(main_1_matriz_1), .col2(main_1_matriz_2), .col3(main_1_matriz_3),
    .col4(main_1_matriz_4), .col5(main_1_matriz_5), .col6(main_1_matriz_6), .col7(main_1_matriz_7),
    .col8(main_1_matriz_8), .col9(main_1_matriz_9), .col10(main_1_matriz_10), .col11(main_1_matriz_11),
    .col12(main_1_matriz_12), .col13(main_1_matriz_13), .col14(main_1_matriz_14));
  CI_joystick_main main_1 (
    .EIXO_x(joystick_1_y), .EIXO_Y(joystick_1_x), .Matriz_0(main_1_matriz_0), .Matriz_1(main_1_matriz_1),
    .Matriz_2(main_1_matriz_2), .Matriz_3(main_1_matriz_3), .Matriz_4(main_1_matriz_4),
    .Matriz_5(main_1_matriz_5), .Matriz_6(main_1_matriz_6), .Matriz_7(main_1_matriz_7),
    .Matriz_8(main_1_matriz_8), .Matriz_9(main_1_matriz_9), .Matriz_10(main_1_matriz_10),
    .Matriz_11(main_1_matriz_11), .Matriz_12(main_1_matriz_12), .Matriz_13(main_1_matriz_13),
    .Matriz_14(main_1_matriz_14));
  DotMatrix #(.matrixcols(9), .matrixrows(9)) dotmatrix_2 (
    .col0(\coração_de_leds_1_matriz_1 ), .col1(\coração_de_leds_1_matriz_2 ),
    .col2(\coração_de_leds_1_matriz_3 ), .col3(\coração_de_leds_1_matriz_4 ),
    .col4(\coração_de_leds_1_matriz_5 ), .col5(\coração_de_leds_1_matriz_6 ),
    .col6(\coração_de_leds_1_matriz_7 ), .col7(\coração_de_leds_1_matriz_8 ),
    .col8(\coração_de_leds_1_matriz_9 ));
  Joystick joystick_1 (.x(joystick_1_x), .y(joystick_1_y));
  Hex_Digit_Display hex_digit_display_1 (.value(\coração_de_leds_1_vel_plus ));  // open: dp
  Hex_Digit_Display hex_digit_display_2 (.value(\coração_de_leds_1_vel_minus ));  // open: dp
  \Coração_de_LEDs  \coração_de_leds_1  (
    .btn_2(button_1_out), .btn_4(button_2_out), .btn_8(button_3_out), .btn_16(button_4_out), .Ligar(in_1),
    .CLOCK_64Hz(clock_1_out), .LED_0(in_3), .LED_1(in_4), .LED_2(in_4), .LED_3(in_4), .LED_4(in_4),
    .LED_5(in_4), .LED_6(in_4), .LED_7(in_4), .LED_8(in_4), .LED_9(in_4), .LED_10(in_4),
    .LED_7_2(\coração_de_leds_1_led_7_2 ), .LED_11(in_4), .LED_6_2(\coração_de_leds_1_led_6_2 ),
    .LED_12(in_4), .LED_13(in_4), .LED_14(in_4), .LED_15(in_4), .LED_16(in_4), .LED_17(in_4),
    .btn_Atualizar(button_5_out), .Inverter(in_2), .LED_0_2(\coração_de_leds_1_led_0_2 ),
    .LED_1_2(\coração_de_leds_1_led_1_2 ), .VEL_plus(\coração_de_leds_1_vel_plus ),
    .VEL_minus(\coração_de_leds_1_vel_minus ), .Matriz_1(\coração_de_leds_1_matriz_1 ),
    .Matriz_2(\coração_de_leds_1_matriz_2 ), .Matriz_3(\coração_de_leds_1_matriz_3 ),
    .Matriz_4(\coração_de_leds_1_matriz_4 ), .Matriz_5(\coração_de_leds_1_matriz_5 ),
    .Matriz_6(\coração_de_leds_1_matriz_6 ), .Matriz_7(\coração_de_leds_1_matriz_7 ),
    .Matriz_8(\coração_de_leds_1_matriz_8 ), .Matriz_9(\coração_de_leds_1_matriz_9 ),
    .LED_2_2(\coração_de_leds_1_led_2_2 ), .LED_3_2(\coração_de_leds_1_led_3_2 ),
    .LED_4_2(\coração_de_leds_1_led_4_2 ), .LED_5_2(\coração_de_leds_1_led_5_2 ),
    .LED_15_2(\coração_de_leds_1_led_15_2 ), .LED_14_2(\coração_de_leds_1_led_14_2 ),
    .LED_16_2(\coração_de_leds_1_led_16_2 ), .LED_13_2(\coração_de_leds_1_led_13_2 ),
    .LED_17_2(\coração_de_leds_1_led_17_2 ), .LED_12_2(\coração_de_leds_1_led_12_2 ),
    .LED_11_2(\coração_de_leds_1_led_11_2 ), .LED_10_2(\coração_de_leds_1_led_10_2 ),
    .LED_9_2(\coração_de_leds_1_led_9_2 ), .LED_8_2(\coração_de_leds_1_led_8_2 ));
  LED led_1 (.in(main_2_out_19));
  LED led_2 (.in(main_2_out_22));
  LED led_3 (.in(main_2_out_21));
  LED led_4 (.in(main_2_out_26));
  LED led_5 (.in(main_2_out_28));
  LED led_6 (.in(main_2_out_30));
  LED led_7 (.in(main_2_out_32));
  LED led_8 (.in(main_2_out_34));
  LED led_9 (.in(main_2_out_20));
  LED led_10 (.in(main_2_out_23));
  LED led_11 (.in(main_2_out_25));
  LED led_12 (.in(main_2_out_33));
  LED led_13 (.in(main_2_out_35));
  LED led_14 (.in(main_2_out_36));
  Clock clock_2 (.out(clock_2_out));
  \CI_led_em_coração_main  main_2 (
    .out_20(main_2_out_20), .out_21(main_2_out_21), .out_22(main_2_out_22), .out_23(main_2_out_23),
    .out_24(main_2_out_24), .out_25(main_2_out_25), .out_26(main_2_out_26), .out_27(main_2_out_27),
    .out_28(main_2_out_28), .out_29(main_2_out_29), .out_30(main_2_out_30), .out_31(main_2_out_31),
    .out_32(main_2_out_32), .out_33(main_2_out_33), .out_34(main_2_out_34), .out_35(main_2_out_35),
    .out_36(main_2_out_36), ._0(\coração_de_leds_1_led_0_2 ), ._1(\coração_de_leds_1_led_1_2 ),
    ._2(\coração_de_leds_1_led_2_2 ), ._3(\coração_de_leds_1_led_3_2 ), ._4(\coração_de_leds_1_led_4_2 ),
    ._5(\coração_de_leds_1_led_5_2 ), ._6(\coração_de_leds_1_led_6_2 ), ._7(\coração_de_leds_1_led_7_2 ),
    ._8(\coração_de_leds_1_led_8_2 ), ._10(\coração_de_leds_1_led_10_2 ), ._11(\coração_de_leds_1_led_11_2 ),
    ._12(\coração_de_leds_1_led_12_2 ), ._13(\coração_de_leds_1_led_17_2 ),
    ._14(\coração_de_leds_1_led_14_2 ), ._15(\coração_de_leds_1_led_13_2 ),
    ._16(\coração_de_leds_1_led_15_2 ), ._17(\coração_de_leds_1_led_16_2 ), ._9(\coração_de_leds_1_led_9_2 ),
    .out_19(main_2_out_19));
  LED led_15 (.in(main_2_out_24));
  LED led_16 (.in(main_2_out_27));
  LED led_17 (.in(main_2_out_29));
  LED led_18 (.in(main_2_out_31));
  Contador_Assincrono_Crescente contador_assincrono_crescente_1 (
    .CLOCK(clock_2_out), .SAIDA_BCD(contador_assincrono_crescente_1_saida_bcd));
  Contador_Asssincrono_Decrescente contador_asssincrono_decrescente_1 (
    .CLOCK(clock_2_out), .SAIDA_BCD(contador_asssincrono_decrescente_1_saida_bcd));
  Contador_Sincrono_Impar contador_sincrono_impar_1 (
    .CLOCK(clock_2_out), .Saiuda_BCD(contador_sincrono_impar_1_saiuda_bcd));
  Contador_Sincrono_Par contador_sincrono_par_1 (.CLOCK(clock_2_out), .SAIDA_BCD(contador_sincrono_par_1_saida_bcd));
  Contador_Decimal contador_decimal_1 (
    .CLOCK(clock_2_out), .Reset(clock_2_out), .SAIDA_BCD(contador_decimal_1_saida_bcd));
  Contador_Hexadecimal contador_hexadecimal_1 (
    .CLOCK(clock_2_out), .Reset(clock_2_out), .SAIDA_BCD(contador_hexadecimal_1_saida_bcd));
  Contador_Qualquer contador_qualquer_1 (.CLOCK(clock_2_out), .SAIDA_BCD(contador_qualquer_1_saida_bcd));
  _7_Segment_Display u_7_segment_display_1 (
    .g(cod_display_7seg_adaptavel_1_g), .f(cod_display_7seg_adaptavel_1_f),
    .a(cod_display_7seg_adaptavel_1_a_2), .b(cod_display_7seg_adaptavel_1_b_2),
    .e(cod_display_7seg_adaptavel_1_e), .d(cod_display_7seg_adaptavel_1_d_2),
    .c(cod_display_7seg_adaptavel_1_c_2), .dp(cod_display_7seg_adaptavel_1_ponto_2));
  _7_Segment_Display u_7_segment_display_2 (
    .g(cod_display_7seg_adaptavel_2_g), .f(cod_display_7seg_adaptavel_2_f),
    .a(cod_display_7seg_adaptavel_2_a_2), .b(cod_display_7seg_adaptavel_2_b_2),
    .e(cod_display_7seg_adaptavel_2_e), .d(cod_display_7seg_adaptavel_2_d_2),
    .c(cod_display_7seg_adaptavel_2_c_2), .dp(cod_display_7seg_adaptavel_2_ponto_2));
  _7_Segment_Display u_7_segment_display_3 (
    .g(cod_display_7seg_adaptavel_3_g), .f(cod_display_7seg_adaptavel_3_f),
    .a(cod_display_7seg_adaptavel_3_a_2), .b(cod_display_7seg_adaptavel_3_b_2),
    .e(cod_display_7seg_adaptavel_3_e), .d(cod_display_7seg_adaptavel_3_d_2),
    .c(cod_display_7seg_adaptavel_3_c_2), .dp(cod_display_7seg_adaptavel_3_ponto_2));
  _7_Segment_Display u_7_segment_display_4 (
    .g(cod_display_7seg_adaptavel_4_g), .f(cod_display_7seg_adaptavel_4_f),
    .a(cod_display_7seg_adaptavel_4_a_2), .b(cod_display_7seg_adaptavel_4_b_2),
    .e(cod_display_7seg_adaptavel_4_e), .d(cod_display_7seg_adaptavel_4_d_2),
    .c(cod_display_7seg_adaptavel_4_c_2), .dp(cod_display_7seg_adaptavel_4_ponto_2));
  _7_Segment_Display u_7_segment_display_5 (
    .g(cod_display_7seg_adaptavel_5_g), .f(cod_display_7seg_adaptavel_5_f),
    .a(cod_display_7seg_adaptavel_5_a_2), .b(cod_display_7seg_adaptavel_5_b_2),
    .e(cod_display_7seg_adaptavel_5_e), .d(cod_display_7seg_adaptavel_5_d_2),
    .c(cod_display_7seg_adaptavel_5_c_2), .dp(cod_display_7seg_adaptavel_5_ponto_2));
  _7_Segment_Display u_7_segment_display_6 (
    .g(cod_display_7seg_adaptavel_6_g), .f(cod_display_7seg_adaptavel_6_f),
    .a(cod_display_7seg_adaptavel_6_a_2), .b(cod_display_7seg_adaptavel_6_b_2),
    .e(cod_display_7seg_adaptavel_6_e), .d(cod_display_7seg_adaptavel_6_d_2),
    .c(cod_display_7seg_adaptavel_6_c_2), .dp(cod_display_7seg_adaptavel_6_ponto_2));
  _7_Segment_Display u_7_segment_display_7 (
    .g(cod_display_7seg_adaptavel_7_g), .f(cod_display_7seg_adaptavel_7_f),
    .a(cod_display_7seg_adaptavel_7_a_2), .b(cod_display_7seg_adaptavel_7_b_2),
    .e(cod_display_7seg_adaptavel_7_e), .d(cod_display_7seg_adaptavel_7_d_2),
    .c(cod_display_7seg_adaptavel_7_c_2), .dp(cod_display_7seg_adaptavel_7_ponto_2));
  Cod__display_7SEG_adaptavel cod_display_7seg_adaptavel_1 (
    .C(contador_assincrono_crescente_1_saida_bcd[2]), .B(contador_assincrono_crescente_1_saida_bcd[1]),
    .A(contador_assincrono_crescente_1_saida_bcd[0]), .E(cod_display_7seg_adaptavel_1_e),
    .C_2(cod_display_7seg_adaptavel_1_c_2), .B_2(cod_display_7seg_adaptavel_1_b_2),
    .G(cod_display_7seg_adaptavel_1_g), .F(cod_display_7seg_adaptavel_1_f),
    .ponto_2(cod_display_7seg_adaptavel_1_ponto_2), .D(contador_assincrono_crescente_1_saida_bcd[3]),
    .D_2(cod_display_7seg_adaptavel_1_d_2), .A_2(cod_display_7seg_adaptavel_1_a_2));  // open: ponto
  Cod__display_7SEG_adaptavel cod_display_7seg_adaptavel_2 (
    .C(contador_asssincrono_decrescente_1_saida_bcd[2]), .B(contador_asssincrono_decrescente_1_saida_bcd[1]),
    .A(contador_asssincrono_decrescente_1_saida_bcd[0]), .E(cod_display_7seg_adaptavel_2_e),
    .C_2(cod_display_7seg_adaptavel_2_c_2), .B_2(cod_display_7seg_adaptavel_2_b_2),
    .G(cod_display_7seg_adaptavel_2_g), .F(cod_display_7seg_adaptavel_2_f),
    .ponto_2(cod_display_7seg_adaptavel_2_ponto_2), .D(contador_asssincrono_decrescente_1_saida_bcd[3]),
    .D_2(cod_display_7seg_adaptavel_2_d_2), .A_2(cod_display_7seg_adaptavel_2_a_2));  // open: ponto
  Cod__display_7SEG_adaptavel cod_display_7seg_adaptavel_3 (
    .C(contador_sincrono_impar_1_saiuda_bcd[2]), .B(contador_sincrono_impar_1_saiuda_bcd[1]),
    .A(contador_sincrono_impar_1_saiuda_bcd[0]), .E(cod_display_7seg_adaptavel_3_e),
    .C_2(cod_display_7seg_adaptavel_3_c_2), .B_2(cod_display_7seg_adaptavel_3_b_2),
    .G(cod_display_7seg_adaptavel_3_g), .F(cod_display_7seg_adaptavel_3_f),
    .ponto_2(cod_display_7seg_adaptavel_3_ponto_2), .D(contador_sincrono_impar_1_saiuda_bcd[3]),
    .D_2(cod_display_7seg_adaptavel_3_d_2), .A_2(cod_display_7seg_adaptavel_3_a_2));  // open: ponto
  Cod__display_7SEG_adaptavel cod_display_7seg_adaptavel_4 (
    .C(contador_sincrono_par_1_saida_bcd[2]), .B(contador_sincrono_par_1_saida_bcd[1]),
    .A(contador_sincrono_par_1_saida_bcd[0]), .E(cod_display_7seg_adaptavel_4_e),
    .C_2(cod_display_7seg_adaptavel_4_c_2), .B_2(cod_display_7seg_adaptavel_4_b_2),
    .G(cod_display_7seg_adaptavel_4_g), .F(cod_display_7seg_adaptavel_4_f),
    .ponto_2(cod_display_7seg_adaptavel_4_ponto_2), .D(contador_sincrono_par_1_saida_bcd[3]),
    .D_2(cod_display_7seg_adaptavel_4_d_2), .A_2(cod_display_7seg_adaptavel_4_a_2));  // open: ponto
  Cod__display_7SEG_adaptavel cod_display_7seg_adaptavel_5 (
    .C(contador_decimal_1_saida_bcd[2]), .B(contador_decimal_1_saida_bcd[1]),
    .A(contador_decimal_1_saida_bcd[0]), .E(cod_display_7seg_adaptavel_5_e),
    .C_2(cod_display_7seg_adaptavel_5_c_2), .B_2(cod_display_7seg_adaptavel_5_b_2),
    .G(cod_display_7seg_adaptavel_5_g), .F(cod_display_7seg_adaptavel_5_f),
    .ponto_2(cod_display_7seg_adaptavel_5_ponto_2), .D(contador_decimal_1_saida_bcd[3]),
    .D_2(cod_display_7seg_adaptavel_5_d_2), .A_2(cod_display_7seg_adaptavel_5_a_2));  // open: ponto
  Cod__display_7SEG_adaptavel cod_display_7seg_adaptavel_6 (
    .C(contador_hexadecimal_1_saida_bcd[2]), .B(contador_hexadecimal_1_saida_bcd[1]),
    .A(contador_hexadecimal_1_saida_bcd[0]), .E(cod_display_7seg_adaptavel_6_e),
    .C_2(cod_display_7seg_adaptavel_6_c_2), .B_2(cod_display_7seg_adaptavel_6_b_2),
    .G(cod_display_7seg_adaptavel_6_g), .F(cod_display_7seg_adaptavel_6_f),
    .ponto_2(cod_display_7seg_adaptavel_6_ponto_2), .D(contador_hexadecimal_1_saida_bcd[3]),
    .D_2(cod_display_7seg_adaptavel_6_d_2), .A_2(cod_display_7seg_adaptavel_6_a_2));  // open: ponto
  Cod__display_7SEG_adaptavel cod_display_7seg_adaptavel_7 (
    .C(contador_qualquer_1_saida_bcd[2]), .B(contador_qualquer_1_saida_bcd[1]),
    .A(contador_qualquer_1_saida_bcd[0]), .E(cod_display_7seg_adaptavel_7_e),
    .C_2(cod_display_7seg_adaptavel_7_c_2), .B_2(cod_display_7seg_adaptavel_7_b_2),
    .G(cod_display_7seg_adaptavel_7_g), .F(cod_display_7seg_adaptavel_7_f),
    .ponto_2(cod_display_7seg_adaptavel_7_ponto_2), .D(contador_qualquer_1_saida_bcd[3]),
    .D_2(cod_display_7seg_adaptavel_7_d_2), .A_2(cod_display_7seg_adaptavel_7_a_2));  // open: ponto
  DotMatrix dotmatrix_3 (
    .col0(redutor_de_clock_1_saida_display_de_leds), .col1(redutor_de_clock_1_saida_display_de_leds_2),
    .col2(redutor_de_clock_1_saida_display_de_leds_4), .col3(redutor_de_clock_1_saida_display_de_leds_3),
    .col4(redutor_de_clock_1_saida_display_de_leds_5));
  Clock clock_3 (.out(clock_3_out));
  Button button_6 (.out(button_6_out));
  Button button_7 (.out(button_7_out));
  Button button_8 (.out(button_8_out));
  Clock clock_4 (.out(clock_4_out));
  Redutor_de_Clock redutor_de_clock_1 (
    .CLOCK(clock_3_out), .Saida_display_de_leds(redutor_de_clock_1_saida_display_de_leds),
    .Saida_display_de_leds_2(redutor_de_clock_1_saida_display_de_leds_2),
    .Saida_display_de_leds_3(redutor_de_clock_1_saida_display_de_leds_3),
    .Saida_display_de_leds_4(redutor_de_clock_1_saida_display_de_leds_4),
    .Saida_display_de_leds_5(redutor_de_clock_1_saida_display_de_leds_5), .btn_atualizar(button_6_out));  // open: Saida_1, Saida_2, Saida_3, Saida_4, Saida_5, Saida_6, Saida_7
  Hex_Digit_Display hex_digit_display_3 (.value(main_3_hor_plus));  // open: dp
  Hex_Digit_Display hex_digit_display_4 (.value(main_3_hor_minus));  // open: dp
  CI_RELOGIO_main main_3 (
    .AJUSHOR(button_7_out), .AJUSMIN(button_8_out), .CLOCK(clock_4_out), .HOR_plus(main_3_hor_plus),
    .HOR_minus(main_3_hor_minus), .Min_plus(main_3_min_plus), .MIN_minus(main_3_min_minus),
    .SEG_plus(main_3_seg_plus), .Seg_minus(main_3_seg_minus));
  Hex_Digit_Display hex_digit_display_5 (.value(main_3_min_plus));  // open: dp
  Hex_Digit_Display hex_digit_display_6 (.value(main_3_min_minus));  // open: dp
  Hex_Digit_Display hex_digit_display_7 (.value(main_3_seg_plus));  // open: dp
  Hex_Digit_Display hex_digit_display_8 (.value(main_3_seg_minus));  // open: dp

  // Notes on the sheet:
  //   :
  //   :
endmodule

module prova (
  input  in_1,
  input  in_2,
  input  in_3,
  input  in_4,
  input  in_5,
  input  in_6,
  input  in_7,
  input  in_8
);

  wire button_1_out, button_2_out, button_3_out, button_4_out, button_5_out, button_6_out, button_7_out,
       clock_1_out, clock_2_out, cod_display_7seg_adaptavel_1_a_2, cod_display_7seg_adaptavel_1_b_2,
       cod_display_7seg_adaptavel_1_c_2, cod_display_7seg_adaptavel_1_d_2, cod_display_7seg_adaptavel_1_e,
       cod_display_7seg_adaptavel_1_f, cod_display_7seg_adaptavel_1_g, cod_display_7seg_adaptavel_1_ponto_2,
       \coração_de_leds_1_led_0_2 , \coração_de_leds_1_led_1_2 , \coração_de_leds_1_led_2_2 ,
       \coração_de_leds_1_led_3_2 , \coração_de_leds_1_led_4_2 , \coração_de_leds_1_led_5_2 ,
       \coração_de_leds_1_led_6_2 , \coração_de_leds_1_led_7_2 , \coração_de_leds_1_led_8_2 ,
       \coração_de_leds_1_led_9_2 , \coração_de_leds_1_led_10_2 , \coração_de_leds_1_led_11_2 ,
       \coração_de_leds_1_led_12_2 , \coração_de_leds_1_led_13_2 , \coração_de_leds_1_led_14_2 ,
       \coração_de_leds_1_led_15_2 , \coração_de_leds_1_led_16_2 , \coração_de_leds_1_led_17_2 ,
       main_1_out_19, main_1_out_20, main_1_out_21, main_1_out_22, main_1_out_23, main_1_out_24,
       main_1_out_25, main_1_out_26, main_1_out_27, main_1_out_28, main_1_out_29, main_1_out_30,
       main_1_out_31, main_1_out_32, main_1_out_33, main_1_out_34, main_1_out_35, main_1_out_36,
       redutor_de_clock_1_saida_1;
  wire [3:0] \coração_de_leds_1_vel_minus , \coração_de_leds_1_vel_plus , joystick_1_x, joystick_1_y,
       main_3_hor_minus, main_3_hor_plus, main_3_min_minus, main_3_min_plus, main_3_seg_minus,
       main_3_seg_plus;
  wire [6:0] redutor_de_clock_1_saida_display_de_leds, redutor_de_clock_1_saida_display_de_leds_2,
       redutor_de_clock_1_saida_display_de_leds_3, redutor_de_clock_1_saida_display_de_leds_4,
       redutor_de_clock_1_saida_display_de_leds_5;

  Clock clock_1 (.out(clock_1_out));
  Button button_1 (.out(button_1_out));
  Button button_2 (.out(button_2_out));
  Button button_3 (.out(button_3_out));
  Button button_4 (.out(button_4_out));
  Button button_5 (.out(button_5_out));
  Clock clock_2 (.out(clock_2_out));
  // Codificador_Display_7SEG codificador_display_7seg_1: pin names not known
  Hex_Digit_Display hex_digit_display_1 (.value(\coração_de_leds_1_vel_plus ));  // open: dp
  Hex_Digit_Display hex_digit_display_2 (.value(\coração_de_leds_1_vel_minus ));  // open: dp
  \Coração_de_LEDs  \coração_de_leds_1  (
    .btn_2(button_1_out), .btn_4(button_2_out), .btn_8(button_3_out), .btn_16(button_4_out), .Ligar(in_5),
    .CLOCK_64Hz(clock_1_out), .LED_0(in_7), .LED_1(in_8), .LED_2(in_8), .LED_3(in_8), .LED_4(in_8),
    .LED_5(in_8), .LED_6(in_8), .LED_7(in_8), .LED_8(in_8), .LED_9(in_8), .LED_10(in_8),
    .LED_7_2(\coração_de_leds_1_led_7_2 ), .LED_11(in_8), .LED_6_2(\coração_de_leds_1_led_6_2 ),
    .LED_12(in_8), .LED_13(in_8), .LED_14(in_8), .LED_15(in_8), .LED_16(in_8), .LED_17(in_8),
    .btn_Atualizar(button_5_out), .Inverter(in_6), .LED_0_2(\coração_de_leds_1_led_0_2 ),
    .LED_1_2(\coração_de_leds_1_led_1_2 ), .VEL_plus(\coração_de_leds_1_vel_plus ),
    .VEL_minus(\coração_de_leds_1_vel_minus ), .LED_2_2(\coração_de_leds_1_led_2_2 ),
    .LED_3_2(\coração_de_leds_1_led_3_2 ), .LED_4_2(\coração_de_leds_1_led_4_2 ),
    .LED_5_2(\coração_de_leds_1_led_5_2 ), .LED_15_2(\coração_de_leds_1_led_15_2 ),
    .LED_14_2(\coração_de_leds_1_led_14_2 ), .LED_16_2(\coração_de_leds_1_led_16_2 ),
    .LED_13_2(\coração_de_leds_1_led_13_2 ), .LED_17_2(\coração_de_leds_1_led_17_2 ),
    .LED_12_2(\coração_de_leds_1_led_12_2 ), .LED_11_2(\coração_de_leds_1_led_11_2 ),
    .LED_10_2(\coração_de_leds_1_led_10_2 ), .LED_9_2(\coração_de_leds_1_led_9_2 ),
    .LED_8_2(\coração_de_leds_1_led_8_2 ));  // open: Matriz_1, Matriz_2, Matriz_3, Matriz_4, Matriz_5, Matriz_6, Matriz_7, Matriz_8, Matriz_9
  LED led_1 (.in(main_1_out_21));
  LED led_2 (.in(main_1_out_26));
  LED led_3 (.in(main_1_out_28));
  LED led_4 (.in(main_1_out_30));
  LED led_5 (.in(main_1_out_32));
  _7_Segment_Display u_7_segment_display_1 (
    .g(cod_display_7seg_adaptavel_1_g), .f(cod_display_7seg_adaptavel_1_f),
    .a(cod_display_7seg_adaptavel_1_a_2), .b(cod_display_7seg_adaptavel_1_b_2),
    .e(cod_display_7seg_adaptavel_1_e), .d(cod_display_7seg_adaptavel_1_d_2),
    .c(cod_display_7seg_adaptavel_1_c_2), .dp(cod_display_7seg_adaptavel_1_ponto_2));
  LED led_6 (.in(main_1_out_19));
  LED led_7 (.in(main_1_out_22));
  LED led_8 (.in(main_1_out_23));
  LED led_9 (.in(main_1_out_25));
  LED led_10 (.in(main_1_out_35));
  LED led_11 (.in(main_1_out_34));
  LED led_12 (.in(main_1_out_36));
  Cod__display_7SEG_adaptavel cod_display_7seg_adaptavel_1 (
    .C(in_3), .B(in_2), .A(in_1), .E(cod_display_7seg_adaptavel_1_e), .C_2(cod_display_7seg_adaptavel_1_c_2),
    .B_2(cod_display_7seg_adaptavel_1_b_2), .G(cod_display_7seg_adaptavel_1_g),
    .F(cod_display_7seg_adaptavel_1_f), .ponto_2(cod_display_7seg_adaptavel_1_ponto_2), .D(in_4),
    .D_2(cod_display_7seg_adaptavel_1_d_2), .A_2(cod_display_7seg_adaptavel_1_a_2));  // open: ponto
  \CI_led_em_coração_main  main_1 (
    .out_20(main_1_out_20), .out_21(main_1_out_21), .out_22(main_1_out_22), .out_23(main_1_out_23),
    .out_24(main_1_out_24), .out_25(main_1_out_25), .out_26(main_1_out_26), .out_27(main_1_out_27),
    .out_28(main_1_out_28), .out_29(main_1_out_29), .out_30(main_1_out_30), .out_31(main_1_out_31),
    .out_32(main_1_out_32), .out_33(main_1_out_33), .out_34(main_1_out_34), .out_35(main_1_out_35),
    .out_36(main_1_out_36), ._0(\coração_de_leds_1_led_0_2 ), ._1(\coração_de_leds_1_led_1_2 ),
    ._2(\coração_de_leds_1_led_2_2 ), ._3(\coração_de_leds_1_led_3_2 ), ._4(\coração_de_leds_1_led_4_2 ),
    ._5(\coração_de_leds_1_led_5_2 ), ._6(\coração_de_leds_1_led_6_2 ), ._7(\coração_de_leds_1_led_7_2 ),
    ._8(\coração_de_leds_1_led_8_2 ), ._10(\coração_de_leds_1_led_10_2 ), ._11(\coração_de_leds_1_led_11_2 ),
    ._12(\coração_de_leds_1_led_12_2 ), ._13(\coração_de_leds_1_led_17_2 ),
    ._14(\coração_de_leds_1_led_14_2 ), ._15(\coração_de_leds_1_led_13_2 ),
    ._16(\coração_de_leds_1_led_15_2 ), ._17(\coração_de_leds_1_led_16_2 ), ._9(\coração_de_leds_1_led_9_2 ),
    .out_19(main_1_out_19));
  LED led_13 (.in(main_1_out_20));
  LED led_14 (.in(main_1_out_24));
  LED led_15 (.in(main_1_out_27));
  LED led_16 (.in(main_1_out_29));
  LED led_17 (.in(main_1_out_31));
  LED led_18 (.in(main_1_out_33));
  DotMatrix dotmatrix_1 (
    .col0(redutor_de_clock_1_saida_display_de_leds), .col1(redutor_de_clock_1_saida_display_de_leds_2),
    .col2(redutor_de_clock_1_saida_display_de_leds_4), .col3(redutor_de_clock_1_saida_display_de_leds_3),
    .col4(redutor_de_clock_1_saida_display_de_leds_5));
  Redutor_de_Clock redutor_de_clock_1 (
    .CLOCK(clock_1_out), .Saida_1(redutor_de_clock_1_saida_1),
    .Saida_display_de_leds(redutor_de_clock_1_saida_display_de_leds),
    .Saida_display_de_leds_2(redutor_de_clock_1_saida_display_de_leds_2),
    .Saida_display_de_leds_3(redutor_de_clock_1_saida_display_de_leds_3),
    .Saida_display_de_leds_4(redutor_de_clock_1_saida_display_de_leds_4),
    .Saida_display_de_leds_5(redutor_de_clock_1_saida_display_de_leds_5));  // open: Saida_2, Saida_3, Saida_4, Saida_5, Saida_6, Saida_7, btn_atualizar
  CI_joystick_main main_2 (
    .EIXO_x(joystick_1_y), .EIXO_Y(joystick_1_x));  // open: Matriz_0, Matriz_1, Matriz_2, Matriz_3, Matriz_4, Matriz_5, Matriz_6, Matriz_7, Matriz_8, Matriz_9, Matriz_10, Matriz_11, Matriz_12, Matriz_13, Matriz_14
  Joystick joystick_1 (.x(joystick_1_x), .y(joystick_1_y));
  Hex_Digit_Display hex_digit_display_3 (.value(main_3_hor_plus));  // open: dp
  Button button_6 (.out(button_6_out));
  CI_RELOGIO_main main_3 (
    .AJUSHOR(button_6_out), .AJUSMIN(button_7_out), .CLOCK(clock_1_out), .HOR_plus(main_3_hor_plus),
    .HOR_minus(main_3_hor_minus), .Min_plus(main_3_min_plus), .MIN_minus(main_3_min_minus),
    .SEG_plus(main_3_seg_plus), .Seg_minus(main_3_seg_minus));
  Button button_7 (.out(button_7_out));
  Hex_Digit_Display hex_digit_display_4 (.value(main_3_min_plus));  // open: dp
  Hex_Digit_Display hex_digit_display_5 (.value(main_3_hor_minus));  // open: dp
  Hex_Digit_Display hex_digit_display_6 (.value(main_3_seg_plus));  // open: dp
  Hex_Digit_Display hex_digit_display_7 (.value(main_3_min_minus));  // open: dp
  Hex_Digit_Display hex_digit_display_8 (.value(main_3_seg_minus));  // open: dp
endmodule
