// Logisim project contadores 2.circ as structural Verilog: 1 circuit, main circuit main
module main (
);

  wire and_1_out, and_2_out, and_3_out, and_4_out, and_5_out, and_6_out, and_7_out, and_8_out, and_9_out,
       and_10_out, and_11_out, and_12_out, and_13_out, and_14_out, and_15_out, and_16_out, and_17_out,
       and_18_out, and_19_out, and_20_out, and_21_out, and_22_out, clock_1_out, clock_2_out, clock_3_out,
       clock_4_out, clock_5_out, clock_6_out, clock_7_out, j_k_ff_1_qn, j_k_ff_8_qn, j_k_ff_10_qn,
       j_k_ff_13_qn, nor_1_out, nor_2_out, nor_3_out, nor_4_out, nor_5_out, nor_6_out, not_1_out, not_2_out,
       or_1_out, or_2_out, or_3_out, or_4_out, t_ff_2_qn, t_ff_3_qn, t_ff_6_qn, t_ff_7_qn, t_ff_10_qn,
       t_ff_11_qn, undriven, undriven_2, undriven_3, xor_1_out;
  wire [3:0] j_k_ff_5_q, j_k_ff_6_q, j_k_ff_12_q, t_ff_1_q, t_ff_2_q, t_ff_3_q, t_ff_9_q;

  Clock clock_1 (.out(clock_1_out));
  Clock clock_2 (.out(clock_2_out));
  Clock clock_3 (.out(clock_3_out));
  not not_1 (not_1_out, 1'b1);
  Clock clock_4 (.out(clock_4_out));
  not not_2 (not_2_out, 1'b0);
  J_K_Flip_Flop j_k_ff_1 (
    .J(and_1_out), .clk(clock_1_out), .K(1'b1), .Q(j_k_ff_6_q[3]), .Qn(j_k_ff_1_qn));  // open: preset, en, reset
  and and_1 (and_1_out, j_k_ff_6_q[1], j_k_ff_6_q[2]);
  T_Flip_Flop #(.trigger("falling")) t_ff_1 (
    .clk(clock_2_out), .T(1'b1), .Q(t_ff_1_q[0]), .reset(and_2_out));  // open: Qn, preset, en
  T_Flip_Flop t_ff_2 (.clk(clock_3_out), .T(1'b1), .Q(t_ff_2_q[0]), .Qn(t_ff_2_qn));  // open: preset, reset, en
  T_Flip_Flop t_ff_3 (.clk(clock_4_out), .T(1'b1), .Q(t_ff_3_q[0]), .Qn(t_ff_3_qn));  // open: preset, reset, en
  J_K_Flip_Flop j_k_ff_2 (
    .J(j_k_ff_6_q[1]), .clk(clock_1_out), .K(j_k_ff_6_q[1]), .Q(j_k_ff_6_q[2]));  // open: Qn, preset, en, reset
  T_Flip_Flop #(.trigger("falling")) t_ff_4 (
    .clk(t_ff_1_q[0]), .T(1'b1), .Q(t_ff_1_q[1]), .reset(and_2_out));  // open: Qn, preset, en
  and and_2 (and_2_out, t_ff_1_q[1], t_ff_1_q[3]);
  and and_3 (and_3_out, t_ff_2_q[0], 1'b1);
  nor nor_1 (nor_1_out, and_3_out, and_4_out);
  and and_4 (and_4_out, t_ff_2_qn, not_1_out);
  and and_5 (and_5_out, t_ff_3_q[0], 1'b0);
  nor nor_2 (nor_2_out, and_5_out, and_6_out);
  and and_6 (and_6_out, t_ff_3_qn, not_2_out);
  J_K_Flip_Flop j_k_ff_3 ();  // open: J, clk, K, Q, Qn, preset, en, reset
  or or_1 (or_1_out, j_k_ff_13_qn, j_k_ff_10_qn, undriven);
  Clock clock_5 (.out(clock_5_out));
  or or_2 (or_2_out, j_k_ff_13_qn, undriven_3, undriven);
  J_K_Flip_Flop j_k_ff_4 (
    .J(j_k_ff_1_qn), .clk(clock_1_out), .K(1'b1), .Q(j_k_ff_6_q[1]));  // open: Qn, preset, en, reset
  T_Flip_Flop #(.trigger("falling")) t_ff_5 (
    .clk(t_ff_1_q[1]), .T(1'b1), .Q(t_ff_1_q[2]), .reset(and_2_out));  // open: Qn, preset, en
  T_Flip_Flop t_ff_6 (.clk(nor_1_out), .T(1'b1), .Q(t_ff_2_q[1]), .Qn(t_ff_6_qn));  // open: preset, reset, en
  T_Flip_Flop t_ff_7 (.clk(nor_2_out), .T(1'b1), .Q(t_ff_3_q[1]), .Qn(t_ff_7_qn));  // open: preset, reset, en
  J_K_Flip_Flop #(.trigger("falling")) j_k_ff_5 (
    .J(or_1_out), .clk(clock_5_out), .K(or_2_out), .Q(j_k_ff_5_q[0]));  // open: Qn, preset, en, reset
  Hex_Digit_Display hex_digit_display_1 (.value(j_k_ff_6_q));  // open: dp
  J_K_Flip_Flop j_k_ff_6 (.J(1'b1), .clk(clock_1_out), .K(1'b0), .Q(j_k_ff_6_q[0]));  // open: Qn, preset, en, reset
  Hex_Digit_Display hex_digit_display_2 (.value(t_ff_1_q));  // open: dp
  T_Flip_Flop #(.trigger("falling")) t_ff_8 (
    .clk(t_ff_1_q[2]), .T(1'b1), .Q(t_ff_1_q[3]), .reset(and_2_out));  // open: Qn, preset, en
  and and_7 (and_7_out, t_ff_2_q[1], 1'b1);
  and and_8 (and_8_out, t_ff_6_qn, not_1_out);
  and and_9 (and_9_out, t_ff_3_q[1], 1'b0);
  and and_10 (and_10_out, t_ff_7_qn, not_2_out);
  or or_3 (or_3_out, and_12_out, and_11_out);
  and and_11 (and_11_out, j_k_ff_5_q[3], j_k_ff_10_qn);
  and and_12 (and_12_out, undriven_3, j_k_ff_5_q[0]);
  xor xor_1 (xor_1_out, and_13_out, undriven);
  Clock clock_6 (.out(clock_6_out));
  Clock clock_7 (.out(clock_7_out));
  nor nor_3 (nor_3_out, and_7_out, and_8_out);
  nor nor_4 (nor_4_out, and_9_out, and_10_out);
  J_K_Flip_Flop #(.trigger("falling")) j_k_ff_7 (
    .J(xor_1_out), .clk(clock_5_out), .K(or_3_out), .Q(j_k_ff_5_q[1]));  // open: Qn, preset, en, reset
  and and_13 (and_13_out, undriven_3, j_k_ff_5_q[3]);
  J_K_Flip_Flop j_k_ff_8 (
    .J(and_14_out), .clk(clock_6_out), .K(1'b1), .Q(j_k_ff_12_q[3]), .Qn(j_k_ff_8_qn));  // open: preset, en, reset
  and and_14 (and_14_out, j_k_ff_12_q[1], j_k_ff_12_q[2]);
  T_Flip_Flop #(.trigger("falling")) t_ff_9 (
    .clk(clock_7_out), .T(1'b1), .Q(t_ff_9_q[0]), .reset(undriven_2));  // open: Qn, preset, en
  T_Flip_Flop t_ff_10 (.clk(nor_3_out), .T(1'b1), .Q(t_ff_2_q[2]), .Qn(t_ff_10_qn));  // open: preset, reset, en
  T_Flip_Flop t_ff_11 (.clk(nor_4_out), .T(1'b1), .Q(t_ff_3_q[2]), .Qn(t_ff_11_qn));  // open: preset, reset, en
  and and_15 (and_15_out, j_k_ff_5_q[3], j_k_ff_5_q[1]);
  or or_4 (or_4_out, and_21_out, and_16_out);
  and and_16 (and_16_out, j_k_ff_5_q[3], j_k_ff_5_q[0]);
  J_K_Flip_Flop j_k_ff_9 (
    .J(j_k_ff_12_q[1]), .clk(clock_6_out), .K(j_k_ff_12_q[1]), .Q(j_k_ff_12_q[2]));  // open: Qn, preset, en, reset
  T_Flip_Flop #(.trigger("falling")) t_ff_12 (
    .clk(t_ff_9_q[0]), .T(1'b1), .Q(t_ff_9_q[1]), .reset(undriven_2));  // open: Qn, preset, en
  and and_17 (and_17_out, t_ff_2_q[2], 1'b1);
  nor nor_5 (nor_5_out, and_17_out, and_18_out);
  and and_18 (and_18_out, t_ff_10_qn, not_1_out);
  and and_19 (and_19_out, t_ff_3_q[2], 1'b0);
  nor nor_6 (nor_6_out, and_19_out, and_20_out);
  and and_20 (and_20_out, t_ff_11_qn, not_2_out);
  J_K_Flip_Flop #(.trigger("falling")) j_k_ff_10 (
    .J(and_15_out), .clk(clock_5_out), .K(or_4_out), .Q(j_k_ff_5_q[2]), .Qn(j_k_ff_10_qn));  // open: preset, en, reset
  J_K_Flip_Flop j_k_ff_11 (
    .J(j_k_ff_8_qn), .clk(clock_6_out), .K(1'b1), .Q(j_k_ff_12_q[1]));  // open: Qn, preset, en, reset
  T_Flip_Flop #(.trigger("falling")) t_ff_13 (
    .clk(t_ff_9_q[1]), .T(1'b1), .Q(t_ff_9_q[2]), .reset(undriven_2));  // open: Qn, preset, en
  Hex_Digit_Display hex_digit_display_3 (.value(t_ff_2_q));  // open: dp
  T_Flip_Flop t_ff_14 (.clk(nor_5_out), .T(1'b1), .Q(t_ff_2_q[3]));  // open: Qn, preset, reset, en
  Hex_Digit_Display hex_digit_display_4 (.value(t_ff_3_q));  // open: dp
  T_Flip_Flop t_ff_15 (.clk(nor_6_out), .T(1'b1), .Q(t_ff_3_q[3]));  // open: Qn, preset, reset, en
  and and_21 (and_21_out, j_k_ff_5_q[0], j_k_ff_13_qn);
  and and_22 (and_22_out, j_k_ff_5_q[2], j_k_ff_5_q[0]);
  Hex_Digit_Display hex_digit_display_5 (.value(j_k_ff_12_q));  // open: dp
  J_K_Flip_Flop j_k_ff_12 (.J(1'b0), .clk(clock_6_out), .K(1'b0), .Q(j_k_ff_12_q[0]));  // open: Qn, preset, en, reset
  Hex_Digit_Display hex_digit_display_6 (.value(t_ff_9_q));  // open: dp
  T_Flip_Flop #(.trigger("falling")) t_ff_16 (
    .clk(t_ff_9_q[2]), .T(1'b1), .Q(t_ff_9_q[3]), .reset(undriven_2));  // open: Qn, preset, en
  J_K_Flip_Flop #(.trigger("falling")) j_k_ff_13 (
    .J(and_21_out), .clk(clock_5_out), .K(and_22_out), .Q(j_k_ff_5_q[3]), .Qn(j_k_ff_13_qn));  // open: preset, en, reset
  Hex_Digit_Display hex_digit_display_7 (.value(j_k_ff_5_q));  // open: dp

  // Notes on the sheet:
  //   Contador Sincrono Impar
  //   Contador de Decimal
  //   Contador Assincrono Crescente
  //   Contador Assincrono Desrescente
  //   Contador Sincrono Par
  //   Contador Hexadecimal
endmodule
