// Logisim project contar.circ as structural Verilog: 1 circuit, main circuit main
module main (
);

  wire and_1_out, and_2_out, and_3_out, clock_1_out, controlled_buffer_1_out, controlled_buffer_2_out;
  wire [3:0] t_ff_1_q, t_ff_2_q, t_ff_3_q;

  Clock clock_1 (.out(clock_1_out));
  T_Flip_Flop #(.trigger("falling")) t_ff_1 (
    .clk(clock_1_out), .T(1'b1), .Q(t_ff_1_q[0]), .reset(controlled_buffer_1_out));  // open: Qn, preset, en
  T_Flip_Flop #(.trigger("falling")) t_ff_2 (
    .clk(and_1_out), .T(1'b1), .Q(t_ff_2_q[0]), .reset(controlled_buffer_2_out));  // open: Qn, preset, en
  T_Flip_Flop #(.trigger("falling")) t_ff_3 (
    .clk(and_2_out), .T(1'b1), .Q(t_ff_3_q[0]), .reset(and_3_out));  // open: Qn, preset, en
  T_Flip_Flop #(.trigger("falling")) t_ff_4 (
    .clk(t_ff_1_q[0]), .T(1'b1), .Q(t_ff_1_q[1]), .reset(controlled_buffer_1_out));  // open: Qn, preset, en
  T_Flip_Flop #(.trigger("falling")) t_ff_5 (
    .clk(t_ff_2_q[0]), .T(1'b1), .Q(t_ff_2_q[1]), .reset(controlled_buffer_2_out));  // open: Qn, preset, en
  T_Flip_Flop #(.trigger("falling")) t_ff_6 (
    .clk(t_ff_3_q[0]), .T(1'b1), .Q(t_ff_3_q[1]), .reset(and_3_out));  // open: Qn, preset, en
  T_Flip_Flop #(.trigger("falling")) t_ff_7 (
    .clk(t_ff_1_q[1]), .T(1'b1), .Q(t_ff_1_q[2]), .reset(controlled_buffer_1_out));  // open: Qn, preset, en
  T_Flip_Flop #(.trigger("falling")) t_ff_8 (
    .clk(t_ff_2_q[1]), .T(1'b1), .Q(t_ff_2_q[2]), .reset(controlled_buffer_2_out));  // open: Qn, preset, en
  T_Flip_Flop #(.trigger("falling")) t_ff_9 (
    .clk(t_ff_3_q[1]), .T(1'b1), .Q(t_ff_3_q[2]), .reset(and_3_out));  // open: Qn, preset, en
  T_Flip_Flop #(.trigger("falling")) t_ff_10 (
    .clk(t_ff_3_q[2]), .T(1'b1), .Q(t_ff_3_q[3]), .reset(and_3_out));  // open: Qn, preset, en
  T_Flip_Flop #(.trigger("falling")) t_ff_11 (
    .clk(t_ff_1_q[2]), .T(1'b1), .Q(t_ff_1_q[3]), .reset(controlled_buffer_1_out));  // open: Qn, preset, en
  T_Flip_Flop #(.trigger("falling")) t_ff_12 (
    .clk(t_ff_2_q[2]), .T(1'b1), .Q(t_ff_2_q[3]), .reset(controlled_buffer_2_out));  // open: Qn, preset, en
  and and_1 (and_1_out, ~t_ff_1_q[0], t_ff_1_q[1], ~t_ff_1_q[2], t_ff_1_q[3]);  // AND_Gate
  assign controlled_buffer_1_out = and_1_out ? and_1_out : 1'bz;  // Controlled_Buffer controlled_buffer_1
  and and_2 (and_2_out, ~t_ff_2_q[0], t_ff_2_q[1], ~t_ff_2_q[2], t_ff_2_q[3]);  // AND_Gate
  assign controlled_buffer_2_out = and_2_out ? and_2_out : 1'bz;  // Controlled_Buffer controlled_buffer_2
  and and_3 (and_3_out, ~t_ff_3_q[0], t_ff_3_q[1], ~t_ff_3_q[2], t_ff_3_q[3]);  // AND_Gate
  Hex_Digit_Display hex_digit_display_1 (.value(t_ff_3_q));  // open: dp
  Hex_Digit_Display hex_digit_display_2 (.value(t_ff_2_q));  // open: dp
  Hex_Digit_Display hex_digit_display_3 (.value(t_ff_1_q));  // open: dp
endmodule
