// Logisim project ise.circ as structural Verilog: 1 circuit, main circuit main
module main (
);

  wire [6:0] undriven, undriven_2, undriven_3, undriven_4, undriven_5, undriven_6, undriven_7, undriven_8,
       undriven_9, undriven_10, undriven_11, undriven_12, undriven_13, undriven_14, undriven_15, undriven_16,
       undriven_17, undriven_18, undriven_19, undriven_20, undriven_21, undriven_22, undriven_23,
       undriven_24, undriven_25, undriven_26, undriven_27, undriven_28, undriven_29, undriven_30,
       undriven_31, undriven_32, undriven_33, undriven_34, undriven_35, undriven_36, undriven_37,
       undriven_38, undriven_39, undriven_40, undriven_41, undriven_42, undriven_43, undriven_44,
       undriven_45, undriven_46, undriven_47, undriven_48, undriven_49, undriven_50, undriven_51,
       undriven_52, undriven_53, undriven_54, undriven_55;

  DotMatrix dotmatrix_1 (.col0({7{1'b0}}), .col1(7'b0100010), .col2(7'b0111110), .col3(7'b0100010), .col4({7{1'b0}}));
  DotMatrix dotmatrix_2 (.col0({7{1'b0}}), .col1(7'b0111010), .col2(7'b0101010), .col3(7'b0101110), .col4({7{1'b0}}));
  DotMatrix dotmatrix_3 (.col0({7{1'b0}}), .col1(7'b0111110), .col2(7'b0101010), .col3(7'b0100010), .col4({7{1'b0}}));
  DotMatrix dotmatrix_4 (
    .col0(undriven), .col1({undriven_2[6], {5{1'b1}}, undriven_2[0]}),
    .col2({undriven_3[6:4], 1'b1, undriven_3[2:0]}),
    .col3({undriven_5[6], 2'b11, undriven_5[3], 2'b11, undriven_5[0]}), .col4(undriven_7));
  DotMatrix dotmatrix_5 (
    .col0(undriven_4), .col1(undriven_6), .col2(undriven_8), .col3(undriven_9), .col4(undriven_10));
  DotMatrix dotmatrix_6 (.col0({7{1'b0}}), .col1(7'b0111110), .col2(7'b0101000), .col3(7'b0111110), .col4({7{1'b0}}));
  DotMatrix dotmatrix_7 (
    .col0(undriven_11), .col1({undriven_12[6], {5{1'b1}}, undriven_12[0]}),
    .col2({undriven_13[6:4], 1'b1, undriven_13[2:0]}), .col3({undriven_14[6], {5{1'b1}}, undriven_14[0]}),
    .col4(undriven_16));
  DotMatrix dotmatrix_8 (
    .col0(undriven_15), .col1({undriven_17[6], {5{1'b1}}, undriven_17[0]}),
    .col2({undriven_18[6:2], 1'b1, undriven_18[0]}), .col3({undriven_19[6:2], 1'b1, undriven_19[0]}),
    .col4(undriven_20));
  DotMatrix dotmatrix_9 (
    .col0(undriven_22), .col1({undriven_24[6], {5{1'b1}}, undriven_24[0]}),
    .col2({undriven_26[6], 1'b1, undriven_26[4], 1'b1, undriven_26[2], 1'b1, undriven_26[0]}),
    .col3({undriven_28[6:5], 1'b1, undriven_28[3], 1'b1, undriven_28[1:0]}), .col4(undriven_30));
  DotMatrix dotmatrix_10 (
    .col0(undriven_21), .col1({undriven_23[6], {5{1'b1}}, undriven_23[0]}),
    .col2({undriven_25[6], 1'b1, undriven_25[4:2], 1'b1, undriven_25[0]}),
    .col3({undriven_27[6:5], 3'b111, undriven_27[1:0]}), .col4(undriven_29));
  DotMatrix dotmatrix_11 (
    .col0(undriven_31), .col1({undriven_32[6], 4'b1111, undriven_32[1:0]}),
    .col2({undriven_33[6:2], 1'b1, undriven_33[0]}), .col3({undriven_34[6:3], 1'b1, undriven_34[1:0]}),
    .col4(undriven_35));
  DotMatrix dotmatrix_12 (
    .col0(undriven_36), .col1({undriven_37[6], {5{1'b1}}, undriven_37[0]}),
    .col2({undriven_39[6], 1'b1, undriven_39[4], 1'b1, undriven_39[2:0]}),
    .col3({undriven_41[6], 1'b1, undriven_41[4:0]}), .col4(undriven_43));
  DotMatrix dotmatrix_13 (
    .col0(undriven_44), .col1({undriven_46[6], {5{1'b1}}, undriven_46[0]}),
    .col2({undriven_48[6], 1'b1, undriven_48[4:2], 1'b1, undriven_48[0]}),
    .col3({undriven_50[6], 1'b1, undriven_50[4:2], 1'b1, undriven_50[0]}), .col4(undriven_52));
  DotMatrix dotmatrix_14 (
    .col0(undriven_49), .col1({undriven_51[6], {5{1'b1}}, undriven_51[0]}),
    .col2({undriven_53[6], 1'b1, undriven_53[4:2], 1'b1, undriven_53[0]}),
    .col3({undriven_54[6], 1'b1, undriven_54[4:3], 2'b11, undriven_54[0]}), .col4(undriven_55));
  DotMatrix dotmatrix_15 (
    .col0(undriven_38), .col1({undriven_40[6], {5{1'b1}}, undriven_40[0]}),
    .col2({undriven_42[6:5], 1'b1, undriven_42[3:0]}), .col3({undriven_45[6], {5{1'b1}}, undriven_45[0]}),
    .col4(undriven_47));
endmodule
