// Logisim project atoa.circ as structural Verilog: 1 circuit, main circuit main
module main (
);

  wire button_1_out, button_2_out, button_3_out, button_4_out, button_5_out, button_6_out, button_7_out,
       button_8_out, clock_1_out, clock_2_out, clock_3_out, clock_4_out, clock_5_out, clock_6_out,
       clock_7_out, clock_8_out, random_1_out, random_2_out, random_3_out, random_4_out, random_5_out,
       random_6_out, random_7_out, random_8_out, random_9_out, random_10_out, random_11_out, random_12_out,
       random_13_out, random_14_out, random_15_out, random_16_out, random_17_out, random_18_out,
       random_19_out, random_20_out, random_21_out, random_22_out, random_23_out, random_24_out,
       random_25_out, random_26_out, random_27_out, random_28_out, random_29_out, random_30_out,
       random_31_out, random_32_out, random_33_out, random_34_out, random_35_out, random_36_out,
       random_37_out, random_38_out, random_39_out, random_40_out, random_41_out, random_42_out,
       random_43_out, random_44_out, random_45_out, random_46_out, random_47_out, random_48_out,
       random_49_out, random_50_out, random_51_out, random_52_out, random_53_out, random_54_out,
       random_55_out, random_56_out, random_57_out, random_58_out, random_59_out, random_60_out,
       random_61_out, random_62_out, random_63_out, random_64_out;
  wire [7:0] t_ff_29_q, t_ff_30_q, t_ff_31_q, t_ff_32_q, t_ff_61_q, t_ff_62_q, t_ff_63_q, t_ff_64_q;

  Clock clock_1 (.out(clock_1_out));
  Random #(.width(1)) random_1 (.clk(clock_1_out), .out(random_1_out));  // open: next, clr
  Clock clock_2 (.out(clock_2_out));
  Random #(.width(1)) random_2 (.clk(clock_2_out), .out(random_2_out));  // open: next, clr
  Button button_1 (.out(button_1_out));
  Clock clock_3 (.out(clock_3_out));
  Random #(.width(1)) random_3 (.clk(clock_3_out), .out(random_3_out));  // open: next, clr
  Button button_2 (.out(button_2_out));
  Clock clock_4 (.out(clock_4_out));
  Random #(.width(1)) random_4 (.clk(clock_4_out), .out(random_4_out));  // open: next, clr
  T_Flip_Flop t_ff_1 (
    .clk(clock_1_out), .T(random_1_out), .Q(t_ff_29_q[7]), .reset(button_3_out));  // open: Qn, preset, en
  Random #(.width(1)) random_5 (.clk(clock_1_out), .out(random_5_out));  // open: next, clr
  Button button_3 (.out(button_3_out));
  T_Flip_Flop t_ff_2 (
    .clk(clock_2_out), .T(random_2_out), .Q(t_ff_30_q[7]), .reset(button_1_out));  // open: Qn, preset, en
  Random #(.width(1)) random_6 (.clk(clock_2_out), .out(random_6_out));  // open: next, clr
  T_Flip_Flop t_ff_3 (
    .clk(clock_3_out), .T(random_3_out), .Q(t_ff_31_q[7]), .reset(button_2_out));  // open: Qn, preset, en
  Random #(.width(1)) random_7 (.clk(clock_3_out), .out(random_7_out));  // open: next, clr
  T_Flip_Flop t_ff_4 (
    .clk(clock_4_out), .T(random_4_out), .Q(t_ff_32_q[7]), .reset(button_4_out));  // open: Qn, preset, en
  Random #(.width(1)) random_8 (.clk(clock_4_out), .out(random_8_out));  // open: next, clr
  Button button_4 (.out(button_4_out));
  T_Flip_Flop t_ff_5 (
    .clk(clock_1_out), .T(random_5_out), .Q(t_ff_29_q[6]), .reset(button_3_out));  // open: Qn, preset, en
  Random #(.width(1)) random_9 (.clk(clock_1_out), .out(random_9_out));  // open: next, clr
  T_Flip_Flop t_ff_6 (
    .clk(clock_2_out), .T(random_6_out), .Q(t_ff_30_q[6]), .reset(button_1_out));  // open: Qn, preset, en
  Random #(.width(1)) random_10 (.clk(clock_2_out), .out(random_10_out));  // open: next, clr
  T_Flip_Flop t_ff_7 (
    .clk(clock_3_out), .T(random_7_out), .Q(t_ff_31_q[6]), .reset(button_2_out));  // open: Qn, preset, en
  Random #(.width(1)) random_11 (.clk(clock_3_out), .out(random_11_out));  // open: next, clr
  T_Flip_Flop t_ff_8 (
    .clk(clock_4_out), .T(random_8_out), .Q(t_ff_32_q[6]), .reset(button_4_out));  // open: Qn, preset, en
  Random #(.width(1)) random_12 (.clk(clock_4_out), .out(random_12_out));  // open: next, clr
  T_Flip_Flop t_ff_9 (
    .clk(clock_1_out), .T(random_9_out), .Q(t_ff_29_q[5]), .reset(button_3_out));  // open: Qn, preset, en
  Random #(.width(1)) random_13 (.clk(clock_1_out), .out(random_13_out));  // open: next, clr
  T_Flip_Flop t_ff_10 (
    .clk(clock_2_out), .T(random_10_out), .Q(t_ff_30_q[5]), .reset(button_1_out));  // open: Qn, preset, en
  Random #(.width(1)) random_14 (.clk(clock_2_out), .out(random_14_out));  // open: next, clr
  T_Flip_Flop t_ff_11 (
    .clk(clock_3_out), .T(random_11_out), .Q(t_ff_31_q[5]), .reset(button_2_out));  // open: Qn, preset, en
  Random #(.width(1)) random_15 (.clk(clock_3_out), .out(random_15_out));  // open: next, clr
  T_Flip_Flop t_ff_12 (
    .clk(clock_4_out), .T(random_12_out), .Q(t_ff_32_q[5]), .reset(button_4_out));  // open: Qn, preset, en
  T_Flip_Flop t_ff_13 (
    .clk(clock_1_out), .T(random_13_out), .Q(t_ff_29_q[4]), .reset(button_3_out));  // open: Qn, preset, en
  T_Flip_Flop t_ff_14 (
    .clk(clock_2_out), .T(random_14_out), .Q(t_ff_30_q[4]), .reset(button_1_out));  // open: Qn, preset, en
  Random #(.width(1)) random_16 (.clk(clock_2_out), .out(random_16_out));  // open: next, clr
  T_Flip_Flop t_ff_15 (
    .clk(clock_3_out), .T(random_15_out), .Q(t_ff_31_q[4]), .reset(button_2_out));  // open: Qn, preset, en
  Random #(.width(1)) random_17 (.clk(clock_3_out), .out(random_17_out));  // open: next, clr
  T_Flip_Flop t_ff_16 (
    .clk(clock_4_out), .T(random_18_out), .Q(t_ff_32_q[4]), .reset(button_4_out));  // open: Qn, preset, en
  Random #(.width(1)) random_18 (.clk(clock_4_out), .out(random_18_out));  // open: next, clr
  T_Flip_Flop t_ff_17 (
    .clk(clock_1_out), .T(random_19_out), .Q(t_ff_29_q[3]), .reset(button_3_out));  // open: Qn, preset, en
  Random #(.width(1)) random_19 (.clk(clock_1_out), .out(random_19_out));  // open: next, clr
  T_Flip_Flop t_ff_18 (
    .clk(clock_2_out), .T(random_16_out), .Q(t_ff_30_q[3]), .reset(button_1_out));  // open: Qn, preset, en
  T_Flip_Flop t_ff_19 (
    .clk(clock_3_out), .T(random_17_out), .Q(t_ff_31_q[3]), .reset(button_2_out));  // open: Qn, preset, en
  T_Flip_Flop t_ff_20 (
    .clk(clock_4_out), .T(random_20_out), .Q(t_ff_32_q[3]), .reset(button_4_out));  // open: Qn, preset, en
  Random #(.width(1)) random_20 (.clk(clock_4_out), .out(random_20_out));  // open: next, clr
  DotMatrix #(.matrixcols(8), .matrixrows(8)) dotmatrix_1 (
    .col0(t_ff_29_q), .col1(t_ff_30_q), .col2(t_ff_31_q), .col3(t_ff_32_q), .col4(t_ff_61_q),
    .col5(t_ff_62_q), .col6(t_ff_63_q), .col7(t_ff_64_q));
  T_Flip_Flop t_ff_21 (
    .clk(clock_1_out), .T(random_21_out), .Q(t_ff_29_q[2]), .reset(button_3_out));  // open: Qn, preset, en
  Random #(.width(1)) random_21 (.clk(clock_1_out), .out(random_21_out));  // open: next, clr
  T_Flip_Flop t_ff_22 (
    .clk(clock_2_out), .T(random_22_out), .Q(t_ff_30_q[2]), .reset(button_1_out));  // open: Qn, preset, en
  Random #(.width(1)) random_22 (.clk(clock_2_out), .out(random_22_out));  // open: next, clr
  T_Flip_Flop t_ff_23 (
    .clk(clock_3_out), .T(random_23_out), .Q(t_ff_31_q[2]), .reset(button_2_out));  // open: Qn, preset, en
  Random #(.width(1)) random_23 (.clk(clock_3_out), .out(random_23_out));  // open: next, clr
  T_Flip_Flop t_ff_24 (
    .clk(clock_4_out), .T(random_24_out), .Q(t_ff_32_q[2]), .reset(button_4_out));  // open: Qn, preset, en
  Random #(.width(1)) random_24 (.clk(clock_4_out), .out(random_24_out));  // open: next, clr
  T_Flip_Flop t_ff_25 (
    .clk(clock_1_out), .T(random_25_out), .Q(t_ff_29_q[1]), .reset(button_3_out));  // open: Qn, preset, en
  Random #(.width(1)) random_25 (.clk(clock_1_out), .out(random_25_out));  // open: next, clr
  T_Flip_Flop t_ff_26 (
    .clk(clock_2_out), .T(random_26_out), .Q(t_ff_30_q[1]), .reset(button_1_out));  // open: Qn, preset, en
  Random #(.width(1)) random_26 (.clk(clock_2_out), .out(random_26_out));  // open: next, clr
  T_Flip_Flop t_ff_27 (
    .clk(clock_3_out), .T(random_27_out), .Q(t_ff_31_q[1]), .reset(button_2_out));  // open: Qn, preset, en
  Random #(.width(1)) random_27 (.clk(clock_3_out), .out(random_27_out));  // open: next, clr
  T_Flip_Flop t_ff_28 (
    .clk(clock_4_out), .T(random_28_out), .Q(t_ff_32_q[1]), .reset(button_4_out));  // open: Qn, preset, en
  Random #(.width(1)) random_28 (.clk(clock_4_out), .out(random_28_out));  // open: next, clr
  T_Flip_Flop t_ff_29 (
    .clk(clock_1_out), .T(random_29_out), .Q(t_ff_29_q[0]), .reset(button_3_out));  // open: Qn, preset, en
  Random #(.width(1)) random_29 (.clk(clock_1_out), .out(random_29_out));  // open: next, clr
  T_Flip_Flop t_ff_30 (
    .clk(clock_2_out), .T(random_30_out), .Q(t_ff_30_q[0]), .reset(button_1_out));  // open: Qn, preset, en
  Random #(.width(1)) random_30 (.clk(clock_2_out), .out(random_30_out));  // open: next, clr
  T_Flip_Flop t_ff_31 (
    .clk(clock_3_out), .T(random_31_out), .Q(t_ff_31_q[0]), .reset(button_2_out));  // open: Qn, preset, en
  Random #(.width(1)) random_31 (.clk(clock_3_out), .out(random_31_out));  // open: next, clr
  Random #(.width(1)) random_32 (.clk(clock_4_out), .out(random_32_out));  // open: next, clr
  Clock clock_5 (.out(clock_5_out));
  Clock clock_6 (.out(clock_6_out));
  T_Flip_Flop t_ff_32 (
    .clk(clock_4_out), .T(random_32_out), .Q(t_ff_32_q[0]), .reset(button_4_out));  // open: Qn, preset, en
  Clock clock_7 (.out(clock_7_out));
  Random #(.width(1)) random_33 (.clk(clock_7_out), .out(random_33_out));  // open: next, clr
  Button button_5 (.out(button_5_out));
  Random #(.width(1)) random_34 (.clk(clock_5_out), .out(random_34_out));  // open: next, clr
  Button button_6 (.out(button_6_out));
  Random #(.width(1)) random_35 (.clk(clock_6_out), .out(random_35_out));  // open: next, clr
  Button button_7 (.out(button_7_out));
  Clock clock_8 (.out(clock_8_out));
  Random #(.width(1)) random_36 (.clk(clock_8_out), .out(random_36_out));  // open: next, clr
  T_Flip_Flop t_ff_33 (
    .clk(clock_7_out), .T(random_33_out), .Q(t_ff_61_q[7]), .reset(button_5_out));  // open: Qn, preset, en
  Random #(.width(1)) random_37 (.clk(clock_7_out), .out(random_37_out));  // open: next, clr
  T_Flip_Flop t_ff_34 (
    .clk(clock_5_out), .T(random_34_out), .Q(t_ff_62_q[7]), .reset(button_6_out));  // open: Qn, preset, en
  Random #(.width(1)) random_38 (.clk(clock_5_out), .out(random_38_out));  // open: next, clr
  T_Flip_Flop t_ff_35 (
    .clk(clock_6_out), .T(random_35_out), .Q(t_ff_63_q[7]), .reset(button_7_out));  // open: Qn, preset, en
  Random #(.width(1)) random_39 (.clk(clock_6_out), .out(random_39_out));  // open: next, clr
  T_Flip_Flop t_ff_36 (
    .clk(clock_8_out), .T(random_36_out), .Q(t_ff_64_q[7]), .reset(button_8_out));  // open: Qn, preset, en
  Random #(.width(1)) random_40 (.clk(clock_8_out), .out(random_40_out));  // open: next, clr
  Button button_8 (.out(button_8_out));
  T_Flip_Flop t_ff_37 (
    .clk(clock_7_out), .T(random_37_out), .Q(t_ff_61_q[6]), .reset(button_5_out));  // open: Qn, preset, en
  Random #(.width(1)) random_41 (.clk(clock_7_out), .out(random_41_out));  // open: next, clr
  T_Flip_Flop t_ff_38 (
    .clk(clock_5_out), .T(random_38_out), .Q(t_ff_62_q[6]), .reset(button_6_out));  // open: Qn, preset, en
  Random #(.width(1)) random_42 (.clk(clock_5_out), .out(random_42_out));  // open: next, clr
  T_Flip_Flop t_ff_39 (
    .clk(clock_6_out), .T(random_39_out), .Q(t_ff_63_q[6]), .reset(button_7_out));  // open: Qn, preset, en
  Random #(.width(1)) random_43 (.clk(clock_6_out), .out(random_43_out));  // open: next, clr
  T_Flip_Flop t_ff_40 (
    .clk(clock_8_out), .T(random_40_out), .Q(t_ff_64_q[6]), .reset(button_8_out));  // open: Qn, preset, en
  Random #(.width(1)) random_44 (.clk(clock_8_out), .out(random_44_out));  // open: next, clr
  T_Flip_Flop t_ff_41 (
    .clk(clock_7_out), .T(random_41_out), .Q(t_ff_61_q[5]), .reset(button_5_out));  // open: Qn, preset, en
  Random #(.width(1)) random_45 (.clk(clock_7_out), .out(random_45_out));  // open: next, clr
  T_Flip_Flop t_ff_42 (
    .clk(clock_5_out), .T(random_42_out), .Q(t_ff_62_q[5]), .reset(button_6_out));  // open: Qn, preset, en
  Random #(.width(1)) random_46 (.clk(clock_5_out), .out(random_46_out));  // open: next, clr
  T_Flip_Flop t_ff_43 (
    .clk(clock_6_out), .T(random_43_out), .Q(t_ff_63_q[5]), .reset(button_7_out));  // open: Qn, preset, en
  Random #(.width(1)) random_47 (.clk(clock_6_out), .out(random_47_out));  // open: next, clr
  T_Flip_Flop t_ff_44 (
    .clk(clock_8_out), .T(random_44_out), .Q(t_ff_64_q[5]), .reset(button_8_out));  // open: Qn, preset, en
  Random #(.width(1)) random_48 (.clk(clock_8_out), .out(random_48_out));  // open: next, clr
  T_Flip_Flop t_ff_45 (
    .clk(clock_7_out), .T(random_45_out), .Q(t_ff_61_q[4]), .reset(button_5_out));  // open: Qn, preset, en
  Random #(.width(1)) random_49 (.clk(clock_7_out), .out(random_49_out));  // open: next, clr
  T_Flip_Flop t_ff_46 (
    .clk(clock_5_out), .T(random_46_out), .Q(t_ff_62_q[4]), .reset(button_6_out));  // open: Qn, preset, en
  Random #(.width(1)) random_50 (.clk(clock_5_out), .out(random_50_out));  // open: next, clr
  T_Flip_Flop t_ff_47 (
    .clk(clock_6_out), .T(random_47_out), .Q(t_ff_63_q[4]), .reset(button_7_out));  // open: Qn, preset, en
  Random #(.width(1)) random_51 (.clk(clock_6_out), .out(random_51_out));  // open: next, clr
  T_Flip_Flop t_ff_48 (
    .clk(clock_8_out), .T(random_48_out), .Q(t_ff_64_q[4]), .reset(button_8_out));  // open: Qn, preset, en
  T_Flip_Flop t_ff_49 (
    .clk(clock_7_out), .T(random_49_out), .Q(t_ff_61_q[3]), .reset(button_5_out));  // open: Qn, preset, en
  T_Flip_Flop t_ff_50 (
    .clk(clock_5_out), .T(random_50_out), .Q(t_ff_62_q[3]), .reset(button_6_out));  // open: Qn, preset, en
  Random #(.width(1)) random_52 (.clk(clock_5_out), .out(random_52_out));  // open: next, clr
  T_Flip_Flop t_ff_51 (
    .clk(clock_6_out), .T(random_51_out), .Q(t_ff_63_q[3]), .reset(button_7_out));  // open: Qn, preset, en
  Random #(.width(1)) random_53 (.clk(clock_6_out), .out(random_53_out));  // open: next, clr
  T_Flip_Flop t_ff_52 (
    .clk(clock_8_out), .T(random_54_out), .Q(t_ff_64_q[3]), .reset(button_8_out));  // open: Qn, preset, en
  Random #(.width(1)) random_54 (.clk(clock_8_out), .out(random_54_out));  // open: next, clr
  T_Flip_Flop t_ff_53 (
    .clk(clock_7_out), .T(random_55_out), .Q(t_ff_61_q[2]), .reset(button_5_out));  // open: Qn, preset, en
  Random #(.width(1)) random_55 (.clk(clock_7_out), .out(random_55_out));  // open: next, clr
  T_Flip_Flop t_ff_54 (
    .clk(clock_5_out), .T(random_52_out), .Q(t_ff_62_q[2]), .reset(button_6_out));  // open: Qn, preset, en
  Random #(.width(1)) random_56 (.clk(clock_5_out), .out(random_56_out));  // open: next, clr
  T_Flip_Flop t_ff_55 (
    .clk(clock_6_out), .T(random_53_out), .Q(t_ff_63_q[2]), .reset(button_7_out));  // open: Qn, preset, en
  Random #(.width(1)) random_57 (.clk(clock_6_out), .out(random_57_out));  // open: next, clr
  T_Flip_Flop t_ff_56 (
    .clk(clock_8_out), .T(random_58_out), .Q(t_ff_64_q[2]), .reset(button_8_out));  // open: Qn, preset, en
  Random #(.width(1)) random_58 (.clk(clock_8_out), .out(random_58_out));  // open: next, clr
  T_Flip_Flop t_ff_57 (
    .clk(clock_7_out), .T(random_59_out), .Q(t_ff_61_q[1]), .reset(button_5_out));  // open: Qn, preset, en
  Random #(.width(1)) random_59 (.clk(clock_7_out), .out(random_59_out));  // open: next, clr
  T_Flip_Flop t_ff_58 (
    .clk(clock_5_out), .T(random_56_out), .Q(t_ff_62_q[1]), .reset(button_6_out));  // open: Qn, preset, en
  Random #(.width(1)) random_60 (.clk(clock_5_out), .out(random_60_out));  // open: next, clr
  T_Flip_Flop t_ff_59 (
    .clk(clock_6_out), .T(random_57_out), .Q(t_ff_63_q[1]), .reset(button_7_out));  // open: Qn, preset, en
  Random #(.width(1)) random_61 (.clk(clock_6_out), .out(random_61_out));  // open: next, clr
  T_Flip_Flop t_ff_60 (
    .clk(clock_8_out), .T(random_62_out), .Q(t_ff_64_q[1]), .reset(button_8_out));  // open: Qn, preset, en
  Random #(.width(1)) random_62 (.clk(clock_8_out), .out(random_62_out));  // open: next, clr
  T_Flip_Flop t_ff_61 (
    .clk(clock_7_out), .T(random_63_out), .Q(t_ff_61_q[0]), .reset(button_5_out));  // open: Qn, preset, en
  Random #(.width(1)) random_63 (.clk(clock_7_out), .out(random_63_out));  // open: next, clr
  T_Flip_Flop t_ff_62 (
    .clk(clock_5_out), .T(random_60_out), .Q(t_ff_62_q[0]), .reset(button_6_out));  // open: Qn, preset, en
  T_Flip_Flop t_ff_63 (
    .clk(clock_6_out), .T(random_61_out), .Q(t_ff_63_q[0]), .reset(button_7_out));  // open: Qn, preset, en
  T_Flip_Flop t_ff_64 (
    .clk(clock_8_out), .T(random_64_out), .Q(t_ff_64_q[0]), .reset(button_8_out));  // open: Qn, preset, en
  Random #(.width(1)) random_64 (.clk(clock_8_out), .out(random_64_out));  // open: next, clr
endmodule
