// Logisim project joystick.circ as structural Verilog: 2 circuits, main circuit main
module main (
  input  [4:0] X,
  input  [4:0] Y,
  output _1y,
  output _1x,
  output _2y,
  output _2x,
  output _0y,
  output _0x,
  output _3y,
  output _3x,
  output _4y,
  output _4x,
  output _5y,
  output _5x,
  output _6y,
  output _6x,
  output _7y,
  output _7x,
  output _8y,
  output _8x,
  output _9y,
  output _9x,
  output _10y,
  output _10x,
  output _11y,
  output _11x,
  output _12y,
  output _12x,
  output _13y,
  output _13x,
  output _14y,
  output _14x,
  output _15y,
  output _15x,
  output _16y,
  output _16x,
  output _17y,
  output _17x,
  output _18y,
  output _18x,
  output _19y,
  output _19x,
  output _20y,
  output _20x,
  output _21y,
  output _21x,
  output _22y,
  output _22x,
  output _23y,
  output _23x,
  output _24y,
  output _24x,
  output _25y,
  output _25x,
  output _26y,
  output _26x,
  output _27y,
  output _27x,
  output _28y,
  output _28x,
  output _29y,
  output _29x,
  output _30y,
  output _30x
);

  wire buffer_1_out, buffer_2_out, buffer_3_out, buffer_4_out, buffer_5_out, buffer_6_out, buffer_7_out,
       buffer_8_out, buffer_9_out, buffer_10_out, buffer_11_out, buffer_12_out, buffer_13_out, buffer_14_out,
       buffer_15_out, buffer_16_out, buffer_17_out, buffer_18_out, buffer_19_out, buffer_20_out,
       buffer_21_out, buffer_22_out, buffer_23_out, buffer_24_out, buffer_25_out, buffer_26_out,
       buffer_27_out, buffer_28_out, buffer_29_out, buffer_30_out, buffer_31_out, buffer_32_out,
       buffer_33_out, buffer_34_out, buffer_35_out, buffer_36_out, buffer_37_out, buffer_38_out,
       buffer_39_out, buffer_40_out, buffer_41_out, buffer_42_out, buffer_43_out, buffer_44_out,
       buffer_45_out, buffer_46_out, buffer_47_out, buffer_48_out, buffer_49_out, buffer_50_out,
       buffer_51_out, buffer_52_out, buffer_53_out, buffer_54_out, buffer_55_out, buffer_56_out,
       buffer_57_out, buffer_58_out, buffer_59_out, buffer_60_out, buffer_61_out, buffer_62_out,
       buffer_63_out, buffer_64_out, buffer_65_out, buffer_66_out, buffer_67_out, buffer_68_out,
       buffer_69_out, buffer_70_out, buffer_71_out, buffer_72_out, buffer_73_out, buffer_74_out,
       buffer_75_out, buffer_76_out, buffer_77_out, buffer_78_out, buffer_79_out, buffer_80_out,
       buffer_81_out, buffer_82_out, buffer_83_out, buffer_84_out, buffer_85_out, buffer_86_out,
       buffer_87_out, buffer_88_out, buffer_89_out, buffer_90_out, buffer_91_out, buffer_92_out,
       buffer_93_out, buffer_94_out, buffer_95_out, buffer_96_out, buffer_97_out, buffer_98_out,
       buffer_99_out, buffer_100_out, buffer_101_out, buffer_102_out, buffer_103_out, buffer_104_out,
       buffer_105_out, buffer_106_out, buffer_107_out, buffer_108_out, buffer_109_out, buffer_110_out,
       buffer_111_out, buffer_112_out, buffer_113_out, buffer_114_out, buffer_115_out, buffer_116_out,
       buffer_117_out, buffer_118_out, buffer_119_out, buffer_120_out, buffer_121_out, buffer_122_out,
       buffer_123_out, buffer_124_out, buffer_125_out, buffer_126_out, buffer_127_out, buffer_128_out,
       buffer_129_out, buffer_130_out, buffer_131_out, buffer_132_out, buffer_133_out, buffer_134_out,
       buffer_135_out, buffer_136_out, buffer_137_out, buffer_138_out, buffer_139_out, buffer_140_out,
       buffer_141_out, buffer_142_out, buffer_143_out, buffer_144_out, buffer_145_out, buffer_146_out,
       buffer_147_out, buffer_148_out, buffer_149_out, buffer_150_out, buffer_151_out, buffer_152_out,
       buffer_153_out, buffer_154_out, buffer_155_out, buffer_156_out, buffer_157_out, buffer_158_out,
       not_1_out, not_2_out, not_3_out, not_4_out, not_5_out, not_6_out, not_7_out, not_8_out, not_9_out,
       not_10_out, not_11_out, not_12_out, not_13_out, not_14_out, not_15_out, not_16_out, not_17_out,
       not_18_out, not_19_out, not_20_out, not_21_out, not_22_out, not_23_out, not_24_out, not_25_out,
       not_26_out, not_27_out, not_28_out, not_29_out, not_30_out, not_31_out, not_32_out, not_33_out,
       not_34_out, not_35_out, not_36_out, not_37_out, not_38_out, not_39_out, not_40_out, not_41_out,
       not_42_out, not_43_out, not_44_out, not_45_out, not_46_out, not_47_out, not_48_out, not_49_out,
       not_50_out, not_51_out, not_52_out, not_53_out, not_54_out, not_55_out, not_56_out, not_57_out,
       not_58_out, not_59_out, not_60_out, not_61_out, not_62_out, not_63_out, not_64_out, not_65_out,
       not_66_out, not_67_out, not_68_out, not_69_out, not_70_out, not_71_out, not_72_out, not_73_out,
       not_74_out, not_75_out, not_76_out, not_77_out, not_78_out, not_79_out, not_80_out, not_81_out,
       not_82_out, not_83_out, not_84_out, not_85_out, not_86_out, not_87_out, not_88_out, not_89_out,
       not_90_out, not_91_out, not_92_out, not_93_out, not_94_out, not_95_out, not_96_out, not_97_out,
       not_98_out, not_99_out, not_100_out, not_101_out, not_102_out, not_103_out, not_104_out, not_105_out,
       not_106_out, not_107_out, not_108_out, not_109_out, not_110_out, not_111_out, not_112_out,
       not_113_out, not_114_out, not_115_out, not_116_out, not_117_out, not_118_out, not_119_out,
       not_120_out, not_121_out, not_122_out, not_123_out, not_124_out, not_125_out, not_126_out,
       not_127_out, not_128_out, not_129_out, not_130_out, not_131_out, not_132_out, not_133_out,
       not_134_out, not_135_out, not_136_out, not_137_out, not_138_out, not_139_out, not_140_out,
       not_141_out, not_142_out, not_143_out, not_144_out, not_145_out, not_146_out, not_147_out,
       not_148_out, not_149_out, not_150_out, not_151_out, not_152_out;
  wire [4:0] joystick_1_x, joystick_1_y;

  not not_1 (not_1_out, Y[0]);
  not not_2 (not_2_out, Y[1]);
  not not_3 (not_3_out, Y[2]);
  not not_4 (not_4_out, Y[3]);
  buf buffer_1 (buffer_1_out, Y[4]);
  not not_5 (not_5_out, Y[0]);
  not not_6 (not_6_out, Y[1]);
  not not_7 (not_7_out, Y[2]);
  buf buffer_2 (buffer_2_out, Y[3]);
  not not_8 (not_8_out, Y[4]);
  not not_9 (not_9_out, Y[0]);
  not not_10 (not_10_out, Y[1]);
  not not_11 (not_11_out, Y[2]);
  buf buffer_3 (buffer_3_out, Y[3]);
  buf buffer_4 (buffer_4_out, Y[4]);
  not not_12 (not_12_out, Y[0]);
  not not_13 (not_13_out, Y[1]);
  buf buffer_5 (buffer_5_out, Y[2]);
  not not_14 (not_14_out, Y[3]);
  not not_15 (not_15_out, Y[4]);
  not not_16 (not_16_out, Y[0]);
  not not_17 (not_17_out, Y[1]);
  buf buffer_6 (buffer_6_out, Y[2]);
  not not_18 (not_18_out, Y[3]);
  buf buffer_7 (buffer_7_out, Y[4]);
  not not_19 (not_19_out, Y[0]);
  not not_20 (not_20_out, Y[1]);
  buf buffer_8 (buffer_8_out, Y[2]);
  buf buffer_9 (buffer_9_out, Y[3]);
  not not_21 (not_21_out, Y[4]);
  not not_22 (not_22_out, Y[0]);
  not not_23 (not_23_out, Y[1]);
  buf buffer_10 (buffer_10_out, Y[2]);
  buf buffer_11 (buffer_11_out, Y[3]);
  buf buffer_12 (buffer_12_out, Y[4]);
  not not_24 (not_24_out, Y[0]);
  buf buffer_13 (buffer_13_out, Y[1]);
  not not_25 (not_25_out, Y[2]);
  not not_26 (not_26_out, Y[3]);
  not not_27 (not_27_out, Y[4]);
  not not_28 (not_28_out, Y[0]);
  buf buffer_14 (buffer_14_out, Y[1]);
  not not_29 (not_29_out, Y[2]);
  not not_30 (not_30_out, Y[3]);
  buf buffer_15 (buffer_15_out, Y[4]);
  not not_31 (not_31_out, Y[0]);
  buf buffer_16 (buffer_16_out, Y[1]);
  not not_32 (not_32_out, Y[2]);
  buf buffer_17 (buffer_17_out, Y[3]);
  not not_33 (not_33_out, Y[4]);
  not not_34 (not_34_out, Y[0]);
  buf buffer_18 (buffer_18_out, Y[1]);
  not not_35 (not_35_out, Y[2]);
  buf buffer_19 (buffer_19_out, Y[3]);
  buf buffer_20 (buffer_20_out, Y[4]);
  not not_36 (not_36_out, Y[0]);
  buf buffer_21 (buffer_21_out, Y[1]);
  buf buffer_22 (buffer_22_out, Y[2]);
  not not_37 (not_37_out, Y[3]);
  not not_38 (not_38_out, Y[4]);
  not not_39 (not_39_out, Y[0]);
  buf buffer_23 (buffer_23_out, Y[1]);
  buf buffer_24 (buffer_24_out, Y[2]);
  not not_40 (not_40_out, Y[3]);
  buf buffer_25 (buffer_25_out, Y[4]);
  not not_41 (not_41_out, Y[0]);
  buf buffer_26 (buffer_26_out, Y[1]);
  buf buffer_27 (buffer_27_out, Y[2]);
  buf buffer_28 (buffer_28_out, Y[3]);
  not not_42 (not_42_out, Y[4]);
  not not_43 (not_43_out, Y[0]);
  buf buffer_29 (buffer_29_out, Y[1]);
  buf buffer_30 (buffer_30_out, Y[2]);
  buf buffer_31 (buffer_31_out, Y[3]);
  buf buffer_32 (buffer_32_out, Y[4]);
  buf buffer_33 (buffer_33_out, Y[0]);
  not not_44 (not_44_out, Y[1]);
  not not_45 (not_45_out, Y[2]);
  not not_46 (not_46_out, Y[3]);
  buf buffer_34 (buffer_34_out, Y[4]);
  buf buffer_35 (buffer_35_out, Y[0]);
  not not_47 (not_47_out, Y[1]);
  not not_48 (not_48_out, Y[2]);
  buf buffer_36 (buffer_36_out, Y[3]);
  not not_49 (not_49_out, Y[4]);
  buf buffer_37 (buffer_37_out, Y[0]);
  not not_50 (not_50_out, Y[1]);
  not not_51 (not_51_out, Y[2]);
  buf buffer_38 (buffer_38_out, Y[3]);
  buf buffer_39 (buffer_39_out, Y[4]);
  buf buffer_40 (buffer_40_out, Y[0]);
  not not_52 (not_52_out, Y[1]);
  buf buffer_41 (buffer_41_out, Y[2]);
  not not_53 (not_53_out, Y[3]);
  not not_54 (not_54_out, Y[4]);
  buf buffer_42 (buffer_42_out, Y[0]);
  not not_55 (not_55_out, Y[1]);
  buf buffer_43 (buffer_43_out, Y[2]);
  not not_56 (not_56_out, Y[3]);
  buf buffer_44 (buffer_44_out, Y[4]);
  buf buffer_45 (buffer_45_out, Y[0]);
  not not_57 (not_57_out, Y[1]);
  buf buffer_46 (buffer_46_out, Y[2]);
  buf buffer_47 (buffer_47_out, Y[3]);
  not not_58 (not_58_out, Y[4]);
  buf buffer_48 (buffer_48_out, Y[0]);
  not not_59 (not_59_out, Y[1]);
  buf buffer_49 (buffer_49_out, Y[2]);
  buf buffer_50 (buffer_50_out, Y[3]);
  buf buffer_51 (buffer_51_out, Y[4]);
  buf buffer_52 (buffer_52_out, Y[0]);
  buf buffer_53 (buffer_53_out, Y[1]);
  not not_60 (not_60_out, Y[2]);
  not not_61 (not_61_out, Y[3]);
  not not_62 (not_62_out, Y[4]);
  buf buffer_54 (buffer_54_out, Y[0]);
  buf buffer_55 (buffer_55_out, Y[1]);
  not not_63 (not_63_out, Y[2]);
  not not_64 (not_64_out, Y[3]);
  buf buffer_56 (buffer_56_out, Y[4]);
  buf buffer_57 (buffer_57_out, Y[0]);
  buf buffer_58 (buffer_58_out, Y[1]);
  not not_65 (not_65_out, Y[2]);
  buf buffer_59 (buffer_59_out, Y[3]);
  not not_66 (not_66_out, Y[4]);
  buf buffer_60 (buffer_60_out, Y[0]);
  buf buffer_61 (buffer_61_out, Y[1]);
  not not_67 (not_67_out, Y[2]);
  buf buffer_62 (buffer_62_out, Y[3]);
  buf buffer_63 (buffer_63_out, Y[4]);
  buf buffer_64 (buffer_64_out, Y[0]);
  buf buffer_65 (buffer_65_out, Y[1]);
  buf buffer_66 (buffer_66_out, Y[2]);
  not not_68 (not_68_out, Y[3]);
  not not_69 (not_69_out, Y[4]);
  buf buffer_67 (buffer_67_out, Y[0]);
  buf buffer_68 (buffer_68_out, Y[1]);
  buf buffer_69 (buffer_69_out, Y[2]);
  not not_70 (not_70_out, Y[3]);
  buf buffer_70 (buffer_70_out, Y[4]);
  buf buffer_71 (buffer_71_out, Y[0]);
  buf buffer_72 (buffer_72_out, Y[1]);
  buf buffer_73 (buffer_73_out, Y[2]);
  buf buffer_74 (buffer_74_out, Y[3]);
  not not_71 (not_71_out, Y[4]);
  buf buffer_75 (buffer_75_out, Y[0]);
  buf buffer_76 (buffer_76_out, Y[1]);
  buf buffer_77 (buffer_77_out, Y[2]);
  buf buffer_78 (buffer_78_out, Y[3]);
  buf buffer_79 (buffer_79_out, Y[4]);
  not not_72 (not_72_out, Y[0]);
  not not_73 (not_73_out, Y[1]);
  not not_74 (not_74_out, Y[2]);
  not not_75 (not_75_out, Y[3]);
  not not_76 (not_76_out, Y[4]);
  and and_1 (_1y, not_1_out, not_2_out, not_3_out, not_4_out, buffer_1_out);
  and and_2 (_2y, not_5_out, not_6_out, not_7_out, buffer_2_out, not_8_out);
  and and_3 (_3y, not_9_out, not_10_out, not_11_out, buffer_3_out, buffer_4_out);
  and and_4 (_4y, not_12_out, not_13_out, buffer_5_out, not_14_out, not_15_out);
  and and_5 (_5y, not_16_out, not_17_out, buffer_6_out, not_18_out, buffer_7_out);
  and and_6 (_6y, not_19_out, not_20_out, buffer_8_out, buffer_9_out, not_21_out);
  and and_7 (_7y, not_22_out, not_23_out, buffer_10_out, buffer_11_out, buffer_12_out);
  and and_8 (_8y, not_24_out, buffer_13_out, not_25_out, not_26_out, not_27_out);
  and and_9 (_9y, not_28_out, buffer_14_out, not_29_out, not_30_out, buffer_15_out);
  and and_10 (_10y, not_31_out, buffer_16_out, not_32_out, buffer_17_out, not_33_out);
  and and_11 (_11y, not_34_out, buffer_18_out, not_35_out, buffer_19_out, buffer_20_out);
  and and_12 (_12y, not_36_out, buffer_21_out, buffer_22_out, not_37_out, not_38_out);
  and and_13 (_13y, not_39_out, buffer_23_out, buffer_24_out, not_40_out, buffer_25_out);
  and and_14 (_14y, not_41_out, buffer_26_out, buffer_27_out, buffer_28_out, not_42_out);
  and and_15 (_15y, not_43_out, buffer_29_out, buffer_30_out, buffer_31_out, buffer_32_out);
  and and_16 (_16y, buffer_33_out, not_44_out, not_45_out, not_46_out, buffer_34_out);
  and and_17 (_17y, buffer_35_out, not_47_out, not_48_out, buffer_36_out, not_49_out);
  and and_18 (_18y, buffer_37_out, not_50_out, not_51_out, buffer_38_out, buffer_39_out);
  and and_19 (_19y, buffer_40_out, not_52_out, buffer_41_out, not_53_out, not_54_out);
  and and_20 (_20y, buffer_42_out, not_55_out, buffer_43_out, not_56_out, buffer_44_out);
  and and_21 (_21y, buffer_45_out, not_57_out, buffer_46_out, buffer_47_out, not_58_out);
  and and_22 (_22y, buffer_48_out, not_59_out, buffer_49_out, buffer_50_out, buffer_51_out);
  and and_23 (_23y, buffer_52_out, buffer_53_out, not_60_out, not_61_out, not_62_out);
  and and_24 (_24y, buffer_54_out, buffer_55_out, not_63_out, not_64_out, buffer_56_out);
  and and_25 (_25y, buffer_57_out, buffer_58_out, not_65_out, buffer_59_out, not_66_out);
  and and_26 (_26y, buffer_60_out, buffer_61_out, not_67_out, buffer_62_out, buffer_63_out);
  and and_27 (_27y, buffer_64_out, buffer_65_out, buffer_66_out, not_68_out, not_69_out);
  and and_28 (_28y, buffer_67_out, buffer_68_out, buffer_69_out, not_70_out, buffer_70_out);
  and and_29 (_29y, buffer_71_out, buffer_72_out, buffer_73_out, buffer_74_out, not_71_out);
  and and_30 (_30y, buffer_75_out, buffer_76_out, buffer_77_out, buffer_78_out, buffer_79_out);
  // AND_Gate and_31 has open pins: in0=not_72_out, in1=not_73_out, in2=not_74_out, in3=not_75_out, in4=not_76_out, out=open
  Joystick #(.bits(5)) joystick_1 (.x(joystick_1_x), .y(joystick_1_y));
  DotMatrix #(.matrixcols(2), .matrixrows(5)) dotmatrix_1 (.col0(joystick_1_x), .col1(joystick_1_y));
  and and_32 (_0y, ~_1y, ~_2y, ~_3y, ~_4y, ~_5y, ~_6y, ~_7y, ~_8y, ~_9y, ~_10y, ~_11y, ~_12y, ~_13y, ~_14y, ~_15y, ~_16y, ~_17y, ~_18y, ~_19y, ~_20y, ~_21y, ~_22y, ~_23y, ~_24y, ~_25y, ~_26y, ~_27y, ~_28y, ~_29y, ~_30y);  // AND_Gate
  not not_77 (not_77_out, X[0]);
  not not_78 (not_78_out, X[1]);
  and and_33 (_1x, not_77_out, not_78_out, not_79_out, not_80_out, buffer_80_out);
  not not_79 (not_79_out, X[2]);
  not not_80 (not_80_out, X[3]);
  buf buffer_80 (buffer_80_out, X[4]);
  not not_81 (not_81_out, X[0]);
  not not_82 (not_82_out, X[1]);
  not not_83 (not_83_out, X[2]);
  and and_34 (_2x, not_81_out, not_82_out, not_83_out, buffer_81_out, not_84_out);
  buf buffer_81 (buffer_81_out, X[3]);
  not not_84 (not_84_out, X[4]);
  not not_85 (not_85_out, X[0]);
  not not_86 (not_86_out, X[1]);
  and and_35 (_3x, not_85_out, not_86_out, not_87_out, buffer_82_out, buffer_83_out);
  not not_87 (not_87_out, X[2]);
  buf buffer_82 (buffer_82_out, X[3]);
  buf buffer_83 (buffer_83_out, X[4]);
  not not_88 (not_88_out, X[0]);
  not not_89 (not_89_out, X[1]);
  and and_36 (_4x, not_88_out, not_89_out, buffer_84_out, not_90_out, not_91_out);
  buf buffer_84 (buffer_84_out, X[2]);
  not not_90 (not_90_out, X[3]);
  not not_91 (not_91_out, X[4]);
  not not_92 (not_92_out, X[0]);
  not not_93 (not_93_out, X[1]);
  and and_37 (_5x, not_92_out, not_93_out, buffer_85_out, not_94_out, buffer_86_out);
  buf buffer_85 (buffer_85_out, X[2]);
  not not_94 (not_94_out, X[3]);
  buf buffer_86 (buffer_86_out, X[4]);
  not not_95 (not_95_out, X[0]);
  not not_96 (not_96_out, X[1]);
  and and_38 (_6x, not_95_out, not_96_out, buffer_87_out, buffer_88_out, not_97_out);
  buf buffer_87 (buffer_87_out, X[2]);
  buf buffer_88 (buffer_88_out, X[3]);
  not not_97 (not_97_out, X[4]);
  not not_98 (not_98_out, X[0]);
  not not_99 (not_99_out, X[1]);
  and and_39 (_7x, not_98_out, not_99_out, buffer_89_out, buffer_90_out, buffer_91_out);
  buf buffer_89 (buffer_89_out, X[2]);
  buf buffer_90 (buffer_90_out, X[3]);
  buf buffer_91 (buffer_91_out, X[4]);
  not not_100 (not_100_out, X[0]);
  buf buffer_92 (buffer_92_out, X[1]);
  not not_101 (not_101_out, X[2]);
  and and_40 (_8x, not_100_out, buffer_92_out, not_101_out, not_102_out, not_103_out);
  not not_102 (not_102_out, X[3]);
  not not_103 (not_103_out, X[4]);
  not not_104 (not_104_out, X[0]);
  buf buffer_93 (buffer_93_out, X[1]);
  not not_105 (not_105_out, X[2]);
  and and_41 (_9x, not_104_out, buffer_93_out, not_105_out, not_106_out, buffer_94_out);
  not not_106 (not_106_out, X[3]);
  buf buffer_94 (buffer_94_out, X[4]);
  not not_107 (not_107_out, X[0]);
  buf buffer_95 (buffer_95_out, X[1]);
  and and_42 (_10x, not_107_out, buffer_95_out, not_108_out, buffer_96_out, not_109_out);
  not not_108 (not_108_out, X[2]);
  buf buffer_96 (buffer_96_out, X[3]);
  not not_109 (not_109_out, X[4]);
  not not_110 (not_110_out, X[0]);
  buf buffer_97 (buffer_97_out, X[1]);
  and and_43 (_11x, not_110_out, buffer_97_out, not_111_out, buffer_98_out, buffer_99_out);
  not not_111 (not_111_out, X[2]);
  buf buffer_98 (buffer_98_out, X[3]);
  buf buffer_99 (buffer_99_out, X[4]);
  not not_112 (not_112_out, X[0]);
  buf buffer_100 (buffer_100_out, X[1]);
  buf buffer_101 (buffer_101_out, X[2]);
  and and_44 (_12x, not_112_out, buffer_100_out, buffer_101_out, not_113_out, not_114_out);
  not not_113 (not_113_out, X[3]);
  not not_114 (not_114_out, X[4]);
  not not_115 (not_115_out, X[0]);
  buf buffer_102 (buffer_102_out, X[1]);
  and and_45 (_13x, not_115_out, buffer_102_out, buffer_103_out, not_116_out, buffer_104_out);
  buf buffer_103 (buffer_103_out, X[2]);
  not not_116 (not_116_out, X[3]);
  buf buffer_104 (buffer_104_out, X[4]);
  not not_117 (not_117_out, X[0]);
  buf buffer_105 (buffer_105_out, X[1]);
  and and_46 (_14x, not_117_out, buffer_105_out, buffer_106_out, buffer_107_out, not_118_out);
  buf buffer_106 (buffer_106_out, X[2]);
  buf buffer_107 (buffer_107_out, X[3]);
  not not_118 (not_118_out, X[4]);
  not not_119 (not_119_out, X[0]);
  buf buffer_108 (buffer_108_out, X[1]);
  and and_47 (_15x, not_119_out, buffer_108_out, buffer_109_out, buffer_110_out, buffer_111_out);
  buf buffer_109 (buffer_109_out, X[2]);
  buf buffer_110 (buffer_110_out, X[3]);
  buf buffer_111 (buffer_111_out, X[4]);
  buf buffer_112 (buffer_112_out, X[0]);
  not not_120 (not_120_out, X[1]);
  not not_121 (not_121_out, X[2]);
  and and_48 (_16x, buffer_112_out, not_120_out, not_121_out, not_122_out, buffer_113_out);
  not not_122 (not_122_out, X[3]);
  buf buffer_113 (buffer_113_out, X[4]);
  buf buffer_114 (buffer_114_out, X[0]);
  not not_123 (not_123_out, X[1]);
  and and_49 (_17x, buffer_114_out, not_123_out, not_124_out, buffer_115_out, not_125_out);
  not not_124 (not_124_out, X[2]);
  buf buffer_115 (buffer_115_out, X[3]);
  not not_125 (not_125_out, X[4]);
  buf buffer_116 (buffer_116_out, X[0]);
  not not_126 (not_126_out, X[1]);
  not not_127 (not_127_out, X[2]);
  and and_50 (_18x, buffer_116_out, not_126_out, not_127_out, buffer_117_out, buffer_118_out);
  buf buffer_117 (buffer_117_out, X[3]);
  buf buffer_118 (buffer_118_out, X[4]);
  buf buffer_119 (buffer_119_out, X[0]);
  not not_128 (not_128_out, X[1]);
  and and_51 (_19x, buffer_119_out, not_128_out, buffer_120_out, not_129_out, not_130_out);
  buf buffer_120 (buffer_120_out, X[2]);
  not not_129 (not_129_out, X[3]);
  not not_130 (not_130_out, X[4]);
  buf buffer_121 (buffer_121_out, X[0]);
  not not_131 (not_131_out, X[1]);
  and and_52 (_20x, buffer_121_out, not_131_out, buffer_122_out, not_132_out, buffer_123_out);
  buf buffer_122 (buffer_122_out, X[2]);
  not not_132 (not_132_out, X[3]);
  buf buffer_123 (buffer_123_out, X[4]);
  buf buffer_124 (buffer_124_out, X[0]);
  not not_133 (not_133_out, X[1]);
  buf buffer_125 (buffer_125_out, X[2]);
  and and_53 (_21x, buffer_124_out, not_133_out, buffer_125_out, buffer_126_out, not_134_out);
  buf buffer_126 (buffer_126_out, X[3]);
  not not_134 (not_134_out, X[4]);
  buf buffer_127 (buffer_127_out, X[0]);
  not not_135 (not_135_out, X[1]);
  buf buffer_128 (buffer_128_out, X[2]);
  and and_54 (_22x, buffer_127_out, not_135_out, buffer_128_out, buffer_129_out, buffer_130_out);
  buf buffer_129 (buffer_129_out, X[3]);
  buf buffer_130 (buffer_130_out, X[4]);
  buf buffer_131 (buffer_131_out, X[0]);
  buf buffer_132 (buffer_132_out, X[1]);
  not not_136 (not_136_out, X[2]);
  and and_55 (_23x, buffer_131_out, buffer_132_out, not_136_out, not_137_out, not_138_out);
  not not_137 (not_137_out, X[3]);
  not not_138 (not_138_out, X[4]);
  buf buffer_133 (buffer_133_out, X[0]);
  buf buffer_134 (buffer_134_out, X[1]);
  and and_56 (_24x, buffer_133_out, buffer_134_out, not_139_out, not_140_out, buffer_135_out);
  not not_139 (not_139_out, X[2]);
  not not_140 (not_140_out, X[3]);
  buf buffer_135 (buffer_135_out, X[4]);
  buf buffer_136 (buffer_136_out, X[0]);
  buf buffer_137 (buffer_137_out, X[1]);
  not not_141 (not_141_out, X[2]);
  and and_57 (_25x, buffer_136_out, buffer_137_out, not_141_out, buffer_138_out, not_142_out);
  buf buffer_138 (buffer_138_out, X[3]);
  not not_142 (not_142_out, X[4]);
  buf buffer_139 (buffer_139_out, X[0]);
  buf buffer_140 (buffer_140_out, X[1]);
  not not_143 (not_143_out, X[2]);
  and and_58 (_26x, buffer_139_out, buffer_140_out, not_143_out, buffer_141_out, buffer_142_out);
  buf buffer_141 (buffer_141_out, X[3]);
  buf buffer_142 (buffer_142_out, X[4]);
  buf buffer_143 (buffer_143_out, X[0]);
  buf buffer_144 (buffer_144_out, X[1]);
  and and_59 (_27x, buffer_143_out, buffer_144_out, buffer_145_out, not_144_out, not_145_out);
  buf buffer_145 (buffer_145_out, X[2]);
  not not_144 (not_144_out, X[3]);
  not not_145 (not_145_out, X[4]);
  buf buffer_146 (buffer_146_out, X[0]);
  buf buffer_147 (buffer_147_out, X[1]);
  and and_60 (_28x, buffer_146_out, buffer_147_out, buffer_148_out, not_146_out, buffer_149_out);
  buf buffer_148 (buffer_148_out, X[2]);
  not not_146 (not_146_out, X[3]);
  buf buffer_149 (buffer_149_out, X[4]);
  buf buffer_150 (buffer_150_out, X[0]);
  buf buffer_151 (buffer_151_out, X[1]);
  and and_61 (_29x, buffer_150_out, buffer_151_out, buffer_152_out, buffer_153_out, not_147_out);
  buf buffer_152 (buffer_152_out, X[2]);
  buf buffer_153 (buffer_153_out, X[3]);
  not not_147 (not_147_out, X[4]);
  buf buffer_154 (buffer_154_out, X[0]);
  buf buffer_155 (buffer_155_out, X[1]);
  and and_62 (_30x, buffer_154_out, buffer_155_out, buffer_156_out, buffer_157_out, buffer_158_out);
  buf buffer_156 (buffer_156_out, X[2]);
  buf buffer_157 (buffer_157_out, X[3]);
  buf buffer_158 (buffer_158_out, X[4]);
  not not_148 (not_148_out, X[0]);
  not not_149 (not_149_out, X[1]);
  not not_150 (not_150_out, X[2]);
  // AND_Gate and_63 has open pins: in0=not_148_out, in1=not_149_out, in2=not_150_out, in3=not_151_out, in4=not_152_out, out=open
  not not_151 (not_151_out, X[3]);
  not not_152 (not_152_out, X[4]);
  and and_64 (_0x, ~_1x, ~_2x, ~_3x, ~_4x, ~_5x, ~_6x, ~_7x, ~_8x, ~_9x, ~_10x, ~_11x, ~_12x, ~_13x, ~_14x, ~_15x, ~_16x, ~_17x, ~_18x, ~_19x, ~_20x, ~_21x, ~_22x, ~_23x, ~_24x, ~_25x, ~_26x, ~_27x, ~_28x, ~_29x, ~_30x);  // AND_Gate
endmodule

module teste (
);

  wire main_1__1x, main_1__1y, main_1__2x, main_1__2y, main_1__3x, main_1__3y, main_1__4x, main_1__4y,
       main_1__5x, main_1__5y, main_1__6x, main_1__6y, main_1__7x, main_1__7y, main_1__8x, main_1__8y,
       main_1__9x, main_1__9y, main_1__10x, main_1__10y, main_1__11x, main_1__11y, main_1__12x, main_1__12y,
       main_1__13x, main_1__13y, main_1__14x, main_1__14y, main_1__15x, main_1__15y, main_1__16x,
       main_1__16y, main_1__17x, main_1__17y, main_1__18x, main_1__18y, main_1__19x, main_1__19y,
       main_1__20x, main_1__20y, main_1__21x, main_1__21y, main_1__22x, main_1__22y, main_1__23x,
       main_1__23y, main_1__24x, main_1__24y, main_1__25x, main_1__25y, main_1__26x, main_1__26y,
       main_1__27x, main_1__27y, main_1__28x, main_1__28y, main_1__29x, main_1__29y, main_1__30x, main_1__30y;
  wire [4:0] joystick_1_x, joystick_1_y;

  main main_1 (
    .X(joystick_1_x), .Y(joystick_1_y), ._1x(main_1__1x), ._1y(main_1__1y), ._2y(main_1__2y),
    ._2x(main_1__2x), ._3y(main_1__3y), ._3x(main_1__3x), ._4y(main_1__4y), ._4x(main_1__4x),
    ._5y(main_1__5y), ._5x(main_1__5x), ._6y(main_1__6y), ._6x(main_1__6x), ._7y(main_1__7y),
    ._7x(main_1__7x), ._8y(main_1__8y), ._8x(main_1__8x), ._9y(main_1__9y), ._9x(main_1__9x),
    ._10y(main_1__10y), ._10x(main_1__10x), ._11y(main_1__11y), ._11x(main_1__11x), ._12y(main_1__12y),
    ._12x(main_1__12x), ._13y(main_1__13y), ._13x(main_1__13x), ._14y(main_1__14y), ._14x(main_1__14x),
    ._15y(main_1__15y), ._15x(main_1__15x), ._16y(main_1__16y), ._16x(main_1__16x), ._17y(main_1__17y),
    ._17x(main_1__17x), ._18y(main_1__18y), ._18x(main_1__18x), ._19y(main_1__19y), ._19x(main_1__19x),
    ._20y(main_1__20y), ._20x(main_1__20x), ._21y(main_1__21y), ._21x(main_1__21x), ._22y(main_1__22y),
    ._22x(main_1__22x), ._23y(main_1__23y), ._23x(main_1__23x), ._24y(main_1__24y), ._24x(main_1__24x),
    ._25y(main_1__25y), ._25x(main_1__25x), ._26y(main_1__26y), ._26x(main_1__26x), ._27y(main_1__27y),
    ._27x(main_1__27x), ._28y(main_1__28y), ._28x(main_1__28x), ._29y(main_1__29y), ._29x(main_1__29x),
    ._30y(main_1__30y), ._30x(main_1__30x));  // open: _0y, _0x
  Joystick #(.bits(5)) joystick_1 (.x(joystick_1_x), .y(joystick_1_y));
  // AND_Gate and_1 is placed but not wired
endmodule
