// Logisim project logi.circ as structural Verilog: 1 circuit, main circuit main
module main (
  input  in_1,
  input  in_2,
  input  Preset,
  input  Clear,
  input  in_5,
  input  in_6,
  input  in_7,
  input  in_8,
  input  in_9,
  input  in_10,
  input  in_11,
  input  in_12,
  input  in_13,
  input  in_14,
  input  _128,
  input  _64,
  input  _32,
  input  _16,
  input  _8,
  input  _4,
  input  _2,
  input  _1,
  input  in_23,
  input  in_24,
  input  in_25,
  input  in_26,
  input  in_27,
  input  in_28,
  input  in_29,
  input  in_30,
  input  in_31,
  input  in_32,
  input  in_33,
  input  in_34,
  input  in_35,
  input  in_36,
  input  in_37,
  input  in_38,
  input  in_39,
  input  in_40,
  input  in_41,
  output out_42,
  output _1_2,
  output _2_2,
  output _4_2,
  output _8_2,
  output _16_2,
  output _32_2,
  output _64_2,
  output out_50,
  output _128_2,
  output out_52,
  output out_53,
  output out_54
);

  wire A_out, and_1_out, and_2_out, and_3_out, and_4_out, and_5_out, and_6_out, and_7_out, and_8_out,
       and_13_out, and_14_out, and_15_out, and_16_out, B_out, button_1_out, button_2_out, button_3_out,
       C_out, caps_out, clock_1_out, clock_3_out, clock_4_out, clock_5_out, controlled_buffer_2_out,
       controlled_buffer_3_out, d_ff_14_q, d_ff_15_q, d_ff_16_q, d_ff_17_q, d_ff_18_q, d_ff_19_q, d_ff_21_q,
       d_ff_21_qn, D_out, F_out, G_out, H_out, I_out, J_out, K_out, L_out, M_out, N_out, not_1_out,
       not_2_out, not_3_out, not_4_out, not_5_out, not_7_out, not_8_out, O_out, or_2_out, P_out, Q_out,
       R_2_out, R_out, S_out, shift_register_1_out, shift_register_1_q3, T_out, U_out, undriven, V_out,
       W_out, X_out, Y_out, Z_out, \Ç_out ;
  wire [5:5] or_1_out;
  wire [6:0] d_ff_12_q, d_ff_13_q, random_1_out, random_2_out, random_3_out, random_4_out, random_5_out;
  wire [31:0] random_6_out, random_7_out, random_8_out, random_9_out, random_10_out, random_11_out,
       random_12_out, random_13_out, random_14_out, random_15_out, random_16_out, random_17_out,
       random_18_out, random_19_out, random_20_out, random_21_out, random_22_out, random_23_out,
       random_24_out, random_25_out, random_26_out, random_27_out, random_28_out, random_29_out,
       random_30_out, random_31_out, random_32_out, random_33_out, random_34_out, random_35_out,
       random_36_out, random_37_out;

  Clock clock_1 (.out(clock_1_out));
  D_Flip_Flop d_ff_1 (.clk(clock_1_out), .D(d_ff_13_q[0]), .Q(d_ff_13_q[6]));  // open: Qn, preset, en, reset
  Button button_1 (.out(button_1_out));
  Clock CLOCK_2 (.out(d_ff_12_q[6]));
  DotMatrix #(.matrixcols(32), .matrixrows(32)) dotmatrix_1 (
    .col0(random_34_out), .col1(random_35_out), .col2(random_36_out), .col3(random_37_out),
    .col4(random_30_out), .col5(random_31_out), .col6(random_32_out), .col7(random_33_out),
    .col8(random_26_out), .col9(random_27_out), .col10(random_28_out), .col11(random_29_out),
    .col12(random_22_out), .col13(random_23_out), .col14(random_24_out), .col15(random_25_out),
    .col16(random_18_out), .col17(random_19_out), .col18(random_20_out), .col19(random_21_out),
    .col20(random_14_out), .col21(random_15_out), .col22(random_16_out), .col23(random_17_out),
    .col24(random_10_out), .col25(random_11_out), .col26(random_12_out), .col27(random_13_out),
    .col28(random_6_out), .col29(random_7_out), .col30(random_8_out), .col31(random_9_out));
  D_Flip_Flop d_ff_2 (.clk(clock_1_out), .D(d_ff_13_q[6]), .Q(d_ff_13_q[5]));  // open: Qn, preset, en, reset
  LED led_1 (.in(d_ff_12_q[6]));
  D_Flip_Flop d_ff_3 (.clk(clock_1_out), .D(d_ff_13_q[5]), .Q(d_ff_13_q[4]));  // open: Qn, preset, en, reset
  D_Flip_Flop d_ff_4 (.clk(button_1_out), .D(button_1_out), .Q(out_42));  // open: Qn, preset, en, reset
  Random #(.width(7)) random_1 (.clk(d_ff_12_q[6]), .out(random_1_out));  // open: next, clr
  LED led_2 (.in(d_ff_12_q[4]));
  D_Flip_Flop d_ff_5 (
    .clk(d_ff_12_q[6]), .D(d_ff_12_q[0]), .Q(d_ff_12_q[4]), .preset(not_1_out), .reset(not_2_out));  // open: Qn, en
  D_Flip_Flop d_ff_6 (.clk(clock_1_out), .D(d_ff_13_q[4]), .Q(d_ff_13_q[3]));  // open: Qn, preset, en, reset
  Random #(.width(7)) random_2 (.clk(d_ff_12_q[6]), .out(random_2_out));  // open: next, clr
  Random #(.width(7)) random_3 (.clk(d_ff_12_q[6]), .out(random_3_out));  // open: next, clr
  LED led_3 (.in(d_ff_12_q[3]));
  D_Flip_Flop d_ff_7 (
    .clk(d_ff_12_q[6]), .D(d_ff_12_q[4]), .Q(d_ff_12_q[3]), .preset(not_1_out), .reset(not_2_out));  // open: Qn, en
  D_Flip_Flop d_ff_8 (.clk(clock_1_out), .D(d_ff_13_q[3]), .Q(d_ff_13_q[2]));  // open: Qn, preset, en, reset
  Random #(.width(7)) random_4 (.clk(d_ff_12_q[6]), .out(random_4_out));  // open: next, clr
  LED led_4 (.in(d_ff_12_q[2]));
  D_Flip_Flop d_ff_9 (
    .clk(d_ff_12_q[6]), .D(d_ff_12_q[3]), .Q(d_ff_12_q[2]), .preset(not_1_out), .reset(not_2_out));  // open: Qn, en
  DotMatrix dotmatrix_2 (
    .col0(random_5_out), .col1(random_4_out), .col2(random_2_out), .col3(random_3_out), .col4(random_1_out));
  Random #(.width(7)) random_5 (.clk(d_ff_12_q[6]), .out(random_5_out));  // open: next, clr
  LED led_5 (.in(d_ff_12_q[1]));
  D_Flip_Flop d_ff_10 (
    .clk(d_ff_12_q[6]), .D(d_ff_12_q[2]), .Q(d_ff_12_q[1]), .preset(not_1_out), .reset(not_2_out));  // open: Qn, en
  not not_1 (not_1_out, Preset);
  Random #(.width(32)) random_6 (.clk(d_ff_12_q[6]), .out(random_6_out));  // open: next, clr
  Random #(.width(32)) random_7 (.clk(d_ff_12_q[6]), .out(random_7_out));  // open: next, clr
  Random #(.width(32)) random_8 (.clk(d_ff_12_q[6]), .out(random_8_out));  // open: next, clr
  Random #(.width(32)) random_9 (.next(d_ff_12_q[6]), .out(random_9_out));  // open: clk, clr
  D_Flip_Flop d_ff_11 (.clk(clock_1_out), .D(d_ff_13_q[2]), .Q(d_ff_13_q[1]));  // open: Qn, preset, en, reset
  D_Flip_Flop d_ff_12 (
    .clk(d_ff_12_q[6]), .D(d_ff_12_q[1]), .Q(d_ff_12_q[0]), .preset(not_1_out), .reset(not_2_out));  // open: Qn, en
  not not_2 (not_2_out, Clear);
  Random #(.width(32)) random_10 (.clk(d_ff_12_q[6]), .out(random_10_out));  // open: next, clr
  Random #(.width(32)) random_11 (.clk(d_ff_12_q[6]), .out(random_11_out));  // open: next, clr
  Random #(.width(32)) random_12 (.clk(d_ff_12_q[6]), .out(random_12_out));  // open: next, clr
  Random #(.width(32)) random_13 (.next(d_ff_12_q[6]), .out(random_13_out));  // open: clk, clr
  D_Flip_Flop d_ff_13 (.clk(clock_1_out), .D(d_ff_13_q[1]), .Q(d_ff_13_q[0]));  // open: Qn, preset, en, reset
  Random #(.width(32)) random_14 (.clk(d_ff_12_q[6]), .out(random_14_out));  // open: next, clr
  Random #(.width(32)) random_15 (.clk(d_ff_12_q[6]), .out(random_15_out));  // open: next, clr
  Random #(.width(32)) random_16 (.clk(d_ff_12_q[6]), .out(random_16_out));  // open: next, clr
  Random #(.width(32)) random_17 (.next(d_ff_12_q[6]), .out(random_17_out));  // open: clk, clr
  Random #(.width(32)) random_18 (.clk(d_ff_12_q[6]), .out(random_18_out));  // open: next, clr
  Random #(.width(32)) random_19 (.clk(d_ff_12_q[6]), .out(random_19_out));  // open: next, clr
  Random #(.width(32)) random_20 (.clk(d_ff_12_q[6]), .out(random_20_out));  // open: next, clr
  Random #(.width(32)) random_21 (.next(d_ff_12_q[6]), .out(random_21_out));  // open: clk, clr
  Random #(.width(32)) random_22 (.clk(d_ff_12_q[6]), .out(random_22_out));  // open: next, clr
  Random #(.width(32)) random_23 (.clk(d_ff_12_q[6]), .out(random_23_out));  // open: next, clr
  Random #(.width(32)) random_24 (.clk(d_ff_12_q[6]), .out(random_24_out));  // open: next, clr
  Random #(.width(32)) random_25 (.next(d_ff_12_q[6]), .out(random_25_out));  // open: clk, clr
  DotMatrix dotmatrix_3 (.col0(d_ff_13_q), .col1(d_ff_13_q), .col2(d_ff_13_q), .col3(d_ff_13_q), .col4(d_ff_13_q));
  DotMatrix #(.matrixcols(7)) dotmatrix_4 (
    .col0({{2{d_ff_12_q[6]}}, d_ff_12_q[4:0]}), .col1({{2{d_ff_12_q[6]}}, d_ff_12_q[4:0]}),
    .col2({{2{d_ff_12_q[6]}}, d_ff_12_q[4:0]}), .col3({{2{d_ff_12_q[6]}}, d_ff_12_q[4:0]}),
    .col4({{2{d_ff_12_q[6]}}, d_ff_12_q[4:0]}), .col5({{2{d_ff_12_q[6]}}, d_ff_12_q[4:0]}),
    .col6({{2{d_ff_12_q[6]}}, d_ff_12_q[4:0]}));
  Random #(.width(32)) random_26 (.clk(d_ff_12_q[6]), .out(random_26_out));  // open: next, clr
  Random #(.width(32)) random_27 (.clk(d_ff_12_q[6]), .out(random_27_out));  // open: next, clr
  Random #(.width(32)) random_28 (.clk(d_ff_12_q[6]), .out(random_28_out));  // open: next, clr
  Random #(.width(32)) random_29 (.next(d_ff_12_q[6]), .out(random_29_out));  // open: clk, clr
  Random #(.width(32)) random_30 (.clk(d_ff_12_q[6]), .out(random_30_out));  // open: next, clr
  Random #(.width(32)) random_31 (.clk(d_ff_12_q[6]), .out(random_31_out));  // open: next, clr
  Random #(.width(32)) random_32 (.clk(d_ff_12_q[6]), .out(random_32_out));  // open: next, clr
  Random #(.width(32)) random_33 (.next(d_ff_12_q[6]), .out(random_33_out));  // open: clk, clr
  Random #(.width(32)) random_34 (.clk(d_ff_12_q[6]), .out(random_34_out));  // open: next, clr
  Random #(.width(32)) random_35 (.clk(d_ff_12_q[6]), .out(random_35_out));  // open: next, clr
  Random #(.width(32)) random_36 (.clk(d_ff_12_q[6]), .out(random_36_out));  // open: next, clr
  Random #(.width(32)) random_37 (.next(d_ff_12_q[6]), .out(random_37_out));  // open: clk, clr
  Clock clock_3 (.out(clock_3_out));
  Clock clock_4 (.out(clock_4_out));
  DotMatrix #(.matrixcols(9), .matrixrows(9)) dotmatrix_5 (
    .col0({3'b000, {2{or_1_out[5]}}, 4'b0000}), .col1({1'b0, {2{or_1_out[5]}}, 2'b00, or_1_out[5], 3'b000}),
    .col2({1'b0, or_1_out[5], 4'b0000, or_1_out[5], 2'b00}),
    .col3({2'b00, or_1_out[5], 4'b0000, or_1_out[5], 1'b0}),
    .col4({3'b000, or_1_out[5], 4'b0000, or_1_out[5]}),
    .col5({2'b00, or_1_out[5], 4'b0000, or_1_out[5], 1'b0}),
    .col6({1'b0, or_1_out[5], 4'b0000, or_1_out[5], 2'b00}),
    .col7({1'b0, {2{or_1_out[5]}}, 2'b00, or_1_out[5], 3'b000}), .col8({3'b000, {2{or_1_out[5]}}, 4'b0000}));
  not not_3 (not_3_out, clock_4_out);
  Controlled_Buffer controlled_buffer_1 (.in(clock_4_out), .en(not_3_out));  // open: out
  D_Flip_Flop d_ff_14 (.clk(undriven), .Q(d_ff_14_q), .preset(and_1_out), .reset(not_4_out));  // open: D, Qn, en
  and and_1 (and_1_out, d_ff_15_q, not_4_out);
  D_Flip_Flop d_ff_15 (
    .clk(clock_3_out), .D(in_30), .Q(d_ff_15_q), .preset(and_2_out), .reset(not_5_out));  // open: Qn, en
  and and_2 (and_2_out, in_34, in_35);
  D_Flip_Flop d_ff_16 (
    .clk(undriven), .D(d_ff_14_q), .Q(d_ff_16_q), .preset(and_3_out), .reset(not_4_out));  // open: Qn, en
  and and_3 (and_3_out, d_ff_17_q, not_4_out);
  D_Flip_Flop d_ff_17 (
    .clk(clock_3_out), .D(d_ff_15_q), .Q(d_ff_17_q), .preset(and_4_out), .reset(not_5_out));  // open: Qn, en
  and and_4 (and_4_out, in_36, in_34);
  and and_5 (and_5_out, d_ff_19_q, not_4_out);
  and and_6 (and_6_out, in_34, in_37);
  assign controlled_buffer_2_out = in_1 ? 1'b1 : 1'bz;  // Controlled_Buffer controlled_buffer_2
  or or_1 (or_1_out[5], controlled_buffer_2_out, controlled_buffer_3_out);
  D_Flip_Flop d_ff_18 (
    .clk(undriven), .D(d_ff_16_q), .Q(d_ff_18_q), .preset(and_5_out), .reset(not_4_out));  // open: Qn, en
  and and_7 (and_7_out, d_ff_21_q, not_4_out);
  D_Flip_Flop d_ff_19 (
    .clk(clock_3_out), .D(d_ff_17_q), .Q(d_ff_19_q), .preset(and_6_out), .reset(not_5_out));  // open: Qn, en
  and and_8 (and_8_out, in_38, in_34);
  assign controlled_buffer_3_out = in_2 ? d_ff_13_q[6] : 1'bz;  // Controlled_Buffer controlled_buffer_3
  D_Flip_Flop d_ff_20 (.clk(undriven), .D(d_ff_18_q), .preset(and_7_out), .reset(not_4_out));  // open: Q, Qn, en
  not not_4 (not_4_out, d_ff_21_qn);
  D_Flip_Flop d_ff_21 (
    .clk(clock_3_out), .D(d_ff_19_q), .Q(d_ff_21_q), .Qn(d_ff_21_qn), .preset(and_8_out), .reset(not_5_out));  // open: en
  not not_5 (not_5_out, d_ff_21_qn);
  Clock clock_5 (.out(clock_5_out));
  // NOT_Gate not_6 has open pins: in=d_ff_13_q[6], out=open
  not not_7 (not_7_out, in_40);
  Shift_Register #(.length(4)) shift_register_1 (
    .in(shift_register_1_q3), .clk(clock_5_out), .out(shift_register_1_out), .q3(shift_register_1_q3));  // open: shift, load, clr, d0, q0, d1, q1, d2, q2, d3
  and and_9 (out_50, in_40, or_2_out, in_41);
  and and_10 (out_52, not_7_out, or_2_out, in_41);
  and and_11 (out_53, in_41, or_2_out, not_7_out);
  and and_12 (out_54, not_7_out, or_2_out, not_8_out);
  not not_8 (not_8_out, in_41);
  RAM #(.bus("separate")) ram_1 (
    .addr({in_7, in_8, in_9, in_10, in_11, in_12, in_13, in_14}),
    .din({_128, _64, _32, _16, _8, _4, _2, _1}),
    .data({_128_2, _64_2, _32_2, _16_2, _8_2, _4_2, _2_2, _1_2}), .str(in_23), .sel(in_25),
    .clk(shift_register_1_out), .ld(in_26), .clr(in_24));
  and and_13 (and_13_out, in_41, in_29, in_40);
  and and_14 (and_14_out, not_7_out, in_31, not_8_out);
  and and_15 (and_15_out, not_8_out, in_32, in_40);
  and and_16 (and_16_out, not_8_out, in_33, not_7_out);
  Button Q (.out(Q_out));
  Button R (.out(R_out));
  Button W (.out(W_out));
  Button A (.out(A_out));
  Button S (.out(S_out));
  Button D (.out(D_out));
  Button C (.out(C_out));
  Button Z (.out(Z_out));
  Button X (.out(X_out));
  or or_2 (or_2_out, and_13_out, and_14_out, and_15_out, and_16_out);
  Button T (.out(T_out));
  Button R_2 (.out(R_2_out));
  Button G (.out(G_out));
  Button F (.out(F_out));
  Button B (.out(B_out));
  Button V (.out(V_out));
  Button I (.out(I_out));
  Button U (.out(U_out));
  Button Y (.out(Y_out));
  Button K (.out(K_out));
  Button H (.out(H_out));
  Button J (.out(J_out));
  Button M (.out(M_out));
  Button button_2 (.out(button_2_out));
  Button N (.out(N_out));
  Button P (.out(P_out));
  Button O (.out(O_out));
  Button \u_Ç  (.out(\Ç_out ));
  Button L (.out(L_out));
  Button button_3 (.out(button_3_out));
  Button caps (.out(caps_out));
  TTY tty_1 (.data({in_5, {4{in_6}}, in_5, in_6}), .clk(shift_register_1_out), .we(in_27), .clr(in_28));
endmodule
