// Logisim project mouse.circ as structural Verilog: 2 circuits, main circuit main
module main (
);

  wire decoder_1_out0, decoder_1_out1, decoder_1_out2, decoder_1_out3, decoder_1_out4, decoder_1_out5,
       decoder_1_out6, decoder_1_out7, decoder_1_out8, decoder_1_out9, decoder_1_out10, decoder_1_out11,
       decoder_1_out12, decoder_1_out13, decoder_1_out14, decoder_1_out15, decoder_2_out1, decoder_2_out2,
       decoder_2_out3, decoder_2_out4, decoder_2_out5, decoder_2_out6, decoder_2_out7, decoder_2_out8,
       decoder_2_out9, decoder_2_out10, decoder_2_out11, decoder_2_out12, decoder_2_out13, decoder_2_out14,
       decoder_2_out15;
  wire [3:0] joystick_1_x, joystick_1_y;
  wire [14:0] and_15_out, and_30_out, and_45_out, and_60_out, and_75_out, and_90_out, and_105_out,
       and_120_out, and_135_out, and_150_out, and_165_out, and_180_out, and_195_out, and_210_out, and_225_out;

  Decoder #(.select(4)) decoder_1 (
    .out0(decoder_1_out0), .out1(decoder_1_out1), .out2(decoder_1_out2), .out3(decoder_1_out3),
    .out4(decoder_1_out4), .out5(decoder_1_out5), .out6(decoder_1_out6), .out7(decoder_1_out7),
    .out8(decoder_1_out8), .out9(decoder_1_out9), .out10(decoder_1_out10), .out11(decoder_1_out11),
    .out12(decoder_1_out12), .out13(decoder_1_out13), .out14(decoder_1_out14), .out15(decoder_1_out15),
    .sel(joystick_1_y));  // open: en
  Joystick joystick_1 (.x(joystick_1_x), .y(joystick_1_y));
  Decoder #(.select(4)) decoder_2 (
    .out1(decoder_2_out1), .out2(decoder_2_out2), .out3(decoder_2_out3), .out4(decoder_2_out4),
    .out5(decoder_2_out5), .out6(decoder_2_out6), .out7(decoder_2_out7), .out8(decoder_2_out8),
    .out9(decoder_2_out9), .out10(decoder_2_out10), .out11(decoder_2_out11), .out12(decoder_2_out12),
    .out13(decoder_2_out13), .out14(decoder_2_out14), .out15(decoder_2_out15), .sel(joystick_1_x));  // open: out0, en
  and and_1 (and_15_out[14], decoder_1_out1, decoder_2_out1);
  and and_2 (and_15_out[13], decoder_1_out2, decoder_2_out1);
  and and_3 (and_15_out[12], decoder_1_out3, decoder_2_out1);
  and and_4 (and_15_out[11], decoder_1_out4, decoder_2_out1);
  and and_5 (and_15_out[10], decoder_1_out5, decoder_2_out1);
  and and_6 (and_15_out[9], decoder_1_out6, decoder_2_out1);
  and and_7 (and_15_out[8], decoder_1_out7, decoder_2_out1);
  and and_8 (and_15_out[7], decoder_1_out8, decoder_2_out1);
  and and_9 (and_15_out[6], decoder_1_out9, decoder_2_out1);
  and and_10 (and_15_out[5], decoder_1_out10, decoder_2_out1);
  and and_11 (and_15_out[4], decoder_1_out11, decoder_2_out1);
  and and_12 (and_15_out[3], decoder_1_out12, decoder_2_out1);
  and and_13 (and_15_out[2], decoder_1_out13, decoder_2_out1);
  and and_14 (and_15_out[1], decoder_1_out14, decoder_2_out1);
  and and_15 (and_15_out[0], decoder_1_out15, decoder_2_out1);
  and and_16 (and_30_out[14], decoder_1_out1, decoder_2_out2);
  and and_17 (and_30_out[13], decoder_1_out2, decoder_2_out2);
  and and_18 (and_30_out[12], decoder_1_out3, decoder_2_out2);
  and and_19 (and_30_out[11], decoder_1_out4, decoder_2_out2);
  and and_20 (and_30_out[10], decoder_1_out5, decoder_2_out2);
  and and_21 (and_30_out[9], decoder_1_out6, decoder_2_out2);
  and and_22 (and_30_out[8], decoder_1_out7, decoder_2_out2);
  and and_23 (and_30_out[7], decoder_1_out8, decoder_2_out2);
  and and_24 (and_30_out[6], decoder_1_out9, decoder_2_out2);
  and and_25 (and_30_out[5], decoder_1_out10, decoder_2_out2);
  and and_26 (and_30_out[4], decoder_1_out11, decoder_2_out2);
  and and_27 (and_30_out[3], decoder_1_out12, decoder_2_out2);
  and and_28 (and_30_out[2], decoder_1_out13, decoder_2_out2);
  and and_29 (and_30_out[1], decoder_1_out14, decoder_2_out2);
  and and_30 (and_30_out[0], decoder_1_out15, decoder_2_out2);
  and and_31 (and_45_out[14], decoder_1_out1, decoder_2_out3);
  and and_32 (and_45_out[13], decoder_1_out2, decoder_2_out3);
  and and_33 (and_45_out[12], decoder_1_out3, decoder_2_out3);
  and and_34 (and_45_out[11], decoder_1_out4, decoder_2_out3);
  and and_35 (and_45_out[10], decoder_1_out5, decoder_2_out3);
  and and_36 (and_45_out[9], decoder_1_out6, decoder_2_out3);
  and and_37 (and_45_out[8], decoder_1_out7, decoder_2_out3);
  and and_38 (and_45_out[7], decoder_1_out8, decoder_2_out3);
  and and_39 (and_45_out[6], decoder_1_out9, decoder_2_out3);
  and and_40 (and_45_out[5], decoder_1_out10, decoder_2_out3);
  and and_41 (and_45_out[4], decoder_1_out11, decoder_2_out3);
  and and_42 (and_45_out[3], decoder_1_out12, decoder_2_out3);
  and and_43 (and_45_out[2], decoder_1_out13, decoder_2_out3);
  and and_44 (and_45_out[1], decoder_1_out14, decoder_2_out3);
  and and_45 (and_45_out[0], decoder_1_out15, decoder_2_out3);
  and and_46 (and_60_out[14], decoder_1_out1, decoder_2_out4);
  and and_47 (and_60_out[13], decoder_1_out2, decoder_2_out4);
  and and_48 (and_60_out[12], decoder_1_out3, decoder_2_out4);
  and and_49 (and_60_out[11], decoder_1_out4, decoder_2_out4);
  and and_50 (and_60_out[10], decoder_1_out5, decoder_2_out4);
  and and_51 (and_60_out[9], decoder_1_out6, decoder_2_out4);
  and and_52 (and_60_out[8], decoder_1_out7, decoder_2_out4);
  and and_53 (and_60_out[7], decoder_1_out8, decoder_2_out4);
  and and_54 (and_60_out[6], decoder_1_out9, decoder_2_out4);
  and and_55 (and_60_out[5], decoder_1_out10, decoder_2_out4);
  and and_56 (and_60_out[4], decoder_1_out11, decoder_2_out4);
  and and_57 (and_60_out[3], decoder_1_out12, decoder_2_out4);
  and and_58 (and_60_out[2], decoder_1_out13, decoder_2_out4);
  and and_59 (and_60_out[1], decoder_1_out14, decoder_2_out4);
  and and_60 (and_60_out[0], decoder_1_out15, decoder_2_out4);
  and and_61 (and_75_out[14], decoder_1_out1, decoder_2_out5);
  and and_62 (and_75_out[13], decoder_1_out2, decoder_2_out5);
  and and_63 (and_75_out[12], decoder_1_out3, decoder_2_out5);
  and and_64 (and_75_out[11], decoder_1_out4, decoder_2_out5);
  and and_65 (and_75_out[10], decoder_1_out5, decoder_2_out5);
  and and_66 (and_75_out[9], decoder_1_out6, decoder_2_out5);
  and and_67 (and_75_out[8], decoder_1_out7, decoder_2_out5);
  and and_68 (and_75_out[7], decoder_1_out8, decoder_2_out5);
  and and_69 (and_75_out[6], decoder_1_out9, decoder_2_out5);
  and and_70 (and_75_out[5], decoder_1_out10, decoder_2_out5);
  and and_71 (and_75_out[4], decoder_1_out11, decoder_2_out5);
  and and_72 (and_75_out[3], decoder_1_out12, decoder_2_out5);
  and and_73 (and_75_out[2], decoder_1_out13, decoder_2_out5);
  and and_74 (and_75_out[1], decoder_1_out14, decoder_2_out5);
  and and_75 (and_75_out[0], decoder_1_out15, decoder_2_out5);
  and and_76 (and_90_out[14], decoder_1_out1, decoder_2_out6);
  and and_77 (and_90_out[13], decoder_1_out2, decoder_2_out6);
  and and_78 (and_90_out[12], decoder_1_out3, decoder_2_out6);
  and and_79 (and_90_out[11], decoder_1_out4, decoder_2_out6);
  and and_80 (and_90_out[10], decoder_1_out5, decoder_2_out6);
  and and_81 (and_90_out[9], decoder_1_out6, decoder_2_out6);
  and and_82 (and_90_out[8], decoder_1_out7, decoder_2_out6);
  and and_83 (and_90_out[7], decoder_1_out8, decoder_2_out6);
  and and_84 (and_90_out[6], decoder_1_out9, decoder_2_out6);
  and and_85 (and_90_out[5], decoder_1_out10, decoder_2_out6);
  and and_86 (and_90_out[4], decoder_1_out11, decoder_2_out6);
  and and_87 (and_90_out[3], decoder_1_out12, decoder_2_out6);
  and and_88 (and_90_out[2], decoder_1_out13, decoder_2_out6);
  and and_89 (and_90_out[1], decoder_1_out14, decoder_2_out6);
  and and_90 (and_90_out[0], decoder_1_out15, decoder_2_out6);
  and and_91 (and_105_out[14], decoder_1_out1, decoder_2_out7);
  and and_92 (and_105_out[13], decoder_1_out2, decoder_2_out7);
  and and_93 (and_105_out[12], decoder_1_out3, decoder_2_out7);
  and and_94 (and_105_out[11], decoder_1_out4, decoder_2_out7);
  and and_95 (and_105_out[10], decoder_1_out5, decoder_2_out7);
  and and_96 (and_105_out[9], decoder_1_out6, decoder_2_out7);
  and and_97 (and_105_out[8], decoder_1_out7, decoder_2_out7);
  and and_98 (and_105_out[7], decoder_1_out8, decoder_2_out7);
  and and_99 (and_105_out[6], decoder_1_out9, decoder_2_out7);
  and and_100 (and_105_out[5], decoder_1_out10, decoder_2_out7);
  and and_101 (and_105_out[4], decoder_1_out11, decoder_2_out7);
  and and_102 (and_105_out[3], decoder_1_out12, decoder_2_out7);
  and and_103 (and_105_out[2], decoder_1_out13, decoder_2_out7);
  and and_104 (and_105_out[1], decoder_1_out14, decoder_2_out7);
  and and_105 (and_105_out[0], decoder_1_out15, decoder_2_out7);
  and and_106 (and_120_out[14], decoder_1_out1, decoder_2_out8);
  and and_107 (and_120_out[13], decoder_1_out2, decoder_2_out8);
  and and_108 (and_120_out[12], decoder_1_out3, decoder_2_out8);
  and and_109 (and_120_out[11], decoder_1_out4, decoder_2_out8);
  and and_110 (and_120_out[10], decoder_1_out5, decoder_2_out8);
  and and_111 (and_120_out[9], decoder_1_out6, decoder_2_out8);
  and and_112 (and_120_out[8], decoder_1_out7, decoder_2_out8);
  and and_113 (and_120_out[7], decoder_1_out8, decoder_2_out8);
  and and_114 (and_120_out[6], decoder_1_out9, decoder_2_out8);
  and and_115 (and_120_out[5], decoder_1_out10, decoder_2_out8);
  and and_116 (and_120_out[4], decoder_1_out11, decoder_2_out8);
  and and_117 (and_120_out[3], decoder_1_out12, decoder_2_out8);
  and and_118 (and_120_out[2], decoder_1_out13, decoder_2_out8);
  and and_119 (and_120_out[1], decoder_1_out14, decoder_2_out8);
  and and_120 (and_120_out[0], decoder_1_out15, decoder_2_out8);
  and and_121 (and_135_out[14], decoder_1_out1, decoder_2_out9);
  and and_122 (and_135_out[13], decoder_1_out2, decoder_2_out9);
  and and_123 (and_135_out[12], decoder_1_out3, decoder_2_out9);
  and and_124 (and_135_out[11], decoder_1_out4, decoder_2_out9);
  and and_125 (and_135_out[10], decoder_1_out5, decoder_2_out9);
  and and_126 (and_135_out[9], decoder_1_out6, decoder_2_out9);
  and and_127 (and_135_out[8], decoder_1_out7, decoder_2_out9);
  and and_128 (and_135_out[7], decoder_1_out8, decoder_2_out9);
  and and_129 (and_135_out[6], decoder_1_out9, decoder_2_out9);
  and and_130 (and_135_out[5], decoder_1_out10, decoder_2_out9);
  and and_131 (and_135_out[4], decoder_1_out11, decoder_2_out9);
  and and_132 (and_135_out[3], decoder_1_out12, decoder_2_out9);
  and and_133 (and_135_out[2], decoder_1_out13, decoder_2_out9);
  and and_134 (and_135_out[1], decoder_1_out14, decoder_2_out9);
  and and_135 (and_135_out[0], decoder_1_out15, decoder_2_out9);
  and and_136 (and_150_out[14], decoder_1_out1, decoder_2_out10);
  and and_137 (and_150_out[13], decoder_1_out2, decoder_2_out10);
  and and_138 (and_150_out[12], decoder_1_out3, decoder_2_out10);
  and and_139 (and_150_out[11], decoder_1_out4, decoder_2_out10);
  and and_140 (and_150_out[10], decoder_1_out5, decoder_2_out10);
  and and_141 (and_150_out[9], decoder_1_out6, decoder_2_out10);
  and and_142 (and_150_out[8], decoder_1_out7, decoder_2_out10);
  and and_143 (and_150_out[7], decoder_1_out8, decoder_2_out10);
  and and_144 (and_150_out[6], decoder_1_out9, decoder_2_out10);
  and and_145 (and_150_out[5], decoder_1_out10, decoder_2_out10);
  and and_146 (and_150_out[4], decoder_1_out11, decoder_2_out10);
  and and_147 (and_150_out[3], decoder_1_out12, decoder_2_out10);
  and and_148 (and_150_out[2], decoder_1_out13, decoder_2_out10);
  and and_149 (and_150_out[1], decoder_1_out14, decoder_2_out10);
  and and_150 (and_150_out[0], decoder_1_out15, decoder_2_out10);
  and and_151 (and_165_out[14], decoder_1_out1, decoder_2_out11);
  and and_152 (and_165_out[13], decoder_1_out2, decoder_2_out11);
  and and_153 (and_165_out[12], decoder_1_out3, decoder_2_out11);
  and and_154 (and_165_out[11], decoder_1_out4, decoder_2_out11);
  and and_155 (and_165_out[10], decoder_1_out5, decoder_2_out11);
  and and_156 (and_165_out[9], decoder_1_out6, decoder_2_out11);
  and and_157 (and_165_out[8], decoder_1_out7, decoder_2_out11);
  and and_158 (and_165_out[7], decoder_1_out8, decoder_2_out11);
  and and_159 (and_165_out[6], decoder_1_out9, decoder_2_out11);
  and and_160 (and_165_out[5], decoder_1_out10, decoder_2_out11);
  and and_161 (and_165_out[4], decoder_1_out11, decoder_2_out11);
  and and_162 (and_165_out[3], decoder_1_out12, decoder_2_out11);
  and and_163 (and_165_out[2], decoder_1_out13, decoder_2_out11);
  and and_164 (and_165_out[1], decoder_1_out14, decoder_2_out11);
  and and_165 (and_165_out[0], decoder_1_out15, decoder_2_out11);
  and and_166 (and_180_out[14], decoder_1_out1, decoder_2_out12);
  and and_167 (and_180_out[13], decoder_1_out2, decoder_2_out12);
  and and_168 (and_180_out[12], decoder_1_out3, decoder_2_out12);
  and and_169 (and_180_out[11], decoder_1_out4, decoder_2_out12);
  and and_170 (and_180_out[10], decoder_1_out5, decoder_2_out12);
  and and_171 (and_180_out[9], decoder_1_out6, decoder_2_out12);
  and and_172 (and_180_out[8], decoder_1_out7, decoder_2_out12);
  and and_173 (and_180_out[7], decoder_1_out8, decoder_2_out12);
  and and_174 (and_180_out[6], decoder_1_out9, decoder_2_out12);
  and and_175 (and_180_out[5], decoder_1_out10, decoder_2_out12);
  and and_176 (and_180_out[4], decoder_1_out11, decoder_2_out12);
  and and_177 (and_180_out[3], decoder_1_out12, decoder_2_out12);
  and and_178 (and_180_out[2], decoder_1_out13, decoder_2_out12);
  and and_179 (and_180_out[1], decoder_1_out14, decoder_2_out12);
  and and_180 (and_180_out[0], decoder_1_out15, decoder_2_out12);
  and and_181 (and_195_out[14], decoder_1_out1, decoder_2_out13);
  and and_182 (and_195_out[13], decoder_1_out2, decoder_2_out13);
  and and_183 (and_195_out[12], decoder_1_out3, decoder_2_out13);
  and and_184 (and_195_out[11], decoder_1_out4, decoder_2_out13);
  and and_185 (and_195_out[10], decoder_1_out5, decoder_2_out13);
  and and_186 (and_195_out[9], decoder_1_out6, decoder_2_out13);
  and and_187 (and_195_out[8], decoder_1_out7, decoder_2_out13);
  and and_188 (and_195_out[7], decoder_1_out8, decoder_2_out13);
  and and_189 (and_195_out[6], decoder_1_out9, decoder_2_out13);
  and and_190 (and_195_out[5], decoder_1_out10, decoder_2_out13);
  and and_191 (and_195_out[4], decoder_1_out11, decoder_2_out13);
  and and_192 (and_195_out[3], decoder_1_out12, decoder_2_out13);
  and and_193 (and_195_out[2], decoder_1_out13, decoder_2_out13);
  and and_194 (and_195_out[1], decoder_1_out14, decoder_2_out13);
  and and_195 (and_195_out[0], decoder_1_out15, decoder_2_out13);
  and and_196 (and_210_out[14], decoder_1_out1, decoder_2_out14);
  and and_197 (and_210_out[13], decoder_1_out2, decoder_2_out14);
  and and_198 (and_210_out[12], decoder_1_out3, decoder_2_out14);
  and and_199 (and_210_out[11], decoder_1_out4, decoder_2_out14);
  and and_200 (and_210_out[10], decoder_1_out5, decoder_2_out14);
  and and_201 (and_210_out[9], decoder_1_out6, decoder_2_out14);
  and and_202 (and_210_out[8], decoder_1_out7, decoder_2_out14);
  and and_203 (and_210_out[7], decoder_1_out8, decoder_2_out14);
  and and_204 (and_210_out[6], decoder_1_out9, decoder_2_out14);
  and and_205 (and_210_out[5], decoder_1_out10, decoder_2_out14);
  and and_206 (and_210_out[4], decoder_1_out11, decoder_2_out14);
  and and_207 (and_210_out[3], decoder_1_out12, decoder_2_out14);
  and and_208 (and_210_out[2], decoder_1_out13, decoder_2_out14);
  and and_209 (and_210_out[1], decoder_1_out14, decoder_2_out14);
  and and_210 (and_210_out[0], decoder_1_out15, decoder_2_out14);
  and and_211 (and_225_out[14], decoder_1_out1, decoder_2_out15);
  and and_212 (and_225_out[13], decoder_1_out2, decoder_2_out15);
  and and_213 (and_225_out[12], decoder_1_out3, decoder_2_out15);
  and and_214 (and_225_out[11], decoder_1_out4, decoder_2_out15);
  and and_215 (and_225_out[10], decoder_1_out5, decoder_2_out15);
  and and_216 (and_225_out[9], decoder_1_out6, decoder_2_out15);
  and and_217 (and_225_out[8], decoder_1_out7, decoder_2_out15);
  and and_218 (and_225_out[7], decoder_1_out8, decoder_2_out15);
  and and_219 (and_225_out[6], decoder_1_out9, decoder_2_out15);
  and and_220 (and_225_out[5], decoder_1_out10, decoder_2_out15);
  and and_221 (and_225_out[4], decoder_1_out11, decoder_2_out15);
  and and_222 (and_225_out[3], decoder_1_out12, decoder_2_out15);
  and and_223 (and_225_out[2], decoder_1_out13, decoder_2_out15);
  and and_224 (and_225_out[1], decoder_1_out14, decoder_2_out15);
  and and_225 (and_225_out[0], decoder_1_out15, decoder_2_out15);
  DotMatrix #(.matrixcols(15), .matrixrows(15)) dotmatrix_1 (
    .col0(and_15_out), .col1(and_30_out), .col2(and_45_out), .col3(and_60_out), .col4(and_75_out),
    .col5(and_90_out), .col6(and_105_out), .col7(and_120_out), .col8(and_135_out), .col9(and_150_out),
    .col10(and_165_out), .col11(and_180_out), .col12(and_195_out), .col13(and_210_out), .col14(and_225_out));
endmodule

module seila (
  input  in_1,
  input  in_2,
  input  in_3,
  input  in_4,
  input  in_5,
  input  in_6,
  input  in_7
);

  wire button_1_out, button_2_out, clock_1_out;
  wire [3:0] contador_assincrono_crescente_1_saida_bcd, contador_asssincrono_decrescente_1_saida_bcd,
       contador_decimal_1_saida_bcd, contador_hexadecimal_1_saida_bcd, contador_hexadecimal_2_saida_bcd,
       contador_qualquer_1_saida_bcd, contador_sincrono_impar_1_saiuda_bcd,
       contador_sincrono_par_1_saida_bcd, joystick_1_x, joystick_1_y, main_1_hor_minus, main_1_hor_plus,
       main_1_min_minus, main_1_min_plus, main_1_seg_minus, main_1_seg_plus;
  wire [14:0] main_2_matriz_0, main_2_matriz_1, main_2_matriz_2, main_2_matriz_3, main_2_matriz_4,
       main_2_matriz_5, main_2_matriz_6, main_2_matriz_7, main_2_matriz_8, main_2_matriz_9, main_2_matriz_10,
       main_2_matriz_11, main_2_matriz_12, main_2_matriz_13, main_2_matriz_14;

  Hex_Digit_Display hex_digit_display_1 (.value(main_1_hor_plus));  // open: dp
  Contador_Hexadecimal contador_hexadecimal_1 (
    .CLOCK(clock_1_out), .SAIDA_BCD(contador_hexadecimal_1_saida_bcd));  // open: Reset
  Hex_Digit_Display hex_digit_display_2 (.value(contador_asssincrono_decrescente_1_saida_bcd));  // open: dp
  Contador_Asssincrono_Decrescente contador_asssincrono_decrescente_1 (
    .CLOCK(clock_1_out), .SAIDA_BCD(contador_asssincrono_decrescente_1_saida_bcd));
  Contador_Hexadecimal contador_hexadecimal_2 (
    .CLOCK(clock_1_out), .SAIDA_BCD(contador_hexadecimal_2_saida_bcd));  // open: Reset
  Hex_Digit_Display hex_digit_display_3 (.value(main_1_hor_minus));  // open: dp
  Button button_1 (.out(button_1_out));
  CI_RELOGIO_main main_1 (
    .AJUSHOR(button_1_out), .AJUSMIN(button_2_out), .CLOCK(clock_1_out), .HOR_plus(main_1_hor_plus),
    .HOR_minus(main_1_hor_minus), .Min_plus(main_1_min_plus), .MIN_minus(main_1_min_minus),
    .SEG_plus(main_1_seg_plus), .Seg_minus(main_1_seg_minus));
  Button button_2 (.out(button_2_out));
  Clock clock_1 (.out(clock_1_out));
  Hex_Digit_Display hex_digit_display_4 (.value(contador_hexadecimal_1_saida_bcd));  // open: dp
  _7_Segment_Display u_7_segment_display_1 ();  // open: g, f, a, b, e, d, c, dp
  // Cod__display_7SEG_adaptavel cod_display_7seg_adaptavel_1: pin names not known; wires that end beside it: contador_hexadecimal_2_saida_bcd[2], contador_hexadecimal_2_saida_bcd[0], contador_hexadecimal_2_saida_bcd[1], contador_hexadecimal_2_saida_bcd[2], contador_hexadecimal_2_saida_bcd[3]
  Hex_Digit_Display hex_digit_display_5 (.value(main_1_min_minus));  // open: dp
  Hex_Digit_Display hex_digit_display_6 (.value(main_1_min_plus));  // open: dp
  Hex_Digit_Display hex_digit_display_7 (.value(contador_sincrono_par_1_saida_bcd));  // open: dp
  Contador_Sincrono_Par contador_sincrono_par_1 (.CLOCK(clock_1_out), .SAIDA_BCD(contador_sincrono_par_1_saida_bcd));
  Hex_Digit_Display hex_digit_display_8 (.value(contador_assincrono_crescente_1_saida_bcd));  // open: dp
  Contador_Assincrono_Crescente contador_assincrono_crescente_1 (
    .CLOCK(clock_1_out), .SAIDA_BCD(contador_assincrono_crescente_1_saida_bcd));
  Hex_Digit_Display hex_digit_display_9 (.value(main_1_seg_plus));  // open: dp
  Hex_Digit_Display hex_digit_display_10 (.value(main_1_seg_minus));  // open: dp
  _7_Segment_Display u_7_segment_display_2 (
    .g(in_4), .f(in_3), .a(in_2), .b(in_1), .e(in_5), .d(in_6), .c(in_7));  // open: dp
  Hex_Digit_Display hex_digit_display_11 (.value(contador_decimal_1_saida_bcd));  // open: dp
  Contador_Decimal contador_decimal_1 (.CLOCK(clock_1_out), .SAIDA_BCD(contador_decimal_1_saida_bcd));  // open: Reset
  Hex_Digit_Display hex_digit_display_12 (.value(contador_qualquer_1_saida_bcd));  // open: dp
  Contador_Qualquer contador_qualquer_1 (.CLOCK(clock_1_out), .SAIDA_BCD(contador_qualquer_1_saida_bcd));
  Hex_Digit_Display hex_digit_display_13 (.value(contador_sincrono_impar_1_saiuda_bcd));  // open: dp
  Contador_Sincrono_Impar contador_sincrono_impar_1 (
    .CLOCK(clock_1_out), .Saiuda_BCD(contador_sincrono_impar_1_saiuda_bcd));
  CI_joystick_main main_2 (
    .EIXO_x(joystick_1_y), .EIXO_Y(joystick_1_x), .Matriz_0(main_2_matriz_0), .Matriz_1(main_2_matriz_1),
    .Matriz_2(main_2_matriz_2), .Matriz_3(main_2_matriz_3), .Matriz_4(main_2_matriz_4),
    .Matriz_5(main_2_matriz_5), .Matriz_6(main_2_matriz_6), .Matriz_7(main_2_matriz_7),
    .Matriz_8(main_2_matriz_8), .Matriz_9(main_2_matriz_9), .Matriz_10(main_2_matriz_10),
    .Matriz_11(main_2_matriz_11), .Matriz_12(main_2_matriz_12), .Matriz_13(main_2_matriz_13),
    .Matriz_14(main_2_matriz_14));
  DotMatrix #(.matrixcols(15), .matrixrows(15)) dotmatrix_1 (
    .col0(main_2_matriz_0), .col1(main_2_matriz_1), .col2(main_2_matriz_2), .col3(main_2_matriz_3),
    .col4(main_2_matriz_4), .col5(main_2_matriz_5), .col6(main_2_matriz_6), .col7(main_2_matriz_7),
    .col8(main_2_matriz_8), .col9(main_2_matriz_9), .col10(main_2_matriz_10), .col11(main_2_matriz_11),
    .col12(main_2_matriz_12), .col13(main_2_matriz_13), .col14(main_2_matriz_14));
  // Codificador_Display_7SEG codificador_display_7seg_1: pin names not known
  Joystick joystick_1 (.x(joystick_1_x), .y(joystick_1_y));
  _7_Segment_Display u_7_segment_display_3 ();  // open: g, f, a, b, e, d, c, dp

  // Notes on the sheet:
  //   :
  //   :
endmodule
