// Logisim project nome.circ as structural Verilog: 3 circuits, main circuit main
module main (
  output [31:0] out_1
);

  wire and_34_out, button_1_out, clock_1_out, comparator_1_eq, controlled_buffer_1_out,
       controlled_buffer_2_out, d_ff_1_qn, not_1_out, not_2_out, or_1_out, shift_register_1_out,
       shift_register_1_q0, shift_register_1_q1, shift_register_1_q2, shift_register_1_q3,
       shift_register_1_q4, shift_register_1_q5, shift_register_1_q6, shift_register_1_q7,
       shift_register_1_q8, shift_register_1_q9, shift_register_1_q10, shift_register_1_q11,
       shift_register_1_q12, shift_register_1_q13, shift_register_1_q14, shift_register_1_q15,
       shift_register_1_q16, shift_register_1_q17, shift_register_1_q18, shift_register_1_q19,
       shift_register_1_q20, shift_register_1_q21, shift_register_1_q22, shift_register_1_q23,
       shift_register_1_q24, shift_register_1_q25, shift_register_1_q26, shift_register_1_q27,
       shift_register_1_q28, shift_register_1_q29, shift_register_1_q30, shift_register_1_q31, t_ff_1_q,
       undriven;
  wire [7:0] counter_1_q;
  wire [31:0] and_2_out, and_3_out, and_4_out, and_5_out, and_6_out, and_7_out, and_8_out, and_9_out,
       and_10_out, and_11_out, and_12_out, and_13_out, and_14_out, and_15_out, and_16_out, and_17_out,
       and_18_out, and_19_out, and_20_out, and_21_out, and_22_out, and_23_out, and_24_out, and_25_out,
       and_26_out, and_27_out, and_28_out, and_29_out, and_30_out, and_31_out, and_32_out, and_33_out,
       aumentador_de_bits_1_out, aumentador_de_bits_2_out, aumentador_de_bits_3_out,
       aumentador_de_bits_4_out, aumentador_de_bits_5_out, aumentador_de_bits_6_out,
       aumentador_de_bits_7_out, aumentador_de_bits_8_out, aumentador_de_bits_9_out,
       aumentador_de_bits_10_out, aumentador_de_bits_11_out, aumentador_de_bits_12_out,
       aumentador_de_bits_13_out, aumentador_de_bits_14_out, aumentador_de_bits_15_out,
       aumentador_de_bits_16_out, aumentador_de_bits_17_out, aumentador_de_bits_18_out,
       aumentador_de_bits_19_out, aumentador_de_bits_20_out, aumentador_de_bits_21_out,
       aumentador_de_bits_22_out, aumentador_de_bits_23_out, aumentador_de_bits_24_out,
       aumentador_de_bits_25_out, aumentador_de_bits_26_out, aumentador_de_bits_27_out,
       aumentador_de_bits_28_out, aumentador_de_bits_29_out, aumentador_de_bits_30_out,
       aumentador_de_bits_31_out, aumentador_de_bits_32_out, translate_1_output, translate_2_output,
       translate_3_output, translate_4_output, translate_5_output, translate_6_output, translate_7_output,
       translate_8_output, translate_9_output, translate_10_output, translate_11_output, translate_12_output,
       translate_13_output, translate_14_output, translate_15_output, translate_16_output,
       translate_17_output, translate_18_output, translate_19_output, translate_20_output,
       translate_21_output, translate_22_output, translate_23_output, translate_24_output,
       translate_25_output, translate_26_output, translate_27_output, translate_28_output,
       translate_29_output, translate_30_output, translate_31_output, translate_32_output;

  Button button_1 (.out(button_1_out));
  Clock clock_1 (.out(clock_1_out));
  T_Flip_Flop t_ff_1 (.clk(button_1_out), .T(button_1_out), .Q(t_ff_1_q));  // open: Qn, preset, reset, en
  not not_1 (not_1_out, button_1_out);
  not not_2 (not_2_out, not_1_out);
  Counter counter_1 (.Q(counter_1_q), .clk(clock_1_out), .clr(comparator_1_eq));  // open: load, D, count, carry
  // AND_Gate and_1 has open pins: in0=clock_1_out, in1=or_1_out, out=open
  assign controlled_buffer_1_out = not_2_out ? 1'b1 : 1'bz;  // Controlled_Buffer controlled_buffer_1
  assign controlled_buffer_2_out = not_2_out ? 1'b0 : 1'bz;  // Controlled_Buffer controlled_buffer_2
  Shift_Register #(.length(32)) shift_register_1 (
    .in(shift_register_1_out), .clk(clock_1_out), .out(shift_register_1_out), .load(controlled_buffer_1_out),
    .d0(controlled_buffer_1_out), .q0(shift_register_1_q0), .d1(controlled_buffer_2_out),
    .q1(shift_register_1_q1), .d2(controlled_buffer_2_out), .q2(shift_register_1_q2),
    .d3(controlled_buffer_2_out), .q3(shift_register_1_q3), .d4(controlled_buffer_2_out),
    .q4(shift_register_1_q4), .d5(controlled_buffer_2_out), .q5(shift_register_1_q5),
    .d6(controlled_buffer_2_out), .q6(shift_register_1_q6), .d7(controlled_buffer_2_out),
    .q7(shift_register_1_q7), .d8(controlled_buffer_2_out), .q8(shift_register_1_q8),
    .d9(controlled_buffer_2_out), .q9(shift_register_1_q9), .d10(controlled_buffer_2_out),
    .q10(shift_register_1_q10), .d11(controlled_buffer_2_out), .q11(shift_register_1_q11),
    .d12(controlled_buffer_2_out), .q12(shift_register_1_q12), .d13(controlled_buffer_2_out),
    .q13(shift_register_1_q13), .d14(controlled_buffer_2_out), .q14(shift_register_1_q14),
    .d15(controlled_buffer_2_out), .q15(shift_register_1_q15), .d16(controlled_buffer_2_out),
    .q16(shift_register_1_q16), .d17(controlled_buffer_2_out), .q17(shift_register_1_q17),
    .d18(controlled_buffer_2_out), .q18(shift_register_1_q18), .d19(controlled_buffer_2_out),
    .q19(shift_register_1_q19), .d20(controlled_buffer_2_out), .q20(shift_register_1_q20),
    .d21(controlled_buffer_2_out), .q21(shift_register_1_q21), .d22(controlled_buffer_2_out),
    .q22(shift_register_1_q22), .d23(controlled_buffer_2_out), .q23(shift_register_1_q23),
    .d24(controlled_buffer_2_out), .q24(shift_register_1_q24), .d25(controlled_buffer_2_out),
    .q25(shift_register_1_q25), .d26(controlled_buffer_2_out), .q26(shift_register_1_q26),
    .d27(controlled_buffer_2_out), .q27(shift_register_1_q27), .d28(controlled_buffer_2_out),
    .q28(shift_register_1_q28), .d29(controlled_buffer_2_out), .q29(shift_register_1_q29),
    .d30(controlled_buffer_2_out), .q30(shift_register_1_q30), .d31(controlled_buffer_2_out),
    .q31(shift_register_1_q31));  // open: shift, clr
  Comparator comparator_1 (.a(8'h20), .b(counter_1_q), .eq(comparator_1_eq));  // open: gt, lt
  ROM #(.dataWidth(32)) rom_1 (.addr(counter_1_q), .data(out_1), .sel(t_ff_1_q));
  or or_1 (or_1_out, shift_register_1_q0, shift_register_1_q1, shift_register_1_q2, shift_register_1_q3, shift_register_1_q4, shift_register_1_q5, shift_register_1_q6, shift_register_1_q7, shift_register_1_q8, shift_register_1_q9, shift_register_1_q10, shift_register_1_q11, shift_register_1_q12, shift_register_1_q13, shift_register_1_q14, shift_register_1_q15, shift_register_1_q16, shift_register_1_q17, shift_register_1_q18, shift_register_1_q19, shift_register_1_q20, shift_register_1_q21, shift_register_1_q22, shift_register_1_q23, shift_register_1_q24, shift_register_1_q25, shift_register_1_q26, shift_register_1_q27, shift_register_1_q28, shift_register_1_q29, shift_register_1_q30, shift_register_1_q31);
  D_Flip_Flop d_ff_1 (
    .clk(shift_register_1_q31), .D(shift_register_1_q31), .Qn(d_ff_1_qn));  // open: Q, preset, en, reset
  assign and_2_out = out_1 & aumentador_de_bits_1_out;  // AND_Gate and_2, 32 bits wide
  aumentador_de_bits aumentador_de_bits_1 (.IN(shift_register_1_q0), .Out(aumentador_de_bits_1_out));
  assign and_3_out = out_1 & aumentador_de_bits_2_out;  // AND_Gate and_3, 32 bits wide
  aumentador_de_bits aumentador_de_bits_2 (.IN(shift_register_1_q1), .Out(aumentador_de_bits_2_out));
  assign and_4_out = out_1 & aumentador_de_bits_3_out;  // AND_Gate and_4, 32 bits wide
  aumentador_de_bits aumentador_de_bits_3 (.IN(shift_register_1_q2), .Out(aumentador_de_bits_3_out));
  assign and_5_out = out_1 & aumentador_de_bits_4_out;  // AND_Gate and_5, 32 bits wide
  aumentador_de_bits aumentador_de_bits_4 (.IN(shift_register_1_q3), .Out(aumentador_de_bits_4_out));
  assign and_6_out = out_1 & aumentador_de_bits_5_out;  // AND_Gate and_6, 32 bits wide
  aumentador_de_bits aumentador_de_bits_5 (.IN(shift_register_1_q4), .Out(aumentador_de_bits_5_out));
  assign and_7_out = out_1 & aumentador_de_bits_6_out;  // AND_Gate and_7, 32 bits wide
  aumentador_de_bits aumentador_de_bits_6 (.IN(shift_register_1_q5), .Out(aumentador_de_bits_6_out));
  assign and_8_out = out_1 & aumentador_de_bits_7_out;  // AND_Gate and_8, 32 bits wide
  aumentador_de_bits aumentador_de_bits_7 (.IN(shift_register_1_q6), .Out(aumentador_de_bits_7_out));
  assign and_9_out = out_1 & aumentador_de_bits_8_out;  // AND_Gate and_9, 32 bits wide
  aumentador_de_bits aumentador_de_bits_8 (.IN(shift_register_1_q7), .Out(aumentador_de_bits_8_out));
  assign and_10_out = out_1 & aumentador_de_bits_9_out;  // AND_Gate and_10, 32 bits wide
  aumentador_de_bits aumentador_de_bits_9 (.IN(shift_register_1_q8), .Out(aumentador_de_bits_9_out));
  assign and_11_out = out_1 & aumentador_de_bits_10_out;  // AND_Gate and_11, 32 bits wide
  aumentador_de_bits aumentador_de_bits_10 (.IN(shift_register_1_q9), .Out(aumentador_de_bits_10_out));
  assign and_12_out = out_1 & aumentador_de_bits_11_out;  // AND_Gate and_12, 32 bits wide
  aumentador_de_bits aumentador_de_bits_11 (.IN(shift_register_1_q10), .Out(aumentador_de_bits_11_out));
  assign and_13_out = out_1 & aumentador_de_bits_12_out;  // AND_Gate and_13, 32 bits wide
  aumentador_de_bits aumentador_de_bits_12 (.IN(shift_register_1_q11), .Out(aumentador_de_bits_12_out));
  assign and_14_out = out_1 & aumentador_de_bits_13_out;  // AND_Gate and_14, 32 bits wide
  aumentador_de_bits aumentador_de_bits_13 (.IN(shift_register_1_q12), .Out(aumentador_de_bits_13_out));
  assign and_15_out = out_1 & aumentador_de_bits_14_out;  // AND_Gate and_15, 32 bits wide
  aumentador_de_bits aumentador_de_bits_14 (.IN(shift_register_1_q13), .Out(aumentador_de_bits_14_out));
  assign and_16_out = out_1 & aumentador_de_bits_15_out;  // AND_Gate and_16, 32 bits wide
  aumentador_de_bits aumentador_de_bits_15 (.IN(shift_register_1_q14), .Out(aumentador_de_bits_15_out));
  assign and_17_out = out_1 & aumentador_de_bits_16_out;  // AND_Gate and_17, 32 bits wide
  aumentador_de_bits aumentador_de_bits_16 (.IN(shift_register_1_q15), .Out(aumentador_de_bits_16_out));
  assign and_18_out = out_1 & aumentador_de_bits_17_out;  // AND_Gate and_18, 32 bits wide
  aumentador_de_bits aumentador_de_bits_17 (.IN(shift_register_1_q16), .Out(aumentador_de_bits_17_out));
  assign and_19_out = out_1 & aumentador_de_bits_18_out;  // AND_Gate and_19, 32 bits wide
  aumentador_de_bits aumentador_de_bits_18 (.IN(shift_register_1_q17), .Out(aumentador_de_bits_18_out));
  assign and_20_out = out_1 & aumentador_de_bits_19_out;  // AND_Gate and_20, 32 bits wide
  aumentador_de_bits aumentador_de_bits_19 (.IN(shift_register_1_q18), .Out(aumentador_de_bits_19_out));
  assign and_21_out = out_1 & aumentador_de_bits_20_out;  // AND_Gate and_21, 32 bits wide
  aumentador_de_bits aumentador_de_bits_20 (.IN(shift_register_1_q19), .Out(aumentador_de_bits_20_out));
  assign and_22_out = out_1 & aumentador_de_bits_21_out;  // AND_Gate and_22, 32 bits wide
  aumentador_de_bits aumentador_de_bits_21 (.IN(shift_register_1_q20), .Out(aumentador_de_bits_21_out));
  assign and_23_out = out_1 & aumentador_de_bits_22_out;  // AND_Gate and_23, 32 bits wide
  aumentador_de_bits aumentador_de_bits_22 (.IN(shift_register_1_q21), .Out(aumentador_de_bits_22_out));
  assign and_24_out = out_1 & aumentador_de_bits_23_out;  // AND_Gate and_24, 32 bits wide
  aumentador_de_bits aumentador_de_bits_23 (.IN(shift_register_1_q22), .Out(aumentador_de_bits_23_out));
  assign and_25_out = out_1 & aumentador_de_bits_24_out;  // AND_Gate and_25, 32 bits wide
  aumentador_de_bits aumentador_de_bits_24 (.IN(shift_register_1_q23), .Out(aumentador_de_bits_24_out));
  assign and_26_out = out_1 & aumentador_de_bits_25_out;  // AND_Gate and_26, 32 bits wide
  aumentador_de_bits aumentador_de_bits_25 (.IN(shift_register_1_q24), .Out(aumentador_de_bits_25_out));
  assign and_27_out = out_1 & aumentador_de_bits_26_out;  // AND_Gate and_27, 32 bits wide
  aumentador_de_bits aumentador_de_bits_26 (.IN(shift_register_1_q25), .Out(aumentador_de_bits_26_out));
  assign and_28_out = out_1 & aumentador_de_bits_27_out;  // AND_Gate and_28, 32 bits wide
  aumentador_de_bits aumentador_de_bits_27 (.IN(shift_register_1_q26), .Out(aumentador_de_bits_27_out));
  assign and_29_out = out_1 & aumentador_de_bits_28_out;  // AND_Gate and_29, 32 bits wide
  aumentador_de_bits aumentador_de_bits_28 (.IN(shift_register_1_q27), .Out(aumentador_de_bits_28_out));
  assign and_30_out = out_1 & aumentador_de_bits_29_out;  // AND_Gate and_30, 32 bits wide
  aumentador_de_bits aumentador_de_bits_29 (.IN(shift_register_1_q28), .Out(aumentador_de_bits_29_out));
  assign and_31_out = out_1 & aumentador_de_bits_30_out;  // AND_Gate and_31, 32 bits wide
  aumentador_de_bits aumentador_de_bits_30 (.IN(shift_register_1_q29), .Out(aumentador_de_bits_30_out));
  assign and_32_out = out_1 & aumentador_de_bits_31_out;  // AND_Gate and_32, 32 bits wide
  aumentador_de_bits aumentador_de_bits_31 (.IN(shift_register_1_q30), .Out(aumentador_de_bits_31_out));
  assign and_33_out = out_1 & aumentador_de_bits_32_out;  // AND_Gate and_33, 32 bits wide
  aumentador_de_bits aumentador_de_bits_32 (.IN(shift_register_1_q31), .Out(aumentador_de_bits_32_out));
  and and_34 (and_34_out, d_ff_1_qn, undriven);
  translate translate_1 (
    .Reset(button_1_out), .Clock(and_34_out), .Input(and_2_out), .Output(translate_1_output));  // open: Set
  translate translate_2 (
    .Reset(button_1_out), .Clock(and_34_out), .Input(and_3_out), .Output(translate_2_output));  // open: Set
  translate translate_3 (
    .Reset(button_1_out), .Clock(and_34_out), .Input(and_4_out), .Output(translate_3_output));  // open: Set
  translate translate_4 (
    .Reset(button_1_out), .Clock(and_34_out), .Input(and_5_out), .Output(translate_4_output));  // open: Set
  translate translate_5 (
    .Reset(button_1_out), .Clock(and_34_out), .Input(and_6_out), .Output(translate_5_output));  // open: Set
  translate translate_6 (
    .Reset(button_1_out), .Clock(and_34_out), .Input(and_7_out), .Output(translate_6_output));  // open: Set
  translate translate_7 (
    .Reset(button_1_out), .Clock(and_34_out), .Input(and_8_out), .Output(translate_7_output));  // open: Set
  translate translate_8 (
    .Reset(button_1_out), .Clock(and_34_out), .Input(and_9_out), .Output(translate_8_output));  // open: Set
  translate translate_9 (
    .Reset(button_1_out), .Clock(and_34_out), .Input(and_10_out), .Output(translate_9_output));  // open: Set
  translate translate_10 (
    .Reset(button_1_out), .Clock(and_34_out), .Input(and_11_out), .Output(translate_10_output));  // open: Set
  translate translate_11 (
    .Reset(button_1_out), .Clock(and_34_out), .Input(and_12_out), .Output(translate_11_output));  // open: Set
  translate translate_12 (
    .Reset(button_1_out), .Clock(and_34_out), .Input(and_13_out), .Output(translate_12_output));  // open: Set
  translate translate_13 (
    .Reset(button_1_out), .Clock(and_34_out), .Input(and_14_out), .Output(translate_13_output));  // open: Set
  translate translate_14 (
    .Reset(button_1_out), .Clock(and_34_out), .Input(and_15_out), .Output(translate_14_output));  // open: Set
  translate translate_15 (
    .Reset(button_1_out), .Clock(and_34_out), .Input(and_16_out), .Output(translate_15_output));  // open: Set
  translate translate_16 (
    .Reset(button_1_out), .Clock(and_34_out), .Input(and_17_out), .Output(translate_16_output));  // open: Set
  translate translate_17 (
    .Reset(button_1_out), .Clock(and_34_out), .Input(and_18_out), .Output(translate_17_output));  // open: Set
  translate translate_18 (
    .Reset(button_1_out), .Clock(and_34_out), .Input(and_19_out), .Output(translate_18_output));  // open: Set
  translate translate_19 (
    .Reset(button_1_out), .Clock(and_34_out), .Input(and_20_out), .Output(translate_19_output));  // open: Set
  translate translate_20 (
    .Reset(button_1_out), .Clock(and_34_out), .Input(and_21_out), .Output(translate_20_output));  // open: Set
  translate translate_21 (
    .Reset(button_1_out), .Clock(and_34_out), .Input(and_22_out), .Output(translate_21_output));  // open: Set
  translate translate_22 (
    .Reset(button_1_out), .Clock(and_34_out), .Input(and_23_out), .Output(translate_22_output));  // open: Set
  translate translate_23 (
    .Reset(button_1_out), .Clock(and_34_out), .Input(and_24_out), .Output(translate_23_output));  // open: Set
  translate translate_24 (
    .Reset(button_1_out), .Clock(and_34_out), .Input(and_25_out), .Output(translate_24_output));  // open: Set
  translate translate_25 (
    .Reset(button_1_out), .Clock(and_34_out), .Input(and_26_out), .Output(translate_25_output));  // open: Set
  translate translate_26 (
    .Reset(button_1_out), .Clock(and_34_out), .Input(and_27_out), .Output(translate_26_output));  // open: Set
  translate translate_27 (
    .Reset(button_1_out), .Clock(and_34_out), .Input(and_28_out), .Output(translate_27_output));  // open: Set
  translate translate_28 (
    .Reset(button_1_out), .Clock(and_34_out), .Input(and_29_out), .Output(translate_28_output));  // open: Set
  translate translate_29 (
    .Reset(button_1_out), .Clock(and_34_out), .Input(and_30_out), .Output(translate_29_output));  // open: Set
  translate translate_30 (
    .Reset(button_1_out), .Clock(and_34_out), .Input(and_31_out), .Output(translate_30_output));  // open: Set
  translate translate_31 (
    .Reset(button_1_out), .Clock(and_34_out), .Input(and_32_out), .Output(translate_31_output));  // open: Set
  translate translate_32 (
    .Reset(button_1_out), .Clock(and_34_out), .Input(and_33_out), .Output(translate_32_output));  // open: Set
  DotMatrix #(.matrixcols(32), .matrixrows(32)) dotmatrix_1 (
    .col0(translate_1_output), .col1(translate_2_output), .col2(translate_3_output),
    .col3(translate_4_output), .col4(translate_5_output), .col5(translate_6_output),
    .col6(translate_7_output), .col7(translate_8_output), .col8(translate_9_output),
    .col9(translate_10_output), .col10(translate_11_output), .col11(translate_12_output),
    .col12(translate_13_output), .col13(translate_14_output), .col14(translate_15_output),
    .col15(translate_16_output), .col16(translate_17_output), .col17(translate_18_output),
    .col18(translate_19_output), .col19(translate_20_output), .col20(translate_21_output),
    .col21(translate_22_output), .col22(translate_23_output), .col23(translate_24_output),
    .col24(translate_25_output), .col25(translate_26_output), .col26(translate_27_output),
    .col27(translate_28_output), .col28(translate_29_output), .col29(translate_30_output),
    .col30(translate_31_output), .col31(translate_32_output));

  // Notes on the sheet:
  //   contents of rom_1 (hex, n*v repeats v):
  //   f8303000 88000000 f8f8f000 408800 f8409800 2400000 4f8f800 8800 f8f8f800 8800 f8f8f800 40a80000
  //   4000400 8000000 f8f80800 a80000 f8000800 a8000000 800000 f8f80000 8800000 f8000000 f80000 200000
  //   f8f80000 40000000 20f80000 f8000000 f80000 f8a00000 90f80000 f8000000 0 c30000
endmodule

module translate (
  input  Reset,
  input  Set,
  input  Clock,
  input  [31:0] Input,
  output [31:0] Output
);

  wire undriven;

  T_Flip_Flop t_ff_1 (
    .clk(Clock), .T(Input[0]), .Q(Output[0]), .preset(Set), .reset(Reset), .en(undriven));  // open: Qn
  T_Flip_Flop t_ff_2 (
    .clk(Clock), .T(Input[1]), .Q(Output[1]), .preset(Set), .reset(Reset), .en(undriven));  // open: Qn
  T_Flip_Flop t_ff_3 (
    .clk(Clock), .T(Input[2]), .Q(Output[2]), .preset(Set), .reset(Reset), .en(undriven));  // open: Qn
  T_Flip_Flop t_ff_4 (
    .clk(Clock), .T(Input[3]), .Q(Output[3]), .preset(Set), .reset(Reset), .en(undriven));  // open: Qn
  T_Flip_Flop t_ff_5 (
    .clk(Clock), .T(Input[4]), .Q(Output[4]), .preset(Set), .reset(Reset), .en(undriven));  // open: Qn
  T_Flip_Flop t_ff_6 (
    .clk(Clock), .T(Input[5]), .Q(Output[5]), .preset(Set), .reset(Reset), .en(undriven));  // open: Qn
  T_Flip_Flop t_ff_7 (
    .clk(Clock), .T(Input[6]), .Q(Output[6]), .preset(Set), .reset(Reset), .en(undriven));  // open: Qn
  T_Flip_Flop t_ff_8 (
    .clk(Clock), .T(Input[7]), .Q(Output[7]), .preset(Set), .reset(Reset), .en(undriven));  // open: Qn
  T_Flip_Flop t_ff_9 (
    .clk(Clock), .T(Input[8]), .Q(Output[8]), .preset(Set), .reset(Reset), .en(undriven));  // open: Qn
  T_Flip_Flop t_ff_10 (
    .clk(Clock), .T(Input[9]), .Q(Output[9]), .preset(Set), .reset(Reset), .en(undriven));  // open: Qn
  T_Flip_Flop t_ff_11 (
    .clk(Clock), .T(Input[10]), .Q(Output[10]), .preset(Set), .reset(Reset), .en(undriven));  // open: Qn
  T_Flip_Flop t_ff_12 (
    .clk(Clock), .T(Input[11]), .Q(Output[11]), .preset(Set), .reset(Reset), .en(undriven));  // open: Qn
  T_Flip_Flop t_ff_13 (
    .clk(Clock), .T(Input[12]), .Q(Output[12]), .preset(Set), .reset(Reset), .en(undriven));  // open: Qn
  T_Flip_Flop t_ff_14 (
    .clk(Clock), .T(Input[13]), .Q(Output[13]), .preset(Set), .reset(Reset), .en(undriven));  // open: Qn
  T_Flip_Flop t_ff_15 (
    .clk(Clock), .T(Input[14]), .Q(Output[14]), .preset(Set), .reset(Reset), .en(undriven));  // open: Qn
  T_Flip_Flop t_ff_16 (
    .clk(Clock), .T(Input[15]), .Q(Output[15]), .preset(Set), .reset(Reset), .en(undriven));  // open: Qn
  T_Flip_Flop t_ff_17 (
    .clk(Clock), .T(Input[16]), .Q(Output[16]), .preset(Set), .reset(Reset), .en(undriven));  // open: Qn
  T_Flip_Flop t_ff_18 (
    .clk(Clock), .T(Input[17]), .Q(Output[17]), .preset(Set), .reset(Reset), .en(undriven));  // open: Qn
  T_Flip_Flop t_ff_19 (
    .clk(Clock), .T(Input[18]), .Q(Output[18]), .preset(Set), .reset(Reset), .en(undriven));  // open: Qn
  T_Flip_Flop t_ff_20 (
    .clk(Clock), .T(Input[19]), .Q(Output[19]), .preset(Set), .reset(Reset), .en(undriven));  // open: Qn
  T_Flip_Flop t_ff_21 (
    .clk(Clock), .T(Input[20]), .Q(Output[20]), .preset(Set), .reset(Reset), .en(undriven));  // open: Qn
  T_Flip_Flop t_ff_22 (
    .clk(Clock), .T(Input[21]), .Q(Output[21]), .preset(Set), .reset(Reset), .en(undriven));  // open: Qn
  T_Flip_Flop t_ff_23 (
    .clk(Clock), .T(Input[22]), .Q(Output[22]), .preset(Set), .reset(Reset), .en(undriven));  // open: Qn
  T_Flip_Flop t_ff_24 (
    .clk(Clock), .T(Input[23]), .Q(Output[23]), .preset(Set), .reset(Reset), .en(undriven));  // open: Qn
  T_Flip_Flop t_ff_25 (
    .clk(Clock), .T(Input[24]), .Q(Output[24]), .preset(Set), .reset(Reset), .en(undriven));  // open: Qn
  T_Flip_Flop t_ff_26 (
    .clk(Clock), .T(Input[25]), .Q(Output[25]), .preset(Set), .reset(Reset), .en(undriven));  // open: Qn
  T_Flip_Flop t_ff_27 (
    .clk(Clock), .T(Input[26]), .Q(Output[26]), .preset(Set), .reset(Reset), .en(undriven));  // open: Qn
  T_Flip_Flop t_ff_28 (
    .clk(Clock), .T(Input[27]), .Q(Output[27]), .preset(Set), .reset(Reset), .en(undriven));  // open: Qn
  T_Flip_Flop t_ff_29 (
    .clk(Clock), .T(Input[28]), .Q(Output[28]), .preset(Set), .reset(Reset), .en(undriven));  // open: Qn
  T_Flip_Flop t_ff_30 (
    .clk(Clock), .T(Input[29]), .Q(Output[29]), .preset(Set), .reset(Reset), .en(undriven));  // open: Qn
  T_Flip_Flop t_ff_31 (.T(Input[30]), .Q(Output[30]), .preset(Set), .reset(Reset), .en(undriven));  // open: clk, Qn
  T_Flip_Flop t_ff_32 (
    .clk(Clock), .T(Input[31]), .Q(Output[31]), .preset(Set), .reset(Reset), .en(undriven));  // open: Qn
endmodule

module aumentador_de_bits (
  input  IN,
  output [31:0] Out
);


  assign Out = {32{IN}};
endmodule
