// Logisim project relogio jimmy.circ as structural Verilog: 1 circuit, main circuit main
module main (
);

  wire and_1_out, and_2_out, and_3_out, and_4_out, and_5_out, and_6_out, and_7_out, and_8_out, button_2_out,
       button_out, clock_1_out, or_1_out, or_2_out, or_3_out, or_4_out, or_5_out, or_6_out;
  wire [3:0] t_ff_1_q, t_ff_2_q, t_ff_5_q, t_ff_6_q, t_ff_7_q, t_ff_8_q;

  Clock clock_1 (.out(clock_1_out));
  or or_1 (or_1_out, or_6_out, and_1_out);
  T_Flip_Flop #(.trigger("falling")) t_ff_1 (
    .clk(or_2_out), .T(1'b1), .Q(t_ff_1_q[0]), .reset(or_1_out));  // open: Qn, preset, en
  or or_2 (or_2_out, or_6_out, clock_1_out);
  T_Flip_Flop #(.trigger("falling")) t_ff_2 (
    .clk(and_1_out), .T(1'b1), .Q(t_ff_2_q[0]), .reset(or_6_out));  // open: Qn, preset, en
  T_Flip_Flop #(.trigger("falling")) t_ff_3 (
    .clk(t_ff_1_q[0]), .T(1'b1), .Q(t_ff_1_q[1]), .reset(or_1_out));  // open: Qn, preset, en
  T_Flip_Flop #(.trigger("falling")) t_ff_4 (
    .clk(t_ff_2_q[0]), .T(1'b1), .Q(t_ff_2_q[1]), .reset(or_6_out));  // open: Qn, preset, en
  T_Flip_Flop #(.trigger("falling")) t_ff_5 (
    .clk(or_4_out), .T(1'b1), .Q(t_ff_5_q[0]), .reset(and_3_out));  // open: Qn, preset, en
  T_Flip_Flop #(.trigger("falling")) t_ff_6 (
    .clk(and_3_out), .T(1'b1), .Q(t_ff_6_q[0]), .reset(and_4_out));  // open: Qn, preset, en
  T_Flip_Flop #(.trigger("falling")) t_ff_7 (
    .clk(or_5_out), .T(1'b1), .Q(t_ff_7_q[0]), .reset(or_3_out));  // open: Qn, preset, en
  T_Flip_Flop #(.trigger("falling")) t_ff_8 (
    .clk(and_6_out), .T(1'b1), .Q(t_ff_8_q[0]), .reset(and_8_out));  // open: Qn, preset, en
  T_Flip_Flop #(.trigger("falling")) t_ff_9 (
    .clk(t_ff_1_q[1]), .T(1'b1), .Q(t_ff_1_q[2]), .reset(or_1_out));  // open: Qn, preset, en
  T_Flip_Flop #(.trigger("falling")) t_ff_10 (
    .clk(t_ff_2_q[1]), .T(1'b1), .Q(t_ff_2_q[2]), .reset(or_6_out));  // open: Qn, preset, en
  T_Flip_Flop #(.trigger("falling")) t_ff_11 (
    .clk(t_ff_5_q[0]), .T(1'b1), .Q(t_ff_5_q[1]), .reset(and_3_out));  // open: Qn, preset, en
  T_Flip_Flop #(.trigger("falling")) t_ff_12 (
    .clk(t_ff_6_q[0]), .T(1'b1), .Q(t_ff_6_q[1]), .reset(and_4_out));  // open: Qn, preset, en
  T_Flip_Flop #(.trigger("falling")) t_ff_13 (
    .clk(t_ff_7_q[0]), .T(1'b1), .Q(t_ff_7_q[1]), .reset(or_3_out));  // open: Qn, preset, en
  T_Flip_Flop #(.trigger("falling")) t_ff_14 (
    .clk(t_ff_8_q[0]), .T(1'b1), .Q(t_ff_8_q[1]), .reset(and_8_out));  // open: Qn, preset, en
  T_Flip_Flop #(.trigger("falling")) t_ff_15 (
    .clk(t_ff_1_q[2]), .T(1'b1), .Q(t_ff_1_q[3]), .reset(or_1_out));  // open: Qn, preset, en
  T_Flip_Flop #(.trigger("falling")) t_ff_16 (
    .clk(t_ff_2_q[2]), .T(1'b1), .Q(t_ff_2_q[3]), .reset(or_6_out));  // open: Qn, preset, en
  T_Flip_Flop #(.trigger("falling")) t_ff_17 (
    .clk(t_ff_5_q[1]), .T(1'b1), .Q(t_ff_5_q[2]), .reset(and_3_out));  // open: Qn, preset, en
  T_Flip_Flop #(.trigger("falling")) t_ff_18 (
    .clk(t_ff_6_q[1]), .T(1'b1), .Q(t_ff_6_q[2]), .reset(and_4_out));  // open: Qn, preset, en
  T_Flip_Flop #(.trigger("falling")) t_ff_19 (
    .clk(t_ff_7_q[1]), .T(1'b1), .Q(t_ff_7_q[2]), .reset(or_3_out));  // open: Qn, preset, en
  T_Flip_Flop #(.trigger("falling")) t_ff_20 (
    .clk(t_ff_8_q[1]), .T(1'b1), .Q(t_ff_8_q[2]), .reset(and_8_out));  // open: Qn, preset, en
  T_Flip_Flop #(.trigger("falling")) t_ff_21 (
    .clk(t_ff_5_q[2]), .T(1'b1), .Q(t_ff_5_q[3]), .reset(and_3_out));  // open: Qn, preset, en
  T_Flip_Flop #(.trigger("falling")) t_ff_22 (
    .clk(t_ff_6_q[2]), .T(1'b1), .Q(t_ff_6_q[3]), .reset(and_4_out));  // open: Qn, preset, en
  T_Flip_Flop #(.trigger("falling")) t_ff_23 (
    .clk(t_ff_7_q[2]), .T(1'b1), .Q(t_ff_7_q[3]), .reset(or_3_out));  // open: Qn, preset, en
  T_Flip_Flop #(.trigger("falling")) t_ff_24 (
    .clk(t_ff_8_q[2]), .T(1'b1), .Q(t_ff_8_q[3]), .reset(and_8_out));  // open: Qn, preset, en
  and and_1 (and_1_out, ~t_ff_1_q[0], t_ff_1_q[1], ~t_ff_1_q[2], t_ff_1_q[3]);  // AND_Gate
  and and_2 (and_2_out, ~t_ff_2_q[0], t_ff_2_q[1], t_ff_2_q[2], ~t_ff_2_q[3]);  // AND_Gate
  and and_3 (and_3_out, ~t_ff_5_q[0], t_ff_5_q[1], ~t_ff_5_q[2], t_ff_5_q[3]);  // AND_Gate
  and and_4 (and_4_out, ~t_ff_6_q[0], t_ff_6_q[1], t_ff_6_q[2], ~t_ff_6_q[3]);  // AND_Gate
  and and_5 (and_5_out, ~t_ff_7_q[0], ~t_ff_7_q[1], t_ff_7_q[2], ~t_ff_7_q[3]);  // AND_Gate
  and and_6 (and_6_out, ~t_ff_7_q[0], t_ff_7_q[1], ~t_ff_7_q[2], t_ff_7_q[3]);  // AND_Gate
  and and_7 (and_7_out, ~t_ff_8_q[0], t_ff_8_q[1], ~t_ff_8_q[2], ~t_ff_8_q[3]);  // AND_Gate
  and and_8 (and_8_out, and_5_out, and_7_out);
  or or_3 (or_3_out, and_6_out, and_8_out);
  Button button (.out(button_out));
  Hex_Digit_Display hex_digit_display_1 (.value(t_ff_8_q));  // open: dp
  Hex_Digit_Display hex_digit_display_2 (.value(t_ff_7_q));  // open: dp
  Hex_Digit_Display hex_digit_display_3 (.value(t_ff_6_q));  // open: dp
  Button button_2 (.out(button_2_out));
  Hex_Digit_Display hex_digit_display_4 (.value(t_ff_5_q));  // open: dp
  Hex_Digit_Display hex_digit_display_5 (.value(t_ff_2_q));  // open: dp
  or or_4 (or_4_out, and_2_out, button_2_out);
  or or_5 (or_5_out, button_out, and_4_out);
  Hex_Digit_Display hex_digit_display_6 (.value(t_ff_1_q));  // open: dp
  or or_6 (or_6_out, and_2_out, or_4_out);
endmodule
